// Logisim project 20240282_LAB_1.circ as structural Verilog: 6 circuits, main circuit main
module preg_1 (
  input  [2:0] in_1,
  input  in_2,
  output out_3,
  output out_4,
  output out_5
);

  wire and_1_out, and_2_out, and_3_out, and_4_out, and_5_out, and_6_out, and_7_out, not_1_out, not_2_out,
       not_3_out;
  wire [2:0] or_1_out;

  not not_1 (not_1_out, in_1[2]);
  not not_2 (not_2_out, in_1[1]);
  not not_3 (not_3_out, in_1[0]);
  and and_1 (and_1_out, not_1_out, not_2_out);
  and and_2 (and_2_out, not_2_out, not_3_out);
  and and_3 (and_3_out, not_2_out, in_1[0]);
  and and_4 (and_4_out, not_1_out, in_1[1], not_3_out);
  and and_5 (and_5_out, not_1_out, not_2_out, not_3_out);
  and and_6 (and_6_out, not_1_out, in_1[1], in_1[0]);
  and and_7 (and_7_out, in_1[2], not_2_out, in_1[0]);
  or or_1 (or_1_out[0], and_1_out, and_2_out);
  or or_2 (or_1_out[1], and_3_out, and_4_out);
  or or_3 (or_1_out[2], and_5_out, and_6_out, and_7_out);
  assign {out_5, out_4, out_3} = or_1_out & {3{in_2}};  // AND_Gate and_8, 3 bits wide
endmodule

module preg_2 (
  input  in_1
);

  wire [2:0] counter_1_q;
  wire [3:0] multiplexer_1_out;

  Counter #(.max('h7), .width(3)) counter_1 (.clk(in_1), .Q(counter_1_q));  // open: clr, load, up, count, D, carry
  Multiplexer #(.select(3), .width(4)) multiplexer_1 (
    .in0(4'b0010), .in1(4'b0000), .in2(4'b0010), .in3(4'b0100), .in4(4'b0000), .in5(4'b0010), .in6(4'b1000),
    .in7(4'b0010), .out(multiplexer_1_out), .sel(counter_1_q));
  Hex_Digit_Display hex_digit_display_1 (.value(multiplexer_1_out));  // open: dp
  Hex_Digit_Display hex_digit_display_2 (.value({1'b0, counter_1_q}));  // open: dp
endmodule

module preg_3 (
  input  [3:0] in_1,
  input  [3:0] in_2,
  input  in_3
);

  wire [2:0] and_1_out, comparator_1_gt;

  Comparator #(.width(4)) comparator_1 (
    .a(in_1), .b(in_2), .gt(comparator_1_gt[0]), .eq(comparator_1_gt[1]), .lt(comparator_1_gt[2]));
  Bit_Extender #(.in_width(4), .out_width(9)) bit_extender_1 ();  // open: in, out
  Bit_Extender #(.in_width(4), .out_width(9)) bit_extender_2 ();  // open: in, out
  LED led_1 (.in(and_1_out[0]));
  LED led_2 (.in(and_1_out[1]));
  assign and_1_out = comparator_1_gt & {3{in_3}};  // AND_Gate and_1, 3 bits wide
  LED led_3 (.in(and_1_out[2]));

  // Other names for the same wires on the sheet: Enabler[2:0] = {3{in_3}}
endmodule

module preg_4 (
  input  Enabler,
  input  [3:0] X,
  input  [3:0] Y
);

  wire x1, x2, x3, x4, x5, x6, x7, x8, x9, x10, x11, x12, x13, x14, x15;
  wire [14:0] and_1_out, and_2_out, and_3_out, and_4_out, and_5_out, and_6_out, and_7_out, and_8_out,
       and_9_out, and_10_out, and_11_out, and_12_out, and_13_out, and_14_out, and_15_out, decoder_2_out15;

  Decoder #(.select(4)) decoder_1 (
    .out1(x1), .out2(x2), .out3(x3), .out4(x4), .out5(x5), .out6(x6), .out7(x7), .out8(x8), .out9(x9),
    .out10(x10), .out11(x11), .out12(x12), .out13(x13), .out14(x14), .out15(x15), .sel(X), .en(Enabler));  // open: out0
  Decoder #(.select(4)) decoder_2 (
    .out1(decoder_2_out15[14]), .out2(decoder_2_out15[13]), .out3(decoder_2_out15[12]),
    .out4(decoder_2_out15[11]), .out5(decoder_2_out15[10]), .out6(decoder_2_out15[9]),
    .out7(decoder_2_out15[8]), .out8(decoder_2_out15[7]), .out9(decoder_2_out15[6]),
    .out10(decoder_2_out15[5]), .out11(decoder_2_out15[4]), .out12(decoder_2_out15[3]),
    .out13(decoder_2_out15[2]), .out14(decoder_2_out15[1]), .out15(decoder_2_out15[0]), .sel(Y), .en(Enabler));  // open: out0
  assign and_1_out = {15{x1}} & decoder_2_out15;  // AND_Gate and_1, 15 bits wide
  assign and_2_out = {15{x2}} & decoder_2_out15;  // AND_Gate and_2, 15 bits wide
  assign and_3_out = {15{x3}} & decoder_2_out15;  // AND_Gate and_3, 15 bits wide
  assign and_4_out = {15{x4}} & decoder_2_out15;  // AND_Gate and_4, 15 bits wide
  DotMatrix #(.matrixcols(15), .matrixrows(15)) dotmatrix_1 (
    .col0(and_1_out), .col1(and_2_out), .col2(and_3_out), .col3(and_4_out), .col4(and_5_out),
    .col5(and_6_out), .col6(and_7_out), .col7(and_8_out), .col8(and_9_out), .col9(and_10_out),
    .col10(and_11_out), .col11(and_12_out), .col12(and_14_out), .col13(and_13_out), .col14(and_15_out));
  assign and_5_out = {15{x5}} & decoder_2_out15;  // AND_Gate and_5, 15 bits wide
  assign and_6_out = {15{x6}} & decoder_2_out15;  // AND_Gate and_6, 15 bits wide
  assign and_7_out = {15{x7}} & decoder_2_out15;  // AND_Gate and_7, 15 bits wide
  assign and_8_out = {15{x8}} & decoder_2_out15;  // AND_Gate and_8, 15 bits wide
  assign and_9_out = {15{x9}} & decoder_2_out15;  // AND_Gate and_9, 15 bits wide
  assign and_10_out = {15{x10}} & decoder_2_out15;  // AND_Gate and_10, 15 bits wide
  assign and_11_out = {15{x11}} & decoder_2_out15;  // AND_Gate and_11, 15 bits wide
  assign and_12_out = {15{x12}} & decoder_2_out15;  // AND_Gate and_12, 15 bits wide
  assign and_13_out = {15{x14}} & decoder_2_out15;  // AND_Gate and_13, 15 bits wide
  assign and_14_out = {15{x13}} & decoder_2_out15;  // AND_Gate and_14, 15 bits wide
  assign and_15_out = {15{x15}} & decoder_2_out15;  // AND_Gate and_15, 15 bits wide
endmodule

module preg_5 (
  input  Enabler,
  input  [3:0] X,
  input  [3:0] Y
);

  wire x1, x2, x3, x4, x5, x6, x7, x8, x9, x10, x11, x12, x13, x14, x15;
  wire [14:0] and_1_out, and_2_out, and_3_out, and_4_out, and_5_out, and_6_out, and_7_out, and_8_out,
       and_9_out, and_10_out, and_11_out, and_12_out, and_13_out, and_14_out, and_15_out, decoder_2_out15;

  Decoder #(.select(4)) decoder_1 (
    .out1(x1), .out2(x2), .out3(x3), .out4(x4), .out5(x5), .out6(x6), .out7(x7), .out8(x8), .out9(x9),
    .out10(x10), .out11(x11), .out12(x12), .out13(x13), .out14(x14), .out15(x15), .sel(X), .en(Enabler));  // open: out0
  Decoder #(.select(4)) decoder_2 (
    .out1(decoder_2_out15[14]), .out2(decoder_2_out15[13]), .out3(decoder_2_out15[12]),
    .out4(decoder_2_out15[11]), .out5(decoder_2_out15[10]), .out6(decoder_2_out15[9]),
    .out7(decoder_2_out15[8]), .out8(decoder_2_out15[7]), .out9(decoder_2_out15[6]),
    .out10(decoder_2_out15[5]), .out11(decoder_2_out15[4]), .out12(decoder_2_out15[3]),
    .out13(decoder_2_out15[2]), .out14(decoder_2_out15[1]), .out15(decoder_2_out15[0]), .sel(Y), .en(Enabler));  // open: out0
  assign and_1_out = {15{x1}} & decoder_2_out15;  // AND_Gate and_1, 15 bits wide
  assign and_2_out = {15{x2}} & decoder_2_out15;  // AND_Gate and_2, 15 bits wide
  assign and_3_out = {15{x3}} & decoder_2_out15;  // AND_Gate and_3, 15 bits wide
  assign and_4_out = {15{x4}} & decoder_2_out15;  // AND_Gate and_4, 15 bits wide
  DotMatrix #(.matrixcols(15), .matrixrows(15)) dotmatrix_1 (
    .col0(and_1_out), .col1(and_2_out), .col2(and_3_out), .col3(and_4_out), .col4(and_5_out),
    .col5(and_6_out), .col6(and_7_out), .col7(and_8_out), .col8(and_9_out), .col9(and_10_out),
    .col10(and_11_out), .col11(and_12_out), .col12(and_13_out), .col13(and_14_out), .col14(and_15_out));
  assign and_5_out = {15{x5}} & decoder_2_out15;  // AND_Gate and_5, 15 bits wide
  assign and_6_out = {15{x6}} & decoder_2_out15;  // AND_Gate and_6, 15 bits wide
  assign and_7_out = {15{x7}} & decoder_2_out15;  // AND_Gate and_7, 15 bits wide
  assign and_8_out = {15{x8}} & decoder_2_out15;  // AND_Gate and_8, 15 bits wide
  assign and_9_out = {15{x9}} & decoder_2_out15;  // AND_Gate and_9, 15 bits wide
  assign and_10_out = {15{x10}} & decoder_2_out15;  // AND_Gate and_10, 15 bits wide
  assign and_11_out = {15{x11}} & decoder_2_out15;  // AND_Gate and_11, 15 bits wide
  assign and_12_out = {15{x12}} & decoder_2_out15;  // AND_Gate and_12, 15 bits wide
  assign and_13_out = {15{x13}} & decoder_2_out15;  // AND_Gate and_13, 15 bits wide
  assign and_14_out = {15{x14}} & decoder_2_out15;  // AND_Gate and_14, 15 bits wide
  assign and_15_out = {15{x15}} & decoder_2_out15;  // AND_Gate and_15, 15 bits wide
endmodule

module main (
  input  Pregunta_4,
  input  in_2,
  input  [2:0] in_3
);

  wire clock_1_out, preg_1_1_out_3, preg_1_1_out_4, preg_1_1_out_5;
  wire [3:0] joystick_1_x, joystick_1_y;

  preg_1 preg_1_1 (.in_1(in_3), .in_2(in_2), .out_3(preg_1_1_out_3), .out_4(preg_1_1_out_4), .out_5(preg_1_1_out_5));
  preg_2 preg_2_1 (.in_1(clock_1_out));
  Clock clock_1 (.out(clock_1_out));
  // RGBLED rgbled_1: pin names not known; wires that end beside it: preg_1_1_out_3, preg_1_1_out_4, preg_1_1_out_5
  preg_4 preg_4_1 (.X(joystick_1_x), .Y(joystick_1_y), .Enabler(Pregunta_4));
  Joystick joystick_1 (.x(joystick_1_x), .y(joystick_1_y));

  // Notes on the sheet:
  //   Pregunta 1: violeta, amarillo, verde, azul, rojo, celeste
  //   Pregunta 2: 20240282
endmodule
