// Logisim project Computadora_Final.circ as structural Verilog: 17 circuits, main circuit registers_8R
module asdasd (
  input  [7:0] in_1,
  input  in_2
);

  wire button_1_out, clock_1_out, clock_2_out, keyboard_1_avail;
  wire [6:0] keyboard_1_data;

  RAM ram_1 ();  // open: addr, we, oe, clk, din, dout
  registers_8R registers_8r_1 ();  // open: dir_RA, dir_RB, enable, dir_W, reset, clock, dato_W, RA, RB
  DipSwitch dipswitch_1 ();  // open: sw1, sw2, sw3, sw4, sw5, sw6, sw7, sw8
  Clock clock_1 (.out(clock_1_out));
  Keyboard #(.buflen(128)) keyboard_1 (
    .clk(clock_1_out), .re(in_2), .clr(button_1_out), .avail(keyboard_1_avail), .data(keyboard_1_data));
  Button button_1 (.out(button_1_out));
  Clock clock_2 (.out(clock_2_out));
  TTY tty_1 (.data(keyboard_1_data), .clk(clock_2_out), .we(keyboard_1_avail), .clr(button_1_out));
endmodule

module registers_8R (
  input  reset,
  input  [2:0] dir_RB,
  input  clock,
  input  [7:0] dato_W,
  input  enable,
  input  [2:0] dir_RA,
  input  [2:0] dir_W,
  output [7:0] RB,
  output [7:0] RA
);

  wire decoder_1_out0, decoder_1_out1, decoder_1_out2, decoder_1_out3, decoder_1_out4, decoder_1_out5,
       decoder_1_out6, decoder_1_out7;
  wire [3:0] binary_to_bcd_converter_1_p2, binary_to_bcd_converter_1_p3, binary_to_bcd_converter_1_p4,
       binary_to_bcd_converter_2_p2, binary_to_bcd_converter_2_p3, binary_to_bcd_converter_2_p4,
       binary_to_bcd_converter_3_p2, binary_to_bcd_converter_3_p3, binary_to_bcd_converter_3_p4,
       binary_to_bcd_converter_4_p2, binary_to_bcd_converter_4_p3, binary_to_bcd_converter_4_p4,
       binary_to_bcd_converter_5_p2, binary_to_bcd_converter_5_p3, binary_to_bcd_converter_5_p4,
       binary_to_bcd_converter_6_p2, binary_to_bcd_converter_6_p3, binary_to_bcd_converter_6_p4,
       binary_to_bcd_converter_7_p2, binary_to_bcd_converter_7_p3, binary_to_bcd_converter_7_p4,
       binary_to_bcd_converter_8_p2, binary_to_bcd_converter_8_p3, binary_to_bcd_converter_8_p4, R0_q,
       R0_q_2, R1_q, R1_q_2, R2_q, R2_q_2, R3_q, R3_q_2, register_1_q, register_1_q_2, register_2_q,
       register_2_q_2, register_3_q, register_3_q_2, register_4_q, register_4_q_2;

  LED W_EN_led (.in(enable));
  LED led_1 (.in(enable));
  LED led_2 (.in(enable));
  LED led_3 (.in(enable));
  Decoder #(.select(3)) decoder_1 (
    .out0(decoder_1_out0), .out1(decoder_1_out1), .out2(decoder_1_out2), .out3(decoder_1_out3),
    .out4(decoder_1_out4), .out5(decoder_1_out5), .out6(decoder_1_out6), .out7(decoder_1_out7), .sel(dir_W),
    .en(enable));
  Register register_1 (.D(dato_W), .en(decoder_1_out7), .clk(clock), .Q({register_1_q_2, register_1_q}), .clr(reset));
  Register register_2 (.D(dato_W), .en(decoder_1_out6), .clk(clock), .Q({register_2_q_2, register_2_q}), .clr(reset));
  Register register_3 (.D(dato_W), .en(decoder_1_out5), .clk(clock), .Q({register_3_q_2, register_3_q}), .clr(reset));
  Register register_4 (.D(dato_W), .en(decoder_1_out4), .clk(clock), .Q({register_4_q_2, register_4_q}), .clr(reset));
  Register R3 (.D(dato_W), .en(decoder_1_out3), .clk(clock), .Q({R3_q_2, R3_q}), .clr(reset));
  Register R2 (.D(dato_W), .en(decoder_1_out2), .clk(clock), .Q({R2_q_2, R2_q}), .clr(reset));
  Register R1 (.D(dato_W), .en(decoder_1_out1), .clk(clock), .Q({R1_q_2, R1_q}), .clr(reset));
  Register R0 (.D(dato_W), .en(decoder_1_out0), .clk(clock), .Q({R0_q_2, R0_q}), .clr(reset));
  Hex_Digit_Display R7H (.value(register_1_q_2));  // open: dp
  Hex_Digit_Display R6H (.value(register_2_q_2));  // open: dp
  Hex_Digit_Display R5H (.value(register_3_q_2));  // open: dp
  Hex_Digit_Display R4H (.value(register_4_q_2));  // open: dp
  Hex_Digit_Display R3H (.value(R3_q_2));  // open: dp
  Hex_Digit_Display R2H (.value(R2_q_2));  // open: dp
  Hex_Digit_Display R1H (.value(R1_q_2));  // open: dp
  Hex_Digit_Display R0H (.value(R0_q_2));  // open: dp
  Hex_Digit_Display R7L (.value(register_1_q));  // open: dp
  Hex_Digit_Display R6L (.value(register_2_q));  // open: dp
  Hex_Digit_Display R5L (.value(register_3_q));  // open: dp
  Hex_Digit_Display R4L (.value(register_4_q));  // open: dp
  Hex_Digit_Display R3L (.value(R3_q));  // open: dp
  Hex_Digit_Display R2L (.value(R2_q));  // open: dp
  Hex_Digit_Display R1L (.value(R1_q));  // open: dp
  Hex_Digit_Display R0L (.value(R0_q));  // open: dp
  Hex_Digit_Display R7d2 (.value(binary_to_bcd_converter_1_p2));  // open: dp
  Hex_Digit_Display R7d1 (.value(binary_to_bcd_converter_1_p3));  // open: dp
  // Binary_to_BCD_converter #(.binvalue(8)) binary_to_bcd_converter_1: pin names not known; wires that end beside it: {register_1_q_2, register_1_q}, binary_to_bcd_converter_1_p2, binary_to_bcd_converter_1_p3, binary_to_bcd_converter_1_p4
  Hex_Digit_Display R6d2 (.value(binary_to_bcd_converter_2_p2));  // open: dp
  Hex_Digit_Display R6d1 (.value(binary_to_bcd_converter_2_p3));  // open: dp
  // Binary_to_BCD_converter #(.binvalue(8)) binary_to_bcd_converter_2: pin names not known; wires that end beside it: {register_2_q_2, register_2_q}, binary_to_bcd_converter_2_p2, binary_to_bcd_converter_2_p3, binary_to_bcd_converter_2_p4
  Hex_Digit_Display R5d2 (.value(binary_to_bcd_converter_3_p2));  // open: dp
  Hex_Digit_Display R5d1 (.value(binary_to_bcd_converter_3_p3));  // open: dp
  // Binary_to_BCD_converter #(.binvalue(8)) binary_to_bcd_converter_3: pin names not known; wires that end beside it: {register_3_q_2, register_3_q}, binary_to_bcd_converter_3_p2, binary_to_bcd_converter_3_p3, binary_to_bcd_converter_3_p4
  Hex_Digit_Display R4d2 (.value(binary_to_bcd_converter_4_p2));  // open: dp
  Hex_Digit_Display R4d1 (.value(binary_to_bcd_converter_4_p3));  // open: dp
  // Binary_to_BCD_converter #(.binvalue(8)) binary_to_bcd_converter_4: pin names not known; wires that end beside it: {register_4_q_2, register_4_q}, binary_to_bcd_converter_4_p2, binary_to_bcd_converter_4_p3, binary_to_bcd_converter_4_p4
  Hex_Digit_Display R3d2 (.value(binary_to_bcd_converter_5_p2));  // open: dp
  Hex_Digit_Display R3d1 (.value(binary_to_bcd_converter_5_p3));  // open: dp
  // Binary_to_BCD_converter #(.binvalue(8)) binary_to_bcd_converter_5: pin names not known; wires that end beside it: {R3_q_2, R3_q}, binary_to_bcd_converter_5_p2, binary_to_bcd_converter_5_p3, binary_to_bcd_converter_5_p4
  Hex_Digit_Display R2d2 (.value(binary_to_bcd_converter_6_p2));  // open: dp
  Hex_Digit_Display R2d1 (.value(binary_to_bcd_converter_6_p3));  // open: dp
  // Binary_to_BCD_converter #(.binvalue(8)) binary_to_bcd_converter_6: pin names not known; wires that end beside it: {R2_q_2, R2_q}, binary_to_bcd_converter_6_p2, binary_to_bcd_converter_6_p3, binary_to_bcd_converter_6_p4
  Hex_Digit_Display R1d2 (.value(binary_to_bcd_converter_7_p2));  // open: dp
  Hex_Digit_Display R1d1 (.value(binary_to_bcd_converter_7_p3));  // open: dp
  // Binary_to_BCD_converter #(.binvalue(8)) binary_to_bcd_converter_7: pin names not known; wires that end beside it: {R1_q_2, R1_q}, binary_to_bcd_converter_7_p2, binary_to_bcd_converter_7_p3, binary_to_bcd_converter_7_p4
  Hex_Digit_Display R0d2 (.value(binary_to_bcd_converter_8_p2));  // open: dp
  Hex_Digit_Display R0d1 (.value(binary_to_bcd_converter_8_p3));  // open: dp
  // Binary_to_BCD_converter #(.binvalue(8)) binary_to_bcd_converter_8: pin names not known; wires that end beside it: {R0_q_2, R0_q}, binary_to_bcd_converter_8_p2, binary_to_bcd_converter_8_p3, binary_to_bcd_converter_8_p4
  Hex_Digit_Display R7d0 (.value(binary_to_bcd_converter_1_p4));  // open: dp
  Hex_Digit_Display R6d0 (.value(binary_to_bcd_converter_2_p4));  // open: dp
  Hex_Digit_Display R5d0 (.value(binary_to_bcd_converter_3_p4));  // open: dp
  Hex_Digit_Display R4d0 (.value(binary_to_bcd_converter_4_p4));  // open: dp
  Hex_Digit_Display R3d0 (.value(binary_to_bcd_converter_5_p4));  // open: dp
  Hex_Digit_Display R2d0 (.value(binary_to_bcd_converter_6_p4));  // open: dp
  Hex_Digit_Display R1d0 (.value(binary_to_bcd_converter_7_p4));  // open: dp
  Hex_Digit_Display R0d0 (.value(binary_to_bcd_converter_8_p4));  // open: dp
  LED led_4 (.in(register_1_q_2[3]));
  LED led_5 (.in(register_1_q_2[2]));
  LED led_6 (.in(register_1_q_2[1]));
  LED led_7 (.in(register_2_q_2[3]));
  LED led_8 (.in(register_2_q_2[2]));
  LED led_9 (.in(register_2_q_2[1]));
  LED led_10 (.in(register_3_q_2[3]));
  LED led_11 (.in(register_3_q_2[2]));
  LED led_12 (.in(register_3_q_2[1]));
  LED b47 (.in(register_4_q_2[3]));
  LED b46 (.in(register_4_q_2[2]));
  LED b45 (.in(register_4_q_2[1]));
  LED b37 (.in(R3_q_2[3]));
  LED b36 (.in(R3_q_2[2]));
  LED b35 (.in(R3_q_2[1]));
  LED led_13 (.in(R2_q_2[3]));
  LED led_14 (.in(R2_q_2[2]));
  LED led_15 (.in(R2_q_2[1]));
  LED led_16 (.in(R1_q_2[3]));
  LED led_17 (.in(R1_q_2[2]));
  LED led_18 (.in(R1_q_2[1]));
  LED led_19 (.in(R0_q_2[3]));
  LED led_20 (.in(R0_q_2[2]));
  LED led_21 (.in(R0_q_2[1]));
  LED led_22 (.in(register_1_q_2[0]));
  LED led_23 (.in(register_1_q[3]));
  LED led_24 (.in(register_1_q[2]));
  LED led_25 (.in(register_1_q[1]));
  LED led_26 (.in(register_2_q_2[0]));
  LED led_27 (.in(register_2_q[3]));
  LED led_28 (.in(register_2_q[2]));
  LED led_29 (.in(register_2_q[1]));
  LED led_30 (.in(register_3_q_2[0]));
  LED led_31 (.in(register_3_q[3]));
  LED led_32 (.in(register_3_q[2]));
  LED led_33 (.in(register_3_q[1]));
  LED b44 (.in(register_4_q_2[0]));
  LED b43 (.in(register_4_q[3]));
  LED b42 (.in(register_4_q[2]));
  LED b41 (.in(register_4_q[1]));
  LED b34 (.in(R3_q_2[0]));
  LED b33 (.in(R3_q[3]));
  LED b32 (.in(R3_q[2]));
  LED b31 (.in(R3_q[1]));
  LED led_34 (.in(R2_q_2[0]));
  LED led_35 (.in(R2_q[3]));
  LED led_36 (.in(R2_q[2]));
  LED led_37 (.in(R2_q[1]));
  LED led_38 (.in(R1_q_2[0]));
  LED led_39 (.in(R1_q[3]));
  LED led_40 (.in(R1_q[2]));
  LED led_41 (.in(R1_q[1]));
  LED led_42 (.in(R0_q_2[0]));
  LED led_43 (.in(R0_q[3]));
  LED led_44 (.in(R0_q[2]));
  LED led_45 (.in(R0_q[1]));
  Multiplexer #(.select(3), .width(8)) multiplexer_1 (
    .in0({R0_q_2, R0_q}), .in1({R1_q_2, R1_q}), .in2({R2_q_2, R2_q}), .in3({R3_q_2, R3_q}),
    .in4({register_4_q_2, register_4_q}), .in5({register_3_q_2, register_3_q}),
    .in6({register_2_q_2, register_2_q}), .in7({register_1_q_2, register_1_q}), .out(RA), .sel(dir_RA));
  LED led_46 (.in(register_1_q[0]));
  LED led_47 (.in(register_2_q[0]));
  LED led_48 (.in(register_3_q[0]));
  LED b40 (.in(register_4_q[0]));
  LED b30 (.in(R3_q[0]));
  LED led_49 (.in(R2_q[0]));
  LED led_50 (.in(R1_q[0]));
  LED led_51 (.in(R0_q[0]));
  Multiplexer #(.select(3), .width(8)) multiplexer_2 (
    .in0({R0_q_2, R0_q}), .in1({R1_q_2, R1_q}), .in2({R2_q_2, R2_q}), .in3({R3_q_2, R3_q}),
    .in4({register_4_q_2, register_4_q}), .in5({register_3_q_2, register_3_q}),
    .in6({register_2_q_2, register_2_q}), .in7({register_1_q_2, register_1_q}), .out(RB), .sel(dir_RB));
endmodule

module Compu_1_1 (
);

  wire resetear, tictac;
  wire [1:0] ope;
  wire [2:0] dirA, dirB;
  wire [7:0] adder_1_out, counter_1_q, multiplexer_1_out, not_1_out, registers_8r_1_ra, registers_8r_1_rb;

  Counter counter_1 (.clr(resetear), .clk(tictac), .Q(counter_1_q));  // open: load, up, count, D, carry
  ROM rom_1 (.addr(counter_1_q), .data({ope[1], dirB[1:0], dirA[1:0], dirB[2], dirA[2], ope[0]}));
  Button button_1 (.out(resetear));
  Button button_2 (.out(tictac));
  registers_8R registers_8r_1 (
    .dir_RA(dirA), .dir_RB(dirB), .enable(1'b1), .dir_W(dirA), .reset(resetear), .clock(tictac),
    .dato_W(multiplexer_1_out), .RA(registers_8r_1_ra), .RB(registers_8r_1_rb));
  // Probe on multiplexer_1_out
  // Probe on multiplexer_1_out
  // Probe on multiplexer_1_out
  Multiplexer #(.select(2), .width(8)) multiplexer_1 (
    .in0(registers_8r_1_rb), .in1(adder_1_out), .in2({{5{1'b0}}, dirB}), .in3(not_1_out),
    .out(multiplexer_1_out), .sel(ope));
  Adder adder_1 (.a(registers_8r_1_ra), .b(registers_8r_1_rb), .out(adder_1_out));  // open: cin, cout
  assign not_1_out = ~registers_8r_1_ra;  // NOT_Gate not_1, 8 bits wide

  // Other names for the same wires on the sheet: inm[2:0] = dirB

  // Notes on the sheet:
  //   contents of rom_1 (hex, n*v repeats v):
  //   0 0 0 2
  //   COPY
  //   SUM
  //   LOAD
  //   NOT
endmodule

module Compu_1_2 (
);

  wire resetear, tictac;
  wire [1:0] ope;
  wire [2:0] dirA, dirB;
  wire [7:0] adder_1_out, counter_1_q, multiplexer_1_out, multiplexer_2_out, not_1_out, registers_8r_1_ra,
       registers_8r_1_rb;

  Counter counter_1 (.clr(resetear), .clk(tictac), .Q(counter_1_q));  // open: load, up, count, D, carry
  ROM rom_1 (.addr(counter_1_q), .data({ope[1], dirB[1:0], dirA[1:0], dirB[2], dirA[2], ope[0]}));
  Button button_1 (.out(resetear));
  Button button_2 (.out(tictac));
  registers_8R registers_8r_1 (
    .dir_RA(dirA), .dir_RB(dirB), .enable(1'b1), .dir_W(dirA), .reset(resetear), .clock(tictac),
    .dato_W(multiplexer_1_out), .RA(registers_8r_1_ra), .RB(registers_8r_1_rb));
  // Probe on multiplexer_1_out
  // Probe on multiplexer_1_out
  // Probe on multiplexer_1_out
  Multiplexer #(.select(2), .width(8)) multiplexer_1 (
    .in0(registers_8r_1_rb), .in1(adder_1_out), .in2({{5{1'b0}}, dirB}), .in3(multiplexer_2_out),
    .out(multiplexer_1_out), .sel(ope));
  Adder adder_1 (.a(registers_8r_1_ra), .b(registers_8r_1_rb), .out(adder_1_out));  // open: cin, cout
  assign not_1_out = ~registers_8r_1_ra;  // NOT_Gate not_1, 8 bits wide
  Multiplexer #(.select(3), .width(8)) multiplexer_2 (
    .in0(not_1_out), .in1({registers_8r_1_ra[3:0], registers_8r_1_ra[7:4]}),
    .in2({registers_8r_1_ra[0], registers_8r_1_ra[1], registers_8r_1_ra[2], registers_8r_1_ra[3], registers_8r_1_ra[4], registers_8r_1_ra[5], registers_8r_1_ra[6], registers_8r_1_ra[7]}),
    .in4({registers_8r_1_ra[6:0], 1'b0}), .in5({1'b0, registers_8r_1_ra[7:1]}),
    .in6({registers_8r_1_ra[6:0], registers_8r_1_ra[7]}),
    .in7({registers_8r_1_ra[0], registers_8r_1_ra[7:1]}), .out(multiplexer_2_out), .sel(dirB));  // open: in3

  // Other names for the same wires on the sheet: inm[2:0] = dirB; sel1arg[2:0] = dirB

  // Notes on the sheet:
  //   contents of rom_1 (hex, n*v repeats v):
  //   a8 d0 f8 ae 42 72 43 73 9b b3 c3 87 b7 c7 c7 5*f7
  //   COPY
  //   SUM
  //   LOAD
  //   NOT
  //   XNOR?
  //   SWAPN
  //   FLIP
  //   (reserved)
  //   LSL
  //   LSR
  //   ROL
  //   ROR
endmodule

module Compu_1_3 (
);

  wire ins_JUMPR, not_1_out, resetear, tictac;
  wire [1:0] ope;
  wire [2:0] dirA, dirB;
  wire [7:0] adder_1_out, adder_2_out, bit_extender_1_out, counter_1_q, multiplexer_1_out, multiplexer_2_out,
       multiplexer_3_out, not_2_out, registers_8r_1_ra, registers_8r_1_rb;

  Counter counter_1 (
    .clr(resetear), .load(1'b1), .clk(tictac), .D(adder_1_out), .Q(counter_1_q));  // open: up, count, carry
  assign bit_extender_1_out = {{5{dirA[2]}}, dirA};  // Bit_Extender bit_extender_1
  Multiplexer #(.width(8)) multiplexer_1 (
    .in0(8'h1), .in1(bit_extender_1_out), .out(multiplexer_1_out), .sel(ins_JUMPR));
  Adder adder_1 (.a(counter_1_q), .b(multiplexer_1_out), .out(adder_1_out));  // open: cin, cout
  ROM #(.misaligned("true")) rom_1 (
    .addr(counter_1_q), .data({ope[1], dirB[1:0], dirA[1:0], dirB[2], dirA[2], ope[0]}));
  Button button_1 (.out(resetear));
  and and_1 (ins_JUMPR, ope[0], ope[1], dirB[0], dirB[1], ~dirB[2]);  // AND_Gate
  Button button_2 (.out(tictac));
  not not_1 (not_1_out, ins_JUMPR);
  registers_8R registers_8r_1 (
    .dir_RA(dirA), .dir_RB(dirB), .enable(not_1_out), .dir_W(dirA), .reset(resetear), .clock(tictac),
    .dato_W(multiplexer_2_out), .RA(registers_8r_1_ra), .RB(registers_8r_1_rb));
  // Probe on multiplexer_2_out
  // Probe on multiplexer_2_out
  // Probe on multiplexer_2_out
  Multiplexer #(.select(2), .width(8)) multiplexer_2 (
    .in0(registers_8r_1_rb), .in1(adder_2_out), .in2({{5{1'b0}}, dirB}), .in3(multiplexer_3_out),
    .out(multiplexer_2_out), .sel(ope));
  Adder adder_2 (.a(registers_8r_1_ra), .b(registers_8r_1_rb), .out(adder_2_out));  // open: cin, cout
  assign not_2_out = ~registers_8r_1_ra;  // NOT_Gate not_2, 8 bits wide
  Multiplexer #(.select(3), .width(8)) multiplexer_3 (
    .in0(not_2_out), .in1({registers_8r_1_ra[3:0], registers_8r_1_ra[7:4]}),
    .in2({registers_8r_1_ra[0], registers_8r_1_ra[1], registers_8r_1_ra[2], registers_8r_1_ra[3], registers_8r_1_ra[4], registers_8r_1_ra[5], registers_8r_1_ra[6], registers_8r_1_ra[7]}),
    .in4({registers_8r_1_ra[6:0], 1'b0}), .in5({1'b0, registers_8r_1_ra[7:1]}),
    .in6({registers_8r_1_ra[6:0], registers_8r_1_ra[7]}),
    .in7({registers_8r_1_ra[0], registers_8r_1_ra[7:1]}), .out(multiplexer_3_out), .sel(dirB));  // open: in3

  // Other names for the same wires on the sheet: inm[2:0] = dirB; sel1arg[2:0] = dirB; step[2:0] = dirA

  // Notes on the sheet:
  //   contents of rom_1 (hex, n*v repeats v):
  //   a8 d0 f8 ae 42 72 43 73 9b b3 c3 87 b7 c7 c7 5*f7 f9 f9 0 f3 f1 e1 fb
  //   Zona de detección de instrucciones
  //   COPY
  //   SUM
  //   LOAD
  //   NOT
  //   XNOR?
  //   SWAPN
  //   FLIP
  //   JUMPR
  //   LSL
  //   LSR
  //   ROL
  //   ROR
endmodule

module Compu_2_1 (
);

  wire and_1_out, ins_JUMPR, ins_SRZ, nor_1_out, RA_zero, resetear, tictac;
  wire [1:0] ope, priority_encoder_1_out;
  wire [2:0] dirA, dirB;
  wire [7:0] adder_1_out, adder_2_out, bit_extender_1_out, counter_1_q, multiplexer_1_out, multiplexer_2_out,
       multiplexer_3_out, not_1_out, RA, registers_8r_1_rb;

  Counter counter_1 (
    .clr(resetear), .load(1'b1), .clk(tictac), .D(adder_1_out), .Q(counter_1_q));  // open: up, count, carry
  and and_1 (and_1_out, ins_SRZ, RA_zero);
  assign bit_extender_1_out = {{5{dirA[2]}}, dirA};  // Bit_Extender bit_extender_1
  Priority_Encoder #(.select(2)) priority_encoder_1 (
    .in0(1'b1), .in1(ins_JUMPR), .in2(and_1_out), .out(priority_encoder_1_out));  // open: in3, gs, en_out, en_in
  Multiplexer #(.select(2), .width(8)) multiplexer_1 (
    .in0(8'h1), .in1(bit_extender_1_out), .in2(8'h2), .out(multiplexer_1_out), .sel(priority_encoder_1_out));  // open: in3
  Adder adder_1 (.a(counter_1_q), .b(multiplexer_1_out), .out(adder_1_out));  // open: cin, cout
  ROM #(.misaligned("true")) rom_1 (
    .addr(counter_1_q), .data({ope[1], dirB[1:0], dirA[1:0], dirB[2], dirA[2], ope[0]}));
  Button button_1 (.out(resetear));
  and and_2 (ins_JUMPR, ope[0], ope[1], dirB[0], dirB[1], ~dirB[2]);  // AND_Gate
  and and_3 (ins_SRZ, ope[0], ope[1], dirB[0], dirB[1], dirB[2]);
  Button button_2 (.out(tictac));
  nor nor_1 (nor_1_out, ins_JUMPR, ins_SRZ);
  registers_8R registers_8r_1 (
    .dir_RA(dirA), .dir_RB(dirB), .enable(nor_1_out), .dir_W(dirA), .reset(resetear), .clock(tictac),
    .dato_W(multiplexer_2_out), .RA(RA), .RB(registers_8r_1_rb));
  // Probe on multiplexer_2_out
  // Probe on multiplexer_2_out
  // Probe on multiplexer_2_out
  Multiplexer #(.select(2), .width(8)) multiplexer_2 (
    .in0(registers_8r_1_rb), .in1(adder_2_out), .in2({{5{1'b0}}, dirB}), .in3(multiplexer_3_out),
    .out(multiplexer_2_out), .sel(ope));
  Adder adder_2 (.a(RA), .b(registers_8r_1_rb), .out(adder_2_out));  // open: cin, cout
  nor nor_2 (RA_zero, RA[0], RA[1], RA[2], RA[3], RA[4], RA[5], RA[6], RA[7]);
  assign not_1_out = ~RA;  // NOT_Gate not_1, 8 bits wide
  Multiplexer #(.select(3), .width(8)) multiplexer_3 (
    .in0(not_1_out), .in1({RA[3:0], RA[7:4]}),
    .in2({RA[0], RA[1], RA[2], RA[3], RA[4], RA[5], RA[6], RA[7]}), .in4({RA[6:0], 1'b0}),
    .in5({1'b0, RA[7:1]}), .in6({RA[6:0], RA[7]}), .in7({RA[0], RA[7:1]}), .out(multiplexer_3_out), .sel(dirB));  // open: in3

  // Other names for the same wires on the sheet: inm[2:0] = dirB; sel1arg[2:0] = dirB; step[2:0] = dirA

  // Notes on the sheet:
  //   contents of rom_1 (hex, n*v repeats v):
  //   a8 d0 f8 ae 42 72 43 73 9b b3 c3 87 b7 c7 c7 5*f7 f9 f9 0 f3 f1 e1 ff e5 e1 e1
  //   Zona de detección de instrucciones
  //   COPY
  //   SUM
  //   LOAD
  //   NOT
  //   XNOR?
  //   SWAPN
  //   FLIP
  //   JUMPR
  //   LSL
  //   LSR
  //   ROL
  //   ROR
endmodule

module Compu_2_2 (
);

  wire and_1_out, and_2_out, ins_JUMPR, ins_SER6, ins_SRZ, nor_1_out, or_1_out, RA_eqR6, RA_zero, resetear,
       tictac;
  wire [1:0] ope, priority_encoder_1_out;
  wire [2:0] dirA, dirB;
  wire [7:0] adder_1_out, adder_2_out, bit_extender_1_out, counter_1_q, multiplexer_1_out, multiplexer_2_out,
       multiplexer_3_out, not_1_out, RA, RB, xnor_1_out;

  Counter counter_1 (
    .clr(resetear), .load(1'b1), .clk(tictac), .D(adder_1_out), .Q(counter_1_q));  // open: up, count, carry
  and and_1 (and_1_out, ins_SRZ, RA_zero);
  or or_1 (or_1_out, and_1_out, and_2_out);
  and and_2 (and_2_out, ins_SER6, RA_eqR6);
  assign bit_extender_1_out = {{5{dirA[2]}}, dirA};  // Bit_Extender bit_extender_1
  Priority_Encoder #(.select(2)) priority_encoder_1 (
    .in0(1'b1), .in1(ins_JUMPR), .in2(or_1_out), .out(priority_encoder_1_out));  // open: in3, gs, en_out, en_in
  Multiplexer #(.select(2), .width(8)) multiplexer_1 (
    .in0(8'h1), .in1(bit_extender_1_out), .in2(8'h2), .out(multiplexer_1_out), .sel(priority_encoder_1_out));  // open: in3
  Adder adder_1 (.a(counter_1_q), .b(multiplexer_1_out), .out(adder_1_out));  // open: cin, cout
  ROM #(.misaligned("true")) rom_1 (
    .addr(counter_1_q), .data({ope[1], dirB[1:0], dirA[1:0], dirB[2], dirA[2], ope[0]}));
  Button button_1 (.out(resetear));
  and and_3 (ins_JUMPR, ope[0], ope[1], dirB[0], dirB[1], ~dirB[2]);  // AND_Gate
  and and_4 (ins_SRZ, ope[0], ope[1], dirB[0], dirB[1], dirB[2]);
  and and_5 (ins_SER6, ope[0], ope[1], ~dirB[0], dirB[1], dirB[2]);  // AND_Gate
  Button button_2 (.out(tictac));
  nor nor_1 (nor_1_out, ins_JUMPR, ins_SRZ, ins_SER6);
  registers_8R registers_8r_1 (
    .dir_RA(dirA), .dir_RB(dirB), .enable(nor_1_out), .dir_W(dirA), .reset(resetear), .clock(tictac),
    .dato_W(multiplexer_2_out), .RA(RA), .RB(RB));
  // Probe on multiplexer_2_out
  // Probe on multiplexer_2_out
  // Probe on multiplexer_2_out
  Multiplexer #(.select(2), .width(8)) multiplexer_2 (
    .in0(RB), .in1(adder_2_out), .in2({{5{1'b0}}, dirB}), .in3(multiplexer_3_out), .out(multiplexer_2_out),
    .sel(ope));
  Adder adder_2 (.a(RA), .b(RB), .out(adder_2_out));  // open: cin, cout
  nor nor_2 (RA_zero, RA[0], RA[1], RA[2], RA[3], RA[4], RA[5], RA[6], RA[7]);
  assign not_1_out = ~RA;  // NOT_Gate not_1, 8 bits wide
  Multiplexer #(.select(3), .width(8)) multiplexer_3 (
    .in0(not_1_out), .in1({RA[3:0], RA[7:4]}),
    .in2({RA[0], RA[1], RA[2], RA[3], RA[4], RA[5], RA[6], RA[7]}), .in4({RA[6:0], 1'b0}),
    .in5({1'b0, RA[7:1]}), .in6({RA[6:0], RA[7]}), .in7({RA[0], RA[7:1]}), .out(multiplexer_3_out), .sel(dirB));  // open: in3
  assign xnor_1_out = ~(RA ^ RB);  // XNOR_Gate xnor_1, 8 bits wide
  and and_6 (RA_eqR6, xnor_1_out[0], xnor_1_out[1], xnor_1_out[2], xnor_1_out[3], xnor_1_out[4], xnor_1_out[5], xnor_1_out[6], xnor_1_out[7]);

  // Other names for the same wires on the sheet: inm[2:0] = dirB; sel1arg[2:0] = dirB; step[2:0] = dirA

  // Notes on the sheet:
  //   contents of rom_1 (hex, n*v repeats v):
  //   a8 d0 f8 ae 42 72 43 73 9b b3 c3 87 b7 c7 c7 5*f7 f9 f9 0 f3 f1 e1 ff e5 e1 dd b9 dd e1 e1
  //   Zona de detección de instrucciones
  //   COPY
  //   SUM
  //   LOAD
  //   NOT
  //   XNOR?
  //   SWAPN
  //   FLIP
  //   JUMPR
  //   LSL
  //   LSR
  //   ROL
  //   ROR
endmodule

module Compu_2_3 (
);

  wire and_1_out, and_2_out, ins_JUMPR, ins_READ, ins_SER6, ins_SRZ, nor_1_out, or_1_out, RA_eqR6, RA_zero,
       resetear, tictac;
  wire [1:0] ope, priority_encoder_1_out;
  wire [2:0] dirA, dirB;
  wire [7:0] adder_1_out, adder_2_out, counter_1_q, multiplexer_1_out, multiplexer_2_out, multiplexer_3_out,
       not_1_out, RA, RB, xnor_1_out;

  Counter counter_1 (
    .clr(resetear), .load(1'b1), .clk(tictac), .D(adder_1_out), .Q(counter_1_q));  // open: up, count, carry
  and and_1 (and_1_out, ins_SRZ, RA_zero);
  or or_1 (or_1_out, and_1_out, and_2_out);
  and and_2 (and_2_out, ins_SER6, RA_eqR6);
  Priority_Encoder #(.select(2)) priority_encoder_1 (
    .in0(1'b1), .in1(ins_JUMPR), .in2(or_1_out), .out(priority_encoder_1_out));  // open: in3, gs, en_out, en_in
  Multiplexer #(.select(2), .width(8)) multiplexer_1 (
    .in0(8'h1), .in1(RA), .in2(8'h2), .out(multiplexer_1_out), .sel(priority_encoder_1_out));  // open: in3
  Adder adder_1 (.a(counter_1_q), .b(multiplexer_1_out), .out(adder_1_out));  // open: cin, cout
  ROM #(.misaligned("true")) rom_1 (
    .addr(counter_1_q), .data({ope[1], dirB[1:0], dirA[1:0], dirB[2], dirA[2], ope[0]}));
  and and_3 (ins_JUMPR, ope[0], ope[1], dirB[0], dirB[1], ~dirB[2]);  // AND_Gate
  and and_4 (ins_SRZ, ope[0], ope[1], dirB[0], dirB[1], dirB[2]);
  and and_5 (ins_SER6, ope[0], ope[1], ~dirB[0], dirB[1], dirB[2]);  // AND_Gate
  Button button_1 ();  // open: out
  Clock clock_1 (.out(tictac));
  Button button_2 (.out(resetear));
  nor nor_1 (nor_1_out, ins_JUMPR, ins_SRZ, ins_SER6);
  registers_8R registers_8r_1 (
    .dir_RA(dirA), .dir_RB(dirB), .enable(nor_1_out), .dir_W(dirA), .reset(resetear), .clock(tictac),
    .dato_W(multiplexer_2_out), .RA(RA), .RB(RB));
  // Probe on multiplexer_2_out
  // Probe on multiplexer_2_out
  // Probe on multiplexer_2_out
  and and_6 (ins_READ, ~ope[0], ~ope[1]);  // AND_Gate
  Multiplexer #(.select(2), .width(8)) multiplexer_2 (
    .in0(RB), .in1(adder_2_out), .in2({{5{1'b0}}, dirB}), .in3(multiplexer_3_out), .out(multiplexer_2_out),
    .sel(ope));
  Adder adder_2 (.a(RA), .b(RB), .out(adder_2_out));  // open: cin, cout
  nor nor_2 (RA_zero, RA[0], RA[1], RA[2], RA[3], RA[4], RA[5], RA[6], RA[7]);
  assign not_1_out = ~RA;  // NOT_Gate not_1, 8 bits wide
  Multiplexer #(.select(3), .width(8)) multiplexer_3 (
    .in0(not_1_out), .in1({RA[3:0], RA[7:4]}),
    .in2({RA[0], RA[1], RA[2], RA[3], RA[4], RA[5], RA[6], RA[7]}), .in4({RA[6:0], 1'b0}),
    .in5({1'b0, RA[7:1]}), .out(multiplexer_3_out), .sel(dirB));  // open: in3, in6, in7
  assign xnor_1_out = ~(RA ^ RB);  // XNOR_Gate xnor_1, 8 bits wide
  and and_7 (RA_eqR6, xnor_1_out[0], xnor_1_out[1], xnor_1_out[2], xnor_1_out[3], xnor_1_out[4], xnor_1_out[5], xnor_1_out[6], xnor_1_out[7]);

  // Other names for the same wires on the sheet: inm[2:0] = dirB; sel1arg[2:0] = dirB; step[7:0] = RA

  // Notes on the sheet:
  //   contents of rom_1 (hex, n*v repeats v):
  //   a8 d0 f8 ae 43 43 73 73 9b b3 b3 c3 f3 5*0 87 a7 ed f1 e1 e5 e1 f9 0 0 a3 43 43 c7 e1 e1
  //   Zona de detección de instrucciones
  //   COPY
  //   SUM
  //   LOAD
  //   NOT
  //   SWAPN
  //   FLIP
  //   JUMPR
  //   LSL
  //   LSR
  //   SER6
  //   SRZ
endmodule

module Compu_3_1 (
);

  wire and_1_out, and_2_out, ins_JUMPR, ins_READ, ins_SER6, ins_SRZ, nor_1_out, or_1_out, RA_eqR6, RA_zero,
       resetear, tictac;
  wire [1:0] ope, priority_encoder_1_out;
  wire [2:0] dirA, dirB;
  wire [7:0] adder_1_out, adder_2_out, counter_1_q, multiplexer_1_out, multiplexer_2_out, multiplexer_3_out,
       multiplexer_4_out, not_1_out, RA, RB, xnor_1_out;

  Counter counter_1 (
    .clr(resetear), .load(1'b1), .clk(tictac), .D(adder_1_out), .Q(counter_1_q));  // open: up, count, carry
  and and_1 (and_1_out, ins_SRZ, RA_zero);
  or or_1 (or_1_out, and_1_out, and_2_out);
  and and_2 (and_2_out, ins_SER6, RA_eqR6);
  Priority_Encoder #(.select(2)) priority_encoder_1 (
    .in0(1'b1), .in1(ins_JUMPR), .in2(or_1_out), .out(priority_encoder_1_out));  // open: in3, gs, en_out, en_in
  Multiplexer #(.select(2), .width(8)) multiplexer_1 (
    .in0(8'h1), .in1(RA), .in2(8'h2), .out(multiplexer_1_out), .sel(priority_encoder_1_out));  // open: in3
  Adder adder_1 (.a(counter_1_q), .b(multiplexer_1_out), .out(adder_1_out));  // open: cin, cout
  Multiplexer #(.width(8)) multiplexer_2 (.in0(counter_1_q), .in1(RB), .out(multiplexer_2_out), .sel(ins_READ));
  ROM #(.misaligned("true")) rom_1 (
    .addr(multiplexer_2_out), .data({ope[1], dirB[1:0], dirA[1:0], dirB[2], dirA[2], ope[0]}));
  and and_3 (ins_JUMPR, ope[0], ope[1], dirB[0], dirB[1], ~dirB[2]);  // AND_Gate
  and and_4 (ins_SRZ, ope[0], ope[1], dirB[0], dirB[1], dirB[2]);
  and and_5 (ins_SER6, ope[0], ope[1], ~dirB[0], dirB[1], dirB[2]);  // AND_Gate
  Button button_1 ();  // open: out
  Clock clock_1 (.out(tictac));
  Button button_2 (.out(resetear));
  nor nor_1 (nor_1_out, ins_JUMPR, ins_SRZ, ins_SER6);
  registers_8R registers_8r_1 (
    .dir_RA(dirA), .dir_RB(dirB), .enable(nor_1_out), .dir_W(dirA), .reset(resetear), .clock(tictac),
    .dato_W(multiplexer_3_out), .RA(RA), .RB(RB));
  // Probe on multiplexer_3_out
  // Probe on multiplexer_3_out
  // Probe on multiplexer_3_out
  and and_6 (ins_READ, ~ope[0], ~ope[1]);  // AND_Gate
  Multiplexer #(.select(2), .width(8)) multiplexer_3 (
    .in0({ope[1], dirB[1:0], dirA[1:0], dirB[2], dirA[2], ope[0]}), .in1(adder_2_out),
    .in2({{5{1'b0}}, dirB}), .in3(multiplexer_4_out), .out(multiplexer_3_out), .sel(ope));
  Adder adder_2 (.a(RA), .b(RB), .out(adder_2_out));  // open: cin, cout
  nor nor_2 (RA_zero, RA[0], RA[1], RA[2], RA[3], RA[4], RA[5], RA[6], RA[7]);
  assign not_1_out = ~RA;  // NOT_Gate not_1, 8 bits wide
  Multiplexer #(.select(3), .width(8)) multiplexer_4 (
    .in0(not_1_out), .in1({RA[3:0], RA[7:4]}),
    .in2({RA[0], RA[1], RA[2], RA[3], RA[4], RA[5], RA[6], RA[7]}), .in4({RA[6:0], 1'b0}),
    .in5({1'b0, RA[7:1]}), .out(multiplexer_4_out), .sel(dirB));  // open: in3, in6, in7
  assign xnor_1_out = ~(RA ^ RB);  // XNOR_Gate xnor_1, 8 bits wide
  and and_7 (RA_eqR6, xnor_1_out[0], xnor_1_out[1], xnor_1_out[2], xnor_1_out[3], xnor_1_out[4], xnor_1_out[5], xnor_1_out[6], xnor_1_out[7]);

  // Other names for the same wires on the sheet: inm[2:0] = dirB;
  //   RAM_out[7:0] = {ope[1], dirB[1:0], dirA[1:0], dirB[2], dirA[2], ope[0]}; sel1arg[2:0] = dirB; step[7:0] = RA;
  //   RB_ptr[7:0] = RB

  // Notes on the sheet:
  //   contents of rom_1 (hex, n*v repeats v):
  //   a8 d0 f8 ae 43 43 73 73 9b b3 b3 c3 f3 5*0 87 a7 ed f1 e1 e5 e1 f9 0 0 a3 43 43 c7 e1 e1
  //   Zona de detección de instrucciones
  //   READ
  //   SUM
  //   LOAD
  //   NOT
  //   SWAPN
  //   FLIP
  //   JUMPR
  //   LSL
  //   LSR
  //   SER6
  //   SRZ
endmodule

module Compu_3_2 (
);

  wire and_1_out, and_2_out, and_3_out, and_7_out, exe, fetch_decode, ins_JUMPR, ins_READ, ins_SER6, ins_SRZ,
       nor_1_out, or_1_out, RA_eqR6, RA_zero, resetear, tictac;
  wire [1:0] ope, priority_encoder_1_out;
  wire [2:0] dirA, dirB;
  wire [7:0] adder_1_out, adder_2_out, counter_1_q, multiplexer_1_out, multiplexer_2_out, multiplexer_3_out,
       multiplexer_4_out, multiplexer_5_out, not_1_out, RA, RAM_out, RB, xnor_1_out;

  Counter counter_1 (
    .clr(resetear), .load(1'b1), .clk(tictac), .D(adder_1_out), .Q(counter_1_q));  // open: up, count, carry
  and and_1 (and_1_out, ins_SRZ, RA_zero);
  or or_1 (or_1_out, and_1_out, and_2_out);
  and and_2 (and_2_out, ins_SER6, RA_eqR6);
  Priority_Encoder #(.select(2)) priority_encoder_1 (
    .in0(1'b1), .in1(ins_JUMPR), .in2(or_1_out), .out(priority_encoder_1_out));  // open: in3, gs, en_out, en_in
  D_Flip_Flop d_ff_1 (.D(fetch_decode), .clk(tictac), .Q(exe), .Qn(fetch_decode), .reset(resetear));  // open: preset
  Multiplexer #(.width(8)) multiplexer_1 (.in0({8{1'b0}}), .in1(multiplexer_2_out), .out(multiplexer_1_out), .sel(exe));
  Multiplexer #(.select(2), .width(8)) multiplexer_2 (
    .in0(8'h1), .in1(RA), .in2(8'h2), .out(multiplexer_2_out), .sel(priority_encoder_1_out));  // open: in3
  Adder adder_1 (.a(counter_1_q), .b(multiplexer_1_out), .out(adder_1_out));  // open: cin, cout
  and and_3 (and_3_out, exe, ins_READ);
  Multiplexer #(.width(8)) multiplexer_3 (.in0(counter_1_q), .in1(RB), .out(multiplexer_3_out), .sel(and_3_out));
  ROM #(.misaligned("true")) rom_1 (.addr(multiplexer_3_out), .data(RAM_out));
  Register IR (
    .D(RAM_out), .en(fetch_decode), .clk(tictac),
    .Q({ope[1], dirB[1:0], dirA[1:0], dirB[2], dirA[2], ope[0]}), .clr(resetear));
  and and_4 (ins_JUMPR, ope[0], ope[1], dirB[0], dirB[1], ~dirB[2]);  // AND_Gate
  and and_5 (ins_SRZ, ope[0], ope[1], dirB[0], dirB[1], dirB[2]);
  and and_6 (ins_SER6, ope[0], ope[1], ~dirB[0], dirB[1], dirB[2]);  // AND_Gate
  Button button_1 ();  // open: out
  Clock clock_1 (.out(tictac));
  and and_7 (and_7_out, exe, nor_1_out);
  Button button_2 (.out(resetear));
  nor nor_1 (nor_1_out, ins_JUMPR, ins_SRZ, ins_SER6);
  registers_8R registers_8r_1 (
    .dir_RA(dirA), .dir_RB(dirB), .enable(and_7_out), .dir_W(dirA), .reset(resetear), .clock(tictac),
    .dato_W(multiplexer_4_out), .RA(RA), .RB(RB));
  // Probe on multiplexer_4_out
  // Probe on multiplexer_4_out
  // Probe on multiplexer_4_out
  and and_8 (ins_READ, ~ope[0], ~ope[1]);  // AND_Gate
  Multiplexer #(.select(2), .width(8)) multiplexer_4 (
    .in0(RAM_out), .in1(adder_2_out), .in2({{5{1'b0}}, dirB}), .in3(multiplexer_5_out),
    .out(multiplexer_4_out), .sel(ope));
  Adder adder_2 (.a(RA), .b(RB), .out(adder_2_out));  // open: cin, cout
  nor nor_2 (RA_zero, RA[0], RA[1], RA[2], RA[3], RA[4], RA[5], RA[6], RA[7]);
  assign not_1_out = ~RA;  // NOT_Gate not_1, 8 bits wide
  Multiplexer #(.select(3), .width(8)) multiplexer_5 (
    .in0(not_1_out), .in1({RA[3:0], RA[7:4]}),
    .in2({RA[0], RA[1], RA[2], RA[3], RA[4], RA[5], RA[6], RA[7]}), .in4({RA[6:0], 1'b0}),
    .in5({1'b0, RA[7:1]}), .out(multiplexer_5_out), .sel(dirB));  // open: in3, in6, in7
  assign xnor_1_out = ~(RA ^ RB);  // XNOR_Gate xnor_1, 8 bits wide
  and and_9 (RA_eqR6, xnor_1_out[0], xnor_1_out[1], xnor_1_out[2], xnor_1_out[3], xnor_1_out[4], xnor_1_out[5], xnor_1_out[6], xnor_1_out[7]);

  // Other names for the same wires on the sheet: inm[2:0] = dirB; sel1arg[2:0] = dirB; step[7:0] = RA;
  //   RB_ptr[7:0] = RB

  // Notes on the sheet:
  //   contents of rom_1 (hex, n*v repeats v):
  //   a8 d0 f8 ae 43 43 73 73 9b b3 b3 c3 f3 5*0 87 a7 ed f1 e1 e5 e1 f9 0 0 a3 43 43 c7 e1 43 a3 16 23 16
  //   e1 89*0 ca fe da d 12 34 45
  //   Zona de detección de instrucciones
  //   READ
  //   SUM
  //   LOAD
  //   NOT
  //   SWAPN
  //   FLIP
  //   JUMPR
  //   LSL
  //   LSR
  //   SER6
  //   SRZ
endmodule

module Compu_3_3 (
);

  wire and_1_out, and_2_out, and_3_out, and_8_out, exe, fetch_decode, ins_JUMPR, ins_READ, ins_SER6, ins_SRZ,
       ins_WRITE, nor_1_out, or_1_out, or_2_out, RA_eqR6, RA_zero, resetear, tictac, WE_RAM;
  wire [1:0] ope, priority_encoder_1_out;
  wire [2:0] dirA, dirB;
  wire [7:0] adder_1_out, adder_2_out, counter_1_q, multiplexer_1_out, multiplexer_2_out, multiplexer_3_out,
       multiplexer_4_out, multiplexer_5_out, not_1_out, RA, RAM_out, RB, xnor_1_out;

  Counter counter_1 (
    .clr(resetear), .load(1'b1), .clk(tictac), .D(adder_1_out), .Q(counter_1_q));  // open: up, count, carry
  and and_1 (and_1_out, ins_SRZ, RA_zero);
  or or_1 (or_1_out, and_1_out, and_2_out);
  and and_2 (and_2_out, ins_SER6, RA_eqR6);
  Priority_Encoder #(.select(2)) priority_encoder_1 (
    .in0(1'b1), .in1(ins_JUMPR), .in2(or_1_out), .out(priority_encoder_1_out));  // open: in3, gs, en_out, en_in
  D_Flip_Flop d_ff_1 (.D(fetch_decode), .clk(tictac), .Q(exe), .Qn(fetch_decode), .reset(resetear));  // open: preset
  Multiplexer #(.width(8)) multiplexer_1 (.in0({8{1'b0}}), .in1(multiplexer_2_out), .out(multiplexer_1_out), .sel(exe));
  Multiplexer #(.select(2), .width(8)) multiplexer_2 (
    .in0(8'h1), .in1(RA), .in2(8'h2), .out(multiplexer_2_out), .sel(priority_encoder_1_out));  // open: in3
  Adder adder_1 (.a(counter_1_q), .b(multiplexer_1_out), .out(adder_1_out));  // open: cin, cout
  and and_3 (and_3_out, exe, or_2_out);
  or or_2 (or_2_out, ins_READ, ins_WRITE);
  Multiplexer #(.width(8)) multiplexer_3 (.in0(counter_1_q), .in1(RB), .out(multiplexer_3_out), .sel(and_3_out));
  RAM #(.asyncread("true"), .\type ("nonvolatile")) ram_1 (
    .addr(multiplexer_3_out), .we(WE_RAM), .clk(tictac), .din(RA), .dout(RAM_out));  // open: oe
  // Probe on RA
  // Probe on RA
  // Probe on RA
  and and_4 (WE_RAM, ins_WRITE, exe);
  Register IR (
    .D(RAM_out), .en(fetch_decode), .clk(tictac),
    .Q({ope[1], dirB[1:0], dirA[1:0], dirB[2], dirA[2], ope[0]}), .clr(resetear));
  and and_5 (ins_JUMPR, ope[0], ope[1], dirB[0], dirB[1], ~dirB[2]);  // AND_Gate
  and and_6 (ins_SRZ, ope[0], ope[1], dirB[0], dirB[1], dirB[2]);
  and and_7 (ins_SER6, ope[0], ope[1], ~dirB[0], dirB[1], dirB[2]);  // AND_Gate
  Button button_1 ();  // open: out
  Clock clock_1 (.out(tictac));
  and and_8 (and_8_out, exe, nor_1_out);
  Button button_2 (.out(resetear));
  nor nor_1 (nor_1_out, ins_WRITE, ins_JUMPR, ins_SRZ, ins_SER6);
  registers_8R registers_8r_1 (
    .dir_RA(dirA), .dir_RB(dirB), .enable(and_8_out), .dir_W(dirA), .reset(resetear), .clock(tictac),
    .dato_W(multiplexer_4_out), .RA(RA), .RB(RB));
  // Probe on multiplexer_4_out
  // Probe on multiplexer_4_out
  // Probe on multiplexer_4_out
  and and_9 (ins_READ, ~ope[0], ~ope[1], dirB[2]);  // AND_Gate
  and and_10 (ins_WRITE, ~ope[0], ~ope[1], ~dirB[2]);  // AND_Gate
  Multiplexer #(.select(2), .width(8)) multiplexer_4 (
    .in0(RAM_out), .in1(adder_2_out), .in2({{5{1'b0}}, dirB}), .in3(multiplexer_5_out),
    .out(multiplexer_4_out), .sel(ope));
  Adder adder_2 (.a(RA), .b(RB), .out(adder_2_out));  // open: cin, cout
  nor nor_2 (RA_zero, RA[0], RA[1], RA[2], RA[3], RA[4], RA[5], RA[6], RA[7]);
  assign not_1_out = ~RA;  // NOT_Gate not_1, 8 bits wide
  Multiplexer #(.select(3), .width(8)) multiplexer_5 (
    .in0(not_1_out), .in1({RA[3:0], RA[7:4]}),
    .in2({RA[0], RA[1], RA[2], RA[3], RA[4], RA[5], RA[6], RA[7]}), .in4({RA[6:0], 1'b0}),
    .in5({1'b0, RA[7:1]}), .out(multiplexer_5_out), .sel(dirB));  // open: in3, in6, in7
  assign xnor_1_out = ~(RA ^ RB);  // XNOR_Gate xnor_1, 8 bits wide
  and and_11 (RA_eqR6, xnor_1_out[0], xnor_1_out[1], xnor_1_out[2], xnor_1_out[3], xnor_1_out[4], xnor_1_out[5], xnor_1_out[6], xnor_1_out[7]);

  // Other names for the same wires on the sheet: inm[2:0] = dirB; sel1arg[2:0] = dirB; RW_sel = dirB[2];
  //   step[7:0] = RA; RB_ptr[7:0] = RB

  // Notes on the sheet:
  //   Zona de detección de instrucciones
  //   READ
  //   SUM
  //   LOAD
  //   NOT
  //   SWAPN
  //   FLIP
  //   JUMPR
  //   LSL
  //   LSR
  //   SER6
  //   SRZ
endmodule

module Compu_4_1 (
);

  wire and_1_out, and_2_out, and_3_out, and_9_out, exe, fetch_decode, ins_CALL, ins_CALL_exe, ins_JUMPR,
       ins_READ, ins_RET, ins_SER6, ins_SRZ, ins_WRITE, nor_1_out, or_1_out, or_2_out, or_3_out, RA_eqR6,
       RA_zero, resetear, tictac, WE_RAM;
  wire [1:0] ope, priority_encoder_1_out;
  wire [2:0] dirA, dirB;
  wire [7:0] adder_1_out, adder_2_out, adder_3_out, multiplexer_1_out, multiplexer_2_out, multiplexer_3_out,
       multiplexer_4_out, multiplexer_5_out, multiplexer_6_out, multiplexer_7_out, multiplexer_8_out,
       not_1_out, PC_output, RA, RAM_out, RB, xnor_1_out;

  Counter counter_1 (
    .clr(resetear), .load(1'b1), .clk(tictac), .D(multiplexer_3_out), .Q(PC_output));  // open: up, count, carry
  and and_1 (and_1_out, ins_SRZ, RA_zero);
  or or_1 (or_1_out, and_1_out, and_2_out);
  and and_2 (and_2_out, ins_SER6, RA_eqR6);
  Priority_Encoder #(.select(2)) priority_encoder_1 (
    .in0(1'b1), .in1(ins_JUMPR), .in2(or_1_out), .out(priority_encoder_1_out));  // open: in3, gs, en_out, en_in
  D_Flip_Flop d_ff_1 (.D(fetch_decode), .clk(tictac), .Q(exe), .Qn(fetch_decode), .reset(resetear));  // open: preset
  Multiplexer #(.width(8)) multiplexer_1 (.in0({8{1'b0}}), .in1(multiplexer_2_out), .out(multiplexer_1_out), .sel(exe));
  Multiplexer #(.select(2), .width(8)) multiplexer_2 (
    .in0(8'h1), .in1(RA), .in2(8'h2), .out(multiplexer_2_out), .sel(priority_encoder_1_out));  // open: in3
  Adder adder_1 (.a(PC_output), .b(multiplexer_1_out), .out(adder_1_out));  // open: cin, cout
  Multiplexer #(.width(8)) multiplexer_3 (.in0(adder_1_out), .in1(RA), .out(multiplexer_3_out), .sel(ins_CALL_exe));
  Multiplexer #(.width(8)) multiplexer_4 (.in0(RB), .in1({8{1'b1}}), .out(multiplexer_4_out), .sel(ins_CALL_exe));
  and and_3 (and_3_out, exe, or_2_out);
  or or_2 (or_2_out, ins_READ, ins_WRITE, ins_CALL);
  Multiplexer #(.width(8)) multiplexer_5 (
    .in0(PC_output), .in1(multiplexer_4_out), .out(multiplexer_5_out), .sel(and_3_out));
  Adder adder_2 (.a(PC_output), .b(8'h1), .out(adder_2_out));  // open: cin, cout
  RAM #(.asyncread("true"), .\type ("nonvolatile")) ram_1 (
    .addr(multiplexer_5_out), .we(WE_RAM), .clk(tictac), .din(multiplexer_6_out), .dout(RAM_out));  // open: oe
  // Probe on multiplexer_6_out
  // Probe on multiplexer_6_out
  // Probe on multiplexer_6_out
  Multiplexer #(.width(8)) multiplexer_6 (.in0(RA), .in1(adder_2_out), .out(multiplexer_6_out), .sel(ins_CALL_exe));
  and and_4 (ins_CALL_exe, ins_CALL, exe);
  or or_3 (or_3_out, ins_WRITE, ins_CALL);
  and and_5 (WE_RAM, or_3_out, exe);
  Register IR (
    .D(RAM_out), .en(fetch_decode), .clk(tictac),
    .Q({ope[1], dirB[1:0], dirA[1:0], dirB[2], dirA[2], ope[0]}), .clr(resetear));
  and and_6 (ins_JUMPR, ope[0], ope[1], dirB[0], dirB[1], ~dirB[2]);  // AND_Gate
  and and_7 (ins_SRZ, ope[0], ope[1], dirB[0], dirB[1], dirB[2]);
  and and_8 (ins_SER6, ope[0], ope[1], ~dirB[0], dirB[1], dirB[2]);  // AND_Gate
  Button button_1 ();  // open: out
  Clock clock_1 (.out(tictac));
  and and_9 (and_9_out, exe, nor_1_out);
  Button button_2 (.out(resetear));
  nor nor_1 (nor_1_out, ins_CALL, ins_WRITE, ins_JUMPR, ins_SRZ, ins_SER6);
  registers_8R registers_8r_1 (
    .dir_RA(dirA), .dir_RB(dirB), .enable(and_9_out), .dir_W(dirA), .reset(resetear), .clock(tictac),
    .dato_W(multiplexer_7_out), .RA(RA), .RB(RB));
  // Probe on multiplexer_7_out
  // Probe on multiplexer_7_out
  // Probe on multiplexer_7_out
  and and_10 (ins_READ, ~ope[0], ~ope[1], dirB[2]);  // AND_Gate
  and and_11 (ins_WRITE, ~ope[0], ~ope[1], ~dirB[2]);  // AND_Gate
  Multiplexer #(.select(2), .width(8)) multiplexer_7 (
    .in0(RAM_out), .in1(adder_3_out), .in2({{5{1'b0}}, dirB}), .in3(multiplexer_8_out),
    .out(multiplexer_7_out), .sel(ope));
  Adder adder_3 (.a(RA), .b(RB), .out(adder_3_out));  // open: cin, cout
  nor nor_2 (RA_zero, RA[0], RA[1], RA[2], RA[3], RA[4], RA[5], RA[6], RA[7]);
  assign not_1_out = ~RA;  // NOT_Gate not_1, 8 bits wide
  Multiplexer #(.select(3), .width(8)) multiplexer_8 (
    .in0(not_1_out), .in4({RA[6:0], 1'b0}), .in5({1'b0, RA[7:1]}), .out(multiplexer_8_out), .sel(dirB));  // open: in1, in2, in3, in6, in7
  assign xnor_1_out = ~(RA ^ RB);  // XNOR_Gate xnor_1, 8 bits wide
  and and_12 (ins_CALL, ope[0], ope[1], ~dirB[0], dirB[1], ~dirB[2]);  // AND_Gate
  and and_13 (ins_RET, ope[0], ope[1], dirB[0], ~dirB[1], ~dirB[2], ~dirA[0], ~dirA[1], ~dirA[2]);  // AND_Gate
  and and_14 (RA_eqR6, xnor_1_out[0], xnor_1_out[1], xnor_1_out[2], xnor_1_out[3], xnor_1_out[4], xnor_1_out[5], xnor_1_out[6], xnor_1_out[7]);

  // Other names for the same wires on the sheet: inm[2:0] = dirB; sel1arg[2:0] = dirB; RW_sel = dirB[2];
  //   step[7:0] = RA; RB_ptr[7:0] = RB; sel0arg[2:0] = dirA

  // Notes on the sheet:
  //   Zona de detección de instrucciones
  //   READ
  //   SUM
  //   LOAD
  //   NOT
  //   RET
  //   CALL
  //   JUMPR
  //   LSL
  //   LSR
  //   SER6
  //   SRZ
endmodule

module Compu_4_2 (
);

  wire and_1_out, and_2_out, and_3_out, and_9_out, exe, fetch_decode, ins_CALL, ins_JUMPR, ins_READ, ins_RET,
       ins_SER6, ins_SRZ, ins_SUBROUTINE, ins_WRITE, nor_1_out, or_1_out, or_2_out, or_3_out, or_4_out,
       RA_eqR6, RA_zero, resetear, tictac, WE_RAM;
  wire [1:0] ope, priority_encoder_1_out;
  wire [2:0] dirA, dirB;
  wire [7:0] adder_1_out, adder_2_out, adder_3_out, multiplexer_1_out, multiplexer_2_out, multiplexer_3_out,
       multiplexer_4_out, multiplexer_5_out, multiplexer_6_out, multiplexer_7_out, multiplexer_8_out,
       multiplexer_9_out, not_1_out, PC_output, RA, RAM_out, RB, xnor_1_out;

  Counter counter_1 (
    .clr(resetear), .load(1'b1), .clk(tictac), .D(multiplexer_3_out), .Q(PC_output));  // open: up, count, carry
  and and_1 (and_1_out, ins_SRZ, RA_zero);
  or or_1 (or_1_out, and_1_out, and_2_out);
  and and_2 (and_2_out, ins_SER6, RA_eqR6);
  Priority_Encoder #(.select(2)) priority_encoder_1 (
    .in0(1'b1), .in1(ins_JUMPR), .in2(or_1_out), .out(priority_encoder_1_out));  // open: in3, gs, en_out, en_in
  D_Flip_Flop d_ff_1 (.D(fetch_decode), .clk(tictac), .Q(exe), .Qn(fetch_decode), .reset(resetear));  // open: preset
  Multiplexer #(.width(8)) multiplexer_1 (.in0({8{1'b0}}), .in1(multiplexer_2_out), .out(multiplexer_1_out), .sel(exe));
  Multiplexer #(.select(2), .width(8)) multiplexer_2 (
    .in0(8'h1), .in1(RA), .in2(8'h2), .out(multiplexer_2_out), .sel(priority_encoder_1_out));  // open: in3
  Adder adder_1 (.a(PC_output), .b(multiplexer_1_out), .out(adder_1_out));  // open: cin, cout
  Multiplexer #(.width(8)) multiplexer_3 (
    .in0(adder_1_out), .in1(multiplexer_4_out), .out(multiplexer_3_out), .sel(ins_SUBROUTINE));
  Multiplexer #(.width(8)) multiplexer_4 (.in0(RA), .in1(RAM_out), .out(multiplexer_4_out), .sel(ins_RET));
  Multiplexer #(.width(8)) multiplexer_5 (.in0(RB), .in1({8{1'b1}}), .out(multiplexer_5_out), .sel(ins_SUBROUTINE));
  and and_3 (and_3_out, exe, or_2_out);
  or or_2 (or_2_out, ins_READ, ins_WRITE, ins_CALL, ins_RET);
  Multiplexer #(.width(8)) multiplexer_6 (
    .in0(PC_output), .in1(multiplexer_5_out), .out(multiplexer_6_out), .sel(and_3_out));
  Adder adder_2 (.a(PC_output), .b(8'h1), .out(adder_2_out));  // open: cin, cout
  or or_3 (or_3_out, ins_CALL, ins_RET);
  RAM #(.asyncread("true"), .\type ("nonvolatile")) ram_1 (
    .addr(multiplexer_6_out), .we(WE_RAM), .clk(tictac), .din(multiplexer_7_out), .dout(RAM_out));  // open: oe
  // Probe on multiplexer_7_out
  // Probe on multiplexer_7_out
  // Probe on multiplexer_7_out
  Multiplexer #(.width(8)) multiplexer_7 (.in0(RA), .in1(adder_2_out), .out(multiplexer_7_out), .sel(ins_SUBROUTINE));
  and and_4 (ins_SUBROUTINE, or_3_out, exe);
  or or_4 (or_4_out, ins_WRITE, ins_CALL);
  and and_5 (WE_RAM, or_4_out, exe);
  Register IR (
    .D(RAM_out), .en(fetch_decode), .clk(tictac),
    .Q({ope[1], dirB[1:0], dirA[1:0], dirB[2], dirA[2], ope[0]}), .clr(resetear));
  and and_6 (ins_JUMPR, ope[0], ope[1], dirB[0], dirB[1], ~dirB[2]);  // AND_Gate
  and and_7 (ins_SRZ, ope[0], ope[1], dirB[0], dirB[1], dirB[2]);
  and and_8 (ins_SER6, ope[0], ope[1], ~dirB[0], dirB[1], dirB[2]);  // AND_Gate
  Button button_1 ();  // open: out
  Clock clock_1 (.out(tictac));
  and and_9 (and_9_out, exe, nor_1_out);
  Button button_2 (.out(resetear));
  nor nor_1 (nor_1_out, ins_RET, ins_CALL, ins_WRITE, ins_JUMPR, ins_SRZ, ins_SER6);
  registers_8R registers_8r_1 (
    .dir_RA(dirA), .dir_RB(dirB), .enable(and_9_out), .dir_W(dirA), .reset(resetear), .clock(tictac),
    .dato_W(multiplexer_8_out), .RA(RA), .RB(RB));
  // Probe on multiplexer_8_out
  // Probe on multiplexer_8_out
  // Probe on multiplexer_8_out
  and and_10 (ins_READ, ~ope[0], ~ope[1], dirB[2]);  // AND_Gate
  and and_11 (ins_WRITE, ~ope[0], ~ope[1], ~dirB[2]);  // AND_Gate
  Multiplexer #(.select(2), .width(8)) multiplexer_8 (
    .in0(RAM_out), .in1(adder_3_out), .in2({{5{1'b0}}, dirB}), .in3(multiplexer_9_out),
    .out(multiplexer_8_out), .sel(ope));
  Adder adder_3 (.a(RA), .b(RB), .out(adder_3_out));  // open: cin, cout
  nor nor_2 (RA_zero, RA[0], RA[1], RA[2], RA[3], RA[4], RA[5], RA[6], RA[7]);
  assign not_1_out = ~RA;  // NOT_Gate not_1, 8 bits wide
  Multiplexer #(.select(3), .width(8)) multiplexer_9 (
    .in0(not_1_out), .in4({RA[6:0], 1'b0}), .in5({1'b0, RA[7:1]}), .out(multiplexer_9_out), .sel(dirB));  // open: in1, in2, in3, in6, in7
  assign xnor_1_out = ~(RA ^ RB);  // XNOR_Gate xnor_1, 8 bits wide
  and and_12 (ins_CALL, ope[0], ope[1], ~dirB[0], dirB[1], ~dirB[2]);  // AND_Gate
  and and_13 (ins_RET, ope[0], ope[1], dirB[0], ~dirB[1], ~dirB[2], ~dirA[0], ~dirA[1], ~dirA[2]);  // AND_Gate
  and and_14 (RA_eqR6, xnor_1_out[0], xnor_1_out[1], xnor_1_out[2], xnor_1_out[3], xnor_1_out[4], xnor_1_out[5], xnor_1_out[6], xnor_1_out[7]);

  // Other names for the same wires on the sheet: inm[2:0] = dirB; sel1arg[2:0] = dirB; RW_sel = dirB[2];
  //   step[7:0] = RA; RB_ptr[7:0] = RB; sel0arg[2:0] = dirA

  // Notes on the sheet:
  //   Zona de detección de instrucciones
  //   READ
  //   SUM
  //   LOAD
  //   NOT
  //   RET
  //   CALL
  //   JUMPR
  //   LSL
  //   LSR
  //   SER6
  //   SRZ
endmodule

module Compu_5_1 (
);

  wire and_1_out, and_2_out, and_3_out, and_10_out, exe, fetch_decode, ins_CALL, ins_JUMPR, ins_READ,
       ins_RET, ins_SER6, ins_SRZ, ins_SUBROUTINE, ins_WIO0, ins_WIO1, ins_WIO2, ins_WIO3, ins_WIO_global,
       ins_WRITE, nor_1_out, or_1_out, or_2_out, or_3_out, or_4_out, RA_eqR6, RA_zero, resetear, tictac,
       WE_RAM;
  wire [1:0] ope, priority_encoder_1_out;
  wire [2:0] dirA, dirB;
  wire [7:0] adder_1_out, adder_2_out, adder_3_out, multiplexer_1_out, multiplexer_2_out, multiplexer_3_out,
       multiplexer_4_out, multiplexer_5_out, multiplexer_6_out, multiplexer_7_out, multiplexer_8_out,
       multiplexer_9_out, multiplexer_10_out, not_1_out, PC_output, RA, RAM_out, RB, RIO1_data, RIO2_data,
       RIO3_data, WIO0_data, WIO1_data, WIO2_data, WIO3_data, xnor_1_out;

  Counter counter_1 (
    .clr(resetear), .load(1'b1), .clk(tictac), .D(multiplexer_3_out), .Q(PC_output));  // open: up, count, carry
  and and_1 (and_1_out, ins_SRZ, RA_zero);
  or or_1 (or_1_out, and_1_out, and_2_out);
  and and_2 (and_2_out, ins_SER6, RA_eqR6);
  Priority_Encoder #(.select(2)) priority_encoder_1 (
    .in0(1'b1), .in1(ins_JUMPR), .in2(or_1_out), .out(priority_encoder_1_out));  // open: in3, gs, en_out, en_in
  D_Flip_Flop d_ff_1 (.D(fetch_decode), .clk(tictac), .Q(exe), .Qn(fetch_decode), .reset(resetear));  // open: preset
  Multiplexer #(.width(8)) multiplexer_1 (.in0({8{1'b0}}), .in1(multiplexer_2_out), .out(multiplexer_1_out), .sel(exe));
  Multiplexer #(.select(2), .width(8)) multiplexer_2 (
    .in0(8'h1), .in1(RA), .in2(8'h2), .out(multiplexer_2_out), .sel(priority_encoder_1_out));  // open: in3
  Adder adder_1 (.a(PC_output), .b(multiplexer_1_out), .out(adder_1_out));  // open: cin, cout
  Multiplexer #(.width(8)) multiplexer_3 (
    .in0(adder_1_out), .in1(multiplexer_4_out), .out(multiplexer_3_out), .sel(ins_SUBROUTINE));
  Multiplexer #(.width(8)) multiplexer_4 (.in0(RA), .in1(RAM_out), .out(multiplexer_4_out), .sel(ins_RET));
  Multiplexer #(.width(8)) multiplexer_5 (.in0(RB), .in1({8{1'b1}}), .out(multiplexer_5_out), .sel(ins_SUBROUTINE));
  and and_3 (and_3_out, exe, or_2_out);
  or or_2 (or_2_out, ins_READ, ins_WRITE, ins_CALL, ins_RET);
  Multiplexer #(.width(8)) multiplexer_6 (
    .in0(PC_output), .in1(multiplexer_5_out), .out(multiplexer_6_out), .sel(and_3_out));
  Adder adder_2 (.a(PC_output), .b(8'h1), .out(adder_2_out));  // open: cin, cout
  or or_3 (or_3_out, ins_CALL, ins_RET);
  RAM #(.asyncread("true"), .\type ("nonvolatile")) ram_1 (
    .addr(multiplexer_6_out), .we(WE_RAM), .clk(tictac), .din(multiplexer_7_out), .dout(RAM_out));  // open: oe
  // Probe on multiplexer_7_out
  // Probe on multiplexer_7_out
  // Probe on multiplexer_7_out
  Multiplexer #(.width(8)) multiplexer_7 (.in0(RA), .in1(adder_2_out), .out(multiplexer_7_out), .sel(ins_SUBROUTINE));
  and and_4 (ins_SUBROUTINE, or_3_out, exe);
  or or_4 (or_4_out, ins_WRITE, ins_CALL);
  and and_5 (WE_RAM, or_4_out, exe);
  Register IR (
    .D(RAM_out), .en(fetch_decode), .clk(tictac),
    .Q({ope[1], dirB[1:0], dirA[1:0], dirB[2], dirA[2], ope[0]}), .clr(resetear));
  and and_6 (ins_JUMPR, ope[0], ope[1], dirB[0], dirB[1], ~dirB[2]);  // AND_Gate
  and and_7 (ins_SRZ, ope[0], ope[1], dirB[0], dirB[1], dirB[2]);
  and and_8 (ins_SER6, ope[0], ope[1], ~dirB[0], dirB[1], dirB[2]);  // AND_Gate
  and and_9 (ins_WIO0, ope[0], ope[1], dirB[0], ~dirB[1], ~dirB[2], ~dirA[0], ~dirA[1], dirA[2]);  // AND_Gate
  Button button_1 ();  // open: out
  Clock clock_1 (.out(tictac));
  and and_10 (and_10_out, exe, nor_1_out);
  Button button_2 (.out(resetear));
  nor nor_1 (nor_1_out, ins_RET, ins_CALL, ins_WIO_global, ins_WRITE, ins_JUMPR, ins_SRZ, ins_SER6);
  and and_11 (ins_WIO1, ope[0], ope[1], dirB[0], ~dirB[1], ~dirB[2], dirA[0], ~dirA[1], dirA[2]);  // AND_Gate
  registers_8R registers_8r_1 (
    .dir_RA(dirA), .dir_RB(dirB), .enable(and_10_out), .dir_W(dirA), .reset(resetear), .clock(tictac),
    .dato_W(multiplexer_8_out), .RA(RA), .RB(RB));
  // Probe on multiplexer_8_out
  // Probe on multiplexer_8_out
  // Probe on multiplexer_8_out
  and and_12 (ins_READ, ~ope[0], ~ope[1], dirB[2]);  // AND_Gate
  and and_13 (ins_WRITE, ~ope[0], ~ope[1], ~dirB[2]);  // AND_Gate
  Multiplexer #(.select(2), .width(8)) multiplexer_8 (
    .in0(RAM_out), .in1(adder_3_out), .in2({{5{1'b0}}, dirB}), .in3(multiplexer_9_out),
    .out(multiplexer_8_out), .sel(ope));
  and and_14 (ins_WIO2, ope[0], ope[1], dirB[0], ~dirB[1], ~dirB[2], ~dirA[0], dirA[1], dirA[2]);  // AND_Gate
  Adder adder_3 (.a(RA), .b(RB), .out(adder_3_out));  // open: cin, cout
  nor nor_2 (RA_zero, RA[0], RA[1], RA[2], RA[3], RA[4], RA[5], RA[6], RA[7]);
  and and_15 (ins_WIO3, ope[0], ope[1], dirB[0], ~dirB[1], ~dirB[2], dirA[0], dirA[1], dirA[2]);  // AND_Gate
  assign not_1_out = ~RA;  // NOT_Gate not_1, 8 bits wide
  Multiplexer #(.select(3), .width(8)) multiplexer_9 (
    .in0(not_1_out), .in1(multiplexer_10_out), .in4({RA[6:0], 1'b0}), .in5({1'b0, RA[7:1]}),
    .out(multiplexer_9_out), .sel(dirB));  // open: in2, in3, in6, in7
  assign xnor_1_out = ~(RA ^ RB);  // XNOR_Gate xnor_1, 8 bits wide
  and and_16 (ins_CALL, ope[0], ope[1], ~dirB[0], dirB[1], ~dirB[2]);  // AND_Gate
  and and_17 (ins_RET, ope[0], ope[1], dirB[0], ~dirB[1], ~dirB[2], ~dirA[0], ~dirA[1], ~dirA[2]);  // AND_Gate
  Multiplexer #(.select(2), .width(8)) multiplexer_10 (
    .in1(RIO1_data), .in2(RIO2_data), .in3(RIO3_data), .out(multiplexer_10_out), .sel(dirA[1:0]));  // open: in0
  and and_18 (RA_eqR6, xnor_1_out[0], xnor_1_out[1], xnor_1_out[2], xnor_1_out[3], xnor_1_out[4], xnor_1_out[5], xnor_1_out[6], xnor_1_out[7]);
  or or_5 (ins_WIO_global, ins_WIO3, ins_WIO2, ins_WIO1, ins_WIO0);
  Register WIO_0 (.D(RA), .en(ins_WIO0), .clk(tictac), .Q(WIO0_data), .clr(resetear));
  Register WIO_1 (.D(RA), .en(ins_WIO1), .clk(tictac), .Q(WIO1_data), .clr(resetear));
  Register WIO_2 (.D(RA), .en(ins_WIO2), .clk(tictac), .Q(WIO2_data), .clr(resetear));
  Register WIO_3 (.D(RA), .en(ins_WIO3), .clk(tictac), .Q(WIO3_data), .clr(resetear));
  DipSwitch dipswitch_1 (
    .sw1(RIO1_data[7]), .sw2(RIO1_data[6]), .sw3(RIO1_data[5]), .sw4(RIO1_data[4]), .sw5(RIO1_data[3]),
    .sw6(RIO1_data[2]), .sw7(RIO1_data[1]), .sw8(RIO1_data[0]));
  DipSwitch dipswitch_2 (
    .sw1(RIO2_data[7]), .sw2(RIO2_data[6]), .sw3(RIO2_data[5]), .sw4(RIO2_data[4]), .sw5(RIO2_data[3]),
    .sw6(RIO2_data[2]), .sw7(RIO2_data[1]), .sw8(RIO2_data[0]));
  DipSwitch dipswitch_3 (
    .sw1(RIO3_data[7]), .sw2(RIO3_data[6]), .sw3(RIO3_data[5]), .sw4(RIO3_data[4]), .sw5(RIO3_data[3]),
    .sw6(RIO3_data[2]), .sw7(RIO3_data[1]), .sw8(RIO3_data[0]));
  // LedBar #(.inputtype("row")) ledbar_1: pin names not known; wires that end beside it: WIO1_data
  // LedBar #(.inputtype("row")) ledbar_2: pin names not known; wires that end beside it: WIO2_data
  // LedBar #(.inputtype("row")) ledbar_3: pin names not known; wires that end beside it: WIO3_data

  // Other names for the same wires on the sheet: inm[2:0] = dirB; sel1arg[2:0] = dirB; RW_sel = dirB[2];
  //   step[7:0] = RA; RB_ptr[7:0] = RB; sel0arg[2:0] = dirA

  // Notes on the sheet:
  //   Zona de detección de instrucciones
  //   WRITE
  //   READ
  //   SUM
  //   LOAD
  //   NOT
  //   RIOn
  //   RET
  //   CALL
  //   JUMPR
  //   LSL
  //   Zona de periféricos
  //   LSR
  //   SER6
  //   SRZ
endmodule

module Compu_5_3 (
);

  wire and_1_out, and_2_out, and_3_out, and_10_out, exe, fetch_decode, ins_CALL, ins_JUMPR, ins_READ,
       ins_RET, ins_SER6, ins_SRZ, ins_SUBROUTINE, ins_WIO0, ins_WIO1, ins_WIO2, ins_WIO3, ins_WIO_global,
       ins_WRITE, nor_1_out, or_1_out, or_2_out, or_3_out, or_4_out, RA_eqR6, RA_zero, resetear, tictac,
       WE_RAM;
  wire [0:0] RIO3_data;
  wire [1:0] ope, priority_encoder_1_out;
  wire [2:0] dirA, dirB;
  wire [6:0] RIO2_data;
  wire [7:0] adder_1_out, adder_2_out, adder_3_out, multiplexer_1_out, multiplexer_2_out, multiplexer_3_out,
       multiplexer_4_out, multiplexer_5_out, multiplexer_6_out, multiplexer_7_out, multiplexer_8_out,
       multiplexer_9_out, multiplexer_10_out, not_1_out, PC_output, RA, RAM_out, RB, RIO1_data, WIO0_data,
       WIO1_data, WIO2_data, WIO3_data, xnor_1_out;

  Counter counter_1 (
    .clr(resetear), .load(1'b1), .clk(tictac), .D(multiplexer_3_out), .Q(PC_output));  // open: up, count, carry
  and and_1 (and_1_out, ins_SRZ, RA_zero);
  or or_1 (or_1_out, and_1_out, and_2_out);
  and and_2 (and_2_out, ins_SER6, RA_eqR6);
  Priority_Encoder #(.select(2)) priority_encoder_1 (
    .in0(1'b1), .in1(ins_JUMPR), .in2(or_1_out), .out(priority_encoder_1_out));  // open: in3, gs, en_out, en_in
  D_Flip_Flop d_ff_1 (.D(fetch_decode), .clk(tictac), .Q(exe), .Qn(fetch_decode), .reset(resetear));  // open: preset
  Multiplexer #(.width(8)) multiplexer_1 (.in0({8{1'b0}}), .in1(multiplexer_2_out), .out(multiplexer_1_out), .sel(exe));
  Multiplexer #(.select(2), .width(8)) multiplexer_2 (
    .in0(8'h1), .in1(RA), .in2(8'h2), .out(multiplexer_2_out), .sel(priority_encoder_1_out));  // open: in3
  Adder adder_1 (.a(PC_output), .b(multiplexer_1_out), .out(adder_1_out));  // open: cin, cout
  Multiplexer #(.width(8)) multiplexer_3 (
    .in0(adder_1_out), .in1(multiplexer_4_out), .out(multiplexer_3_out), .sel(ins_SUBROUTINE));
  Multiplexer #(.width(8)) multiplexer_4 (.in0(RA), .in1(RAM_out), .out(multiplexer_4_out), .sel(ins_RET));
  Multiplexer #(.width(8)) multiplexer_5 (.in0(RB), .in1({8{1'b1}}), .out(multiplexer_5_out), .sel(ins_SUBROUTINE));
  and and_3 (and_3_out, exe, or_2_out);
  or or_2 (or_2_out, ins_READ, ins_WRITE, ins_CALL, ins_RET);
  Multiplexer #(.width(8)) multiplexer_6 (
    .in0(PC_output), .in1(multiplexer_5_out), .out(multiplexer_6_out), .sel(and_3_out));
  Adder adder_2 (.a(PC_output), .b(8'h1), .out(adder_2_out));  // open: cin, cout
  or or_3 (or_3_out, ins_CALL, ins_RET);
  RAM #(.asyncread("true"), .\type ("nonvolatile")) ram_1 (
    .addr(multiplexer_6_out), .we(WE_RAM), .clk(tictac), .din(multiplexer_7_out), .dout(RAM_out));  // open: oe
  // Probe on multiplexer_7_out
  // Probe on multiplexer_7_out
  // Probe on multiplexer_7_out
  Multiplexer #(.width(8)) multiplexer_7 (.in0(RA), .in1(adder_2_out), .out(multiplexer_7_out), .sel(ins_SUBROUTINE));
  and and_4 (ins_SUBROUTINE, or_3_out, exe);
  or or_4 (or_4_out, ins_WRITE, ins_CALL);
  and and_5 (WE_RAM, or_4_out, exe);
  Register IR (
    .D(RAM_out), .en(fetch_decode), .clk(tictac),
    .Q({ope[1], dirB[1:0], dirA[1:0], dirB[2], dirA[2], ope[0]}), .clr(resetear));
  and and_6 (ins_JUMPR, ope[0], ope[1], dirB[0], dirB[1], ~dirB[2]);  // AND_Gate
  and and_7 (ins_SRZ, ope[0], ope[1], dirB[0], dirB[1], dirB[2]);
  and and_8 (ins_SER6, ope[0], ope[1], ~dirB[0], dirB[1], dirB[2]);  // AND_Gate
  and and_9 (ins_WIO0, ope[0], ope[1], dirB[0], ~dirB[1], ~dirB[2], ~dirA[0], ~dirA[1], dirA[2]);  // AND_Gate
  Button button_1 ();  // open: out
  Clock clock_1 (.out(tictac));
  and and_10 (and_10_out, exe, nor_1_out);
  nor nor_1 (nor_1_out, ins_RET, ins_CALL, ins_WIO_global, ins_WRITE, ins_JUMPR, ins_SRZ, ins_SER6);
  and and_11 (ins_WIO1, ope[0], ope[1], dirB[0], ~dirB[1], ~dirB[2], dirA[0], ~dirA[1], dirA[2]);  // AND_Gate
  registers_8R registers_8r_1 (
    .dir_RA(dirA), .dir_RB(dirB), .enable(and_10_out), .dir_W(dirA), .reset(resetear), .clock(tictac),
    .dato_W(multiplexer_8_out), .RA(RA), .RB(RB));
  // Probe on multiplexer_8_out
  // Probe on multiplexer_8_out
  // Probe on multiplexer_8_out
  and and_12 (ins_READ, ~ope[0], ~ope[1], dirB[2]);  // AND_Gate
  and and_13 (ins_WRITE, ~ope[0], ~ope[1], ~dirB[2]);  // AND_Gate
  Multiplexer #(.select(2), .width(8)) multiplexer_8 (
    .in0(RAM_out), .in1(adder_3_out), .in2({{5{1'b0}}, dirB}), .in3(multiplexer_9_out),
    .out(multiplexer_8_out), .sel(ope));
  and and_14 (ins_WIO2, ope[0], ope[1], dirB[0], ~dirB[1], ~dirB[2], ~dirA[0], dirA[1], dirA[2]);  // AND_Gate
  Adder adder_3 (.a(RA), .b(RB), .out(adder_3_out));  // open: cin, cout
  nor nor_2 (RA_zero, RA[0], RA[1], RA[2], RA[3], RA[4], RA[5], RA[6], RA[7]);
  and and_15 (ins_WIO3, ope[0], ope[1], dirB[0], ~dirB[1], ~dirB[2], dirA[0], dirA[1], dirA[2]);  // AND_Gate
  assign not_1_out = ~RA;  // NOT_Gate not_1, 8 bits wide
  Multiplexer #(.select(3), .width(8)) multiplexer_9 (
    .in0(not_1_out), .in1(multiplexer_10_out), .in4({RA[6:0], 1'b0}), .in5({1'b0, RA[7:1]}),
    .out(multiplexer_9_out), .sel(dirB));  // open: in2, in3, in6, in7
  assign xnor_1_out = ~(RA ^ RB);  // XNOR_Gate xnor_1, 8 bits wide
  and and_16 (ins_CALL, ope[0], ope[1], ~dirB[0], dirB[1], ~dirB[2]);  // AND_Gate
  and and_17 (ins_RET, ope[0], ope[1], dirB[0], ~dirB[1], ~dirB[2], ~dirA[0], ~dirA[1], ~dirA[2]);  // AND_Gate
  Multiplexer #(.select(2), .width(8)) multiplexer_10 (
    .in1(RIO1_data), .in2({1'b0, RIO2_data}), .in3({{7{1'b0}}, RIO3_data[0]}), .out(multiplexer_10_out),
    .sel(dirA[1:0]));  // open: in0
  and and_18 (RA_eqR6, xnor_1_out[0], xnor_1_out[1], xnor_1_out[2], xnor_1_out[3], xnor_1_out[4], xnor_1_out[5], xnor_1_out[6], xnor_1_out[7]);
  or or_5 (ins_WIO_global, ins_WIO3, ins_WIO2, ins_WIO1, ins_WIO0);
  Register WIO_0 (.D(RA), .en(ins_WIO0), .clk(tictac), .Q(WIO0_data), .clr(resetear));
  Register WIO_1 (.D(RA), .en(ins_WIO1), .clk(tictac), .Q(WIO1_data), .clr(resetear));
  Register WIO_2 (.D(RA), .en(ins_WIO2), .clk(tictac), .Q(WIO2_data), .clr(resetear));
  Register WIO_3 (.D(RA), .en(ins_WIO3), .clk(tictac), .Q(WIO3_data), .clr(resetear));
  DipSwitch dipswitch_1 (
    .sw1(RIO1_data[7]), .sw2(RIO1_data[6]), .sw3(RIO1_data[5]), .sw4(RIO1_data[4]), .sw5(RIO1_data[3]),
    .sw6(RIO1_data[2]), .sw7(RIO1_data[1]), .sw8(RIO1_data[0]));
  Button button_2 (.out(resetear));
  Keyboard #(.buflen(128)) keyboard_1 (
    .clk(WIO0_data[1]), .re(WIO0_data[0]), .clr(resetear), .avail(RIO3_data[0]), .data(RIO2_data));

  // Other names for the same wires on the sheet: inm[2:0] = dirB; sel1arg[2:0] = dirB; RW_sel = dirB[2];
  //   step[7:0] = RA; RB_ptr[7:0] = RB; sel0arg[2:0] = dirA

  // Notes on the sheet:
  //   Zona de detección de instrucciones
  //   WRITE
  //   READ
  //   SUM
  //   LOAD
  //   NOT
  //   RIOn
  //   RET
  //   CALL
  //   JUMPR
  //   LSL
  //   Zona de periféricos
  //   LSR
  //   SER6
  //   SRZ
endmodule

module compu_video (
);

  wire and_1_out, and_2_out, and_3_out, and_10_out, exe, fetch_decode, ins_CALL, ins_JUMPR, ins_READ,
       ins_RET, ins_SER6, ins_SRZ, ins_SUBROUTINE, ins_WIO0, ins_WIO1, ins_WIO2, ins_WIO3, ins_WIO_global,
       ins_WRITE, nor_1_out, or_1_out, or_2_out, or_3_out, or_4_out, RA_eqR6, RA_zero, resetear, tictac,
       WE_RAM;
  wire [1:0] ope, priority_encoder_1_out;
  wire [2:0] dirA, dirB;
  wire [7:0] adder_1_out, adder_2_out, adder_3_out, multiplexer_1_out, multiplexer_2_out, multiplexer_3_out,
       multiplexer_4_out, multiplexer_5_out, multiplexer_6_out, multiplexer_7_out, multiplexer_8_out,
       multiplexer_9_out, multiplexer_10_out, not_1_out, PC_output, RA, RAM_out, RB, RIO1_data, RIO2_data,
       RIO3_data, WIO0_data, WIO1_data, WIO2_data, WIO3_data, xnor_1_out;

  Counter counter_1 (
    .clr(resetear), .load(1'b1), .clk(tictac), .D(multiplexer_3_out), .Q(PC_output));  // open: up, count, carry
  and and_1 (and_1_out, ins_SRZ, RA_zero);
  or or_1 (or_1_out, and_1_out, and_2_out);
  and and_2 (and_2_out, ins_SER6, RA_eqR6);
  Priority_Encoder #(.select(2)) priority_encoder_1 (
    .in0(1'b1), .in1(ins_JUMPR), .in2(or_1_out), .out(priority_encoder_1_out));  // open: in3, gs, en_out, en_in
  D_Flip_Flop d_ff_1 (.D(fetch_decode), .clk(tictac), .Q(exe), .Qn(fetch_decode), .reset(resetear));  // open: preset
  Multiplexer #(.width(8)) multiplexer_1 (.in0({8{1'b0}}), .in1(multiplexer_2_out), .out(multiplexer_1_out), .sel(exe));
  Multiplexer #(.select(2), .width(8)) multiplexer_2 (
    .in0(8'h1), .in1(RA), .in2(8'h2), .out(multiplexer_2_out), .sel(priority_encoder_1_out));  // open: in3
  Adder adder_1 (.a(PC_output), .b(multiplexer_1_out), .out(adder_1_out));  // open: cin, cout
  Multiplexer #(.width(8)) multiplexer_3 (
    .in0(adder_1_out), .in1(multiplexer_4_out), .out(multiplexer_3_out), .sel(ins_SUBROUTINE));
  Multiplexer #(.width(8)) multiplexer_4 (.in0(RA), .in1(RAM_out), .out(multiplexer_4_out), .sel(ins_RET));
  Multiplexer #(.width(8)) multiplexer_5 (.in0(RB), .in1({8{1'b1}}), .out(multiplexer_5_out), .sel(ins_SUBROUTINE));
  and and_3 (and_3_out, exe, or_2_out);
  or or_2 (or_2_out, ins_READ, ins_WRITE, ins_CALL, ins_RET);
  Multiplexer #(.width(8)) multiplexer_6 (
    .in0(PC_output), .in1(multiplexer_5_out), .out(multiplexer_6_out), .sel(and_3_out));
  Adder adder_2 (.a(PC_output), .b(8'h1), .out(adder_2_out));  // open: cin, cout
  or or_3 (or_3_out, ins_CALL, ins_RET);
  RAM #(.asyncread("true"), .\type ("nonvolatile")) ram_1 (
    .addr(multiplexer_6_out), .we(WE_RAM), .clk(tictac), .din(multiplexer_7_out), .dout(RAM_out));  // open: oe
  // Probe on multiplexer_7_out
  // Probe on multiplexer_7_out
  // Probe on multiplexer_7_out
  Multiplexer #(.width(8)) multiplexer_7 (.in0(RA), .in1(adder_2_out), .out(multiplexer_7_out), .sel(ins_SUBROUTINE));
  and and_4 (ins_SUBROUTINE, or_3_out, exe);
  or or_4 (or_4_out, ins_WRITE, ins_CALL);
  and and_5 (WE_RAM, or_4_out, exe);
  Register IR (
    .D(RAM_out), .en(fetch_decode), .clk(tictac),
    .Q({ope[1], dirB[1:0], dirA[1:0], dirB[2], dirA[2], ope[0]}), .clr(resetear));
  and and_6 (ins_JUMPR, ope[0], ope[1], dirB[0], dirB[1], ~dirB[2]);  // AND_Gate
  and and_7 (ins_SRZ, ope[0], ope[1], dirB[0], dirB[1], dirB[2]);
  and and_8 (ins_SER6, ope[0], ope[1], ~dirB[0], dirB[1], dirB[2]);  // AND_Gate
  and and_9 (ins_WIO0, ope[0], ope[1], dirB[0], ~dirB[1], ~dirB[2], ~dirA[0], ~dirA[1], dirA[2]);  // AND_Gate
  Button button_1 ();  // open: out
  Clock clock_1 (.out(tictac));
  and and_10 (and_10_out, exe, nor_1_out);
  Button button_2 (.out(resetear));
  nor nor_1 (nor_1_out, ins_RET, ins_CALL, ins_WIO_global, ins_WRITE, ins_JUMPR, ins_SRZ, ins_SER6);
  and and_11 (ins_WIO1, ope[0], ope[1], dirB[0], ~dirB[1], ~dirB[2], dirA[0], ~dirA[1], dirA[2]);  // AND_Gate
  registers_8R registers_8r_1 (
    .dir_RA(dirA), .dir_RB(dirB), .enable(and_10_out), .dir_W(dirA), .reset(resetear), .clock(tictac),
    .dato_W(multiplexer_8_out), .RA(RA), .RB(RB));
  // Probe on multiplexer_8_out
  // Probe on multiplexer_8_out
  // Probe on multiplexer_8_out
  and and_12 (ins_READ, ~ope[0], ~ope[1], dirB[2]);  // AND_Gate
  and and_13 (ins_WRITE, ~ope[0], ~ope[1], ~dirB[2]);  // AND_Gate
  Multiplexer #(.select(2), .width(8)) multiplexer_8 (
    .in0(RAM_out), .in1(adder_3_out), .in2({{5{1'b0}}, dirB}), .in3(multiplexer_9_out),
    .out(multiplexer_8_out), .sel(ope));
  and and_14 (ins_WIO2, ope[0], ope[1], dirB[0], ~dirB[1], ~dirB[2], ~dirA[0], dirA[1], dirA[2]);  // AND_Gate
  Adder adder_3 (.a(RA), .b(RB), .out(adder_3_out));  // open: cin, cout
  nor nor_2 (RA_zero, RA[0], RA[1], RA[2], RA[3], RA[4], RA[5], RA[6], RA[7]);
  and and_15 (ins_WIO3, ope[0], ope[1], dirB[0], ~dirB[1], ~dirB[2], dirA[0], dirA[1], dirA[2]);  // AND_Gate
  assign not_1_out = ~RA;  // NOT_Gate not_1, 8 bits wide
  Multiplexer #(.select(3), .width(8)) multiplexer_9 (
    .in0(not_1_out), .in1(multiplexer_10_out), .in4({RA[6:0], 1'b0}), .in5({1'b0, RA[7:1]}),
    .out(multiplexer_9_out), .sel(dirB));  // open: in2, in3, in6, in7
  assign xnor_1_out = ~(RA ^ RB);  // XNOR_Gate xnor_1, 8 bits wide
  and and_16 (ins_CALL, ope[0], ope[1], ~dirB[0], dirB[1], ~dirB[2]);  // AND_Gate
  and and_17 (ins_RET, ope[0], ope[1], dirB[0], ~dirB[1], ~dirB[2], ~dirA[0], ~dirA[1], ~dirA[2]);  // AND_Gate
  Multiplexer #(.select(2), .width(8)) multiplexer_10 (
    .in1(RIO1_data), .in2(RIO2_data), .in3(RIO3_data), .out(multiplexer_10_out), .sel(dirA[1:0]));  // open: in0
  and and_18 (RA_eqR6, xnor_1_out[0], xnor_1_out[1], xnor_1_out[2], xnor_1_out[3], xnor_1_out[4], xnor_1_out[5], xnor_1_out[6], xnor_1_out[7]);
  or or_5 (ins_WIO_global, ins_WIO3, ins_WIO2, ins_WIO1, ins_WIO0);
  Register WIO_0 (.D(RA), .en(ins_WIO0), .clk(tictac), .Q(WIO0_data), .clr(resetear));
  Register WIO_1 (.D(RA), .en(ins_WIO1), .clk(tictac), .Q(WIO1_data), .clr(resetear));
  Register WIO_2 (.D(RA), .en(ins_WIO2), .clk(tictac), .Q(WIO2_data), .clr(resetear));
  Register WIO_3 (.D(RA), .en(ins_WIO3), .clk(tictac), .Q(WIO3_data), .clr(resetear));
  // RGB_Video rgb_video_1: pin names not known; wires that end beside it: resetear, tictac, WIO0_data[0], WIO2_data[6:0], WIO1_data[6:0], WIO3_data

  // Other names for the same wires on the sheet: inm[2:0] = dirB; sel1arg[2:0] = dirB; RW_sel = dirB[2];
  //   step[7:0] = RA; RB_ptr[7:0] = RB; sel0arg[2:0] = dirA

  // Notes on the sheet:
  //   Zona de detección de instrucciones
  //   WRITE
  //   READ
  //   SUM
  //   LOAD
  //   NOT
  //   RIOn
  //   RET
  //   CALL
  //   JUMPR
  //   LSL
  //   Zona de periféricos
  //   LSR
  //   SER6
  //   SRZ
endmodule

module Compu_teclado_tty (
);

  wire and_1_out, and_2_out, and_3_out, and_10_out, exe, fetch_decode, ins_CALL, ins_JUMPR, ins_READ,
       ins_RET, ins_SER6, ins_SRZ, ins_SUBROUTINE, ins_WIO0, ins_WIO1, ins_WIO2, ins_WIO3, ins_WIO_global,
       ins_WRITE, nor_1_out, or_1_out, or_2_out, or_3_out, or_4_out, RA_eqR6, RA_zero, resetear, tictac,
       WE_RAM;
  wire [0:0] RIO2_data;
  wire [1:0] ope, priority_encoder_1_out;
  wire [2:0] dirA, dirB;
  wire [6:0] RIO3_data;
  wire [7:0] adder_1_out, adder_2_out, adder_3_out, multiplexer_1_out, multiplexer_2_out, multiplexer_3_out,
       multiplexer_4_out, multiplexer_5_out, multiplexer_6_out, multiplexer_7_out, multiplexer_8_out,
       multiplexer_9_out, multiplexer_10_out, not_1_out, PC_output, RA, RAM_out, RB, RIO1_data, WIO0_data,
       WIO1_data, WIO2_data, WIO3_data, xnor_1_out;

  Counter counter_1 (
    .clr(resetear), .load(1'b1), .clk(tictac), .D(multiplexer_3_out), .Q(PC_output));  // open: up, count, carry
  and and_1 (and_1_out, ins_SRZ, RA_zero);
  or or_1 (or_1_out, and_1_out, and_2_out);
  and and_2 (and_2_out, ins_SER6, RA_eqR6);
  Priority_Encoder #(.select(2)) priority_encoder_1 (
    .in0(1'b1), .in1(ins_JUMPR), .in2(or_1_out), .out(priority_encoder_1_out));  // open: in3, gs, en_out, en_in
  D_Flip_Flop d_ff_1 (.D(fetch_decode), .clk(tictac), .Q(exe), .Qn(fetch_decode), .reset(resetear));  // open: preset
  Multiplexer #(.width(8)) multiplexer_1 (.in0({8{1'b0}}), .in1(multiplexer_2_out), .out(multiplexer_1_out), .sel(exe));
  Multiplexer #(.select(2), .width(8)) multiplexer_2 (
    .in0(8'h1), .in1(RA), .in2(8'h2), .out(multiplexer_2_out), .sel(priority_encoder_1_out));  // open: in3
  Adder adder_1 (.a(PC_output), .b(multiplexer_1_out), .out(adder_1_out));  // open: cin, cout
  Multiplexer #(.width(8)) multiplexer_3 (
    .in0(adder_1_out), .in1(multiplexer_4_out), .out(multiplexer_3_out), .sel(ins_SUBROUTINE));
  Multiplexer #(.width(8)) multiplexer_4 (.in0(RA), .in1(RAM_out), .out(multiplexer_4_out), .sel(ins_RET));
  Multiplexer #(.width(8)) multiplexer_5 (.in0(RB), .in1({8{1'b1}}), .out(multiplexer_5_out), .sel(ins_SUBROUTINE));
  and and_3 (and_3_out, exe, or_2_out);
  or or_2 (or_2_out, ins_READ, ins_WRITE, ins_CALL, ins_RET);
  Multiplexer #(.width(8)) multiplexer_6 (
    .in0(PC_output), .in1(multiplexer_5_out), .out(multiplexer_6_out), .sel(and_3_out));
  Adder adder_2 (.a(PC_output), .b(8'h1), .out(adder_2_out));  // open: cin, cout
  or or_3 (or_3_out, ins_CALL, ins_RET);
  RAM #(.asyncread("true"), .\type ("nonvolatile")) ram_1 (
    .addr(multiplexer_6_out), .we(WE_RAM), .clk(tictac), .din(multiplexer_7_out), .dout(RAM_out));  // open: oe
  // Probe on multiplexer_7_out
  // Probe on multiplexer_7_out
  // Probe on multiplexer_7_out
  Multiplexer #(.width(8)) multiplexer_7 (.in0(RA), .in1(adder_2_out), .out(multiplexer_7_out), .sel(ins_SUBROUTINE));
  and and_4 (ins_SUBROUTINE, or_3_out, exe);
  or or_4 (or_4_out, ins_WRITE, ins_CALL);
  and and_5 (WE_RAM, or_4_out, exe);
  Register IR (
    .D(RAM_out), .en(fetch_decode), .clk(tictac),
    .Q({ope[1], dirB[1:0], dirA[1:0], dirB[2], dirA[2], ope[0]}), .clr(resetear));
  and and_6 (ins_JUMPR, ope[0], ope[1], dirB[0], dirB[1], ~dirB[2]);  // AND_Gate
  and and_7 (ins_SRZ, ope[0], ope[1], dirB[0], dirB[1], dirB[2]);
  and and_8 (ins_SER6, ope[0], ope[1], ~dirB[0], dirB[1], dirB[2]);  // AND_Gate
  and and_9 (ins_WIO0, ope[0], ope[1], dirB[0], ~dirB[1], ~dirB[2], ~dirA[0], ~dirA[1], dirA[2]);  // AND_Gate
  Button button_1 ();  // open: out
  Clock clock_1 (.out(tictac));
  and and_10 (and_10_out, exe, nor_1_out);
  Button button_2 (.out(resetear));
  nor nor_1 (nor_1_out, ins_RET, ins_CALL, ins_WIO_global, ins_WRITE, ins_JUMPR, ins_SRZ, ins_SER6);
  and and_11 (ins_WIO1, ope[0], ope[1], dirB[0], ~dirB[1], ~dirB[2], dirA[0], ~dirA[1], dirA[2]);  // AND_Gate
  registers_8R registers_8r_1 (
    .dir_RA(dirA), .dir_RB(dirB), .enable(and_10_out), .dir_W(dirA), .reset(resetear), .clock(tictac),
    .dato_W(multiplexer_8_out), .RA(RA), .RB(RB));
  // Probe on multiplexer_8_out
  // Probe on multiplexer_8_out
  // Probe on multiplexer_8_out
  and and_12 (ins_READ, ~ope[0], ~ope[1], dirB[2]);  // AND_Gate
  and and_13 (ins_WRITE, ~ope[0], ~ope[1], ~dirB[2]);  // AND_Gate
  Multiplexer #(.select(2), .width(8)) multiplexer_8 (
    .in0(RAM_out), .in1(adder_3_out), .in2({{5{1'b0}}, dirB}), .in3(multiplexer_9_out),
    .out(multiplexer_8_out), .sel(ope));
  and and_14 (ins_WIO2, ope[0], ope[1], dirB[0], ~dirB[1], ~dirB[2], ~dirA[0], dirA[1], dirA[2]);  // AND_Gate
  Adder adder_3 (.a(RA), .b(RB), .out(adder_3_out));  // open: cin, cout
  nor nor_2 (RA_zero, RA[0], RA[1], RA[2], RA[3], RA[4], RA[5], RA[6], RA[7]);
  and and_15 (ins_WIO3, ope[0], ope[1], dirB[0], ~dirB[1], ~dirB[2], dirA[0], dirA[1], dirA[2]);  // AND_Gate
  assign not_1_out = ~RA;  // NOT_Gate not_1, 8 bits wide
  Multiplexer #(.select(3), .width(8)) multiplexer_9 (
    .in0(not_1_out), .in1(multiplexer_10_out), .in4({RA[6:0], 1'b0}), .in5({1'b0, RA[7:1]}),
    .out(multiplexer_9_out), .sel(dirB));  // open: in2, in3, in6, in7
  assign xnor_1_out = ~(RA ^ RB);  // XNOR_Gate xnor_1, 8 bits wide
  and and_16 (ins_CALL, ope[0], ope[1], ~dirB[0], dirB[1], ~dirB[2]);  // AND_Gate
  and and_17 (ins_RET, ope[0], ope[1], dirB[0], ~dirB[1], ~dirB[2], ~dirA[0], ~dirA[1], ~dirA[2]);  // AND_Gate
  Multiplexer #(.select(2), .width(8)) multiplexer_10 (
    .in1(RIO1_data), .in2({{7{1'b0}}, RIO2_data[0]}), .in3({1'b0, RIO3_data}), .out(multiplexer_10_out),
    .sel(dirA[1:0]));  // open: in0
  and and_18 (RA_eqR6, xnor_1_out[0], xnor_1_out[1], xnor_1_out[2], xnor_1_out[3], xnor_1_out[4], xnor_1_out[5], xnor_1_out[6], xnor_1_out[7]);
  or or_5 (ins_WIO_global, ins_WIO3, ins_WIO2, ins_WIO1, ins_WIO0);
  Register WIO_0 (.D(RA), .en(ins_WIO0), .clk(tictac), .Q(WIO0_data), .clr(resetear));
  Register WIO_1 (.D(RA), .en(ins_WIO1), .clk(tictac), .Q(WIO1_data), .clr(resetear));
  Register WIO_2 (.D(RA), .en(ins_WIO2), .clk(tictac), .Q(WIO2_data), .clr(resetear));
  Register WIO_3 (.D(RA), .en(ins_WIO3), .clk(tictac), .Q(WIO3_data), .clr(resetear));
  Keyboard keyboard_1 (.clk(tictac), .re(RIO1_data[0]), .clr(resetear), .avail(RIO2_data[0]), .data(RIO3_data));
  TTY tty_1 (.data(WIO1_data[6:0]), .clk(tictac), .we(WIO0_data[0]), .clr(resetear));

  // Other names for the same wires on the sheet: inm[2:0] = dirB; sel1arg[2:0] = dirB; RW_sel = dirB[2];
  //   step[7:0] = RA; RB_ptr[7:0] = RB; sel0arg[2:0] = dirA

  // Notes on the sheet:
  //   Zona de detección de instrucciones
  //   WRITE
  //   READ
  //   SUM
  //   LOAD
  //   NOT
  //   RIOn
  //   RET
  //   CALL
  //   JUMPR
  //   LSL
  //   Zona de periféricos
  //   LSR
  //   SER6
  //   SRZ
endmodule
