// Logisim project Clase2.circ as structural Verilog: 8 circuits, main circuit registers_4R
module registers_2R_1 (
  input  clock,
  input  [7:0] dato_W,
  input  dir_W
);

  wire decoder_1_out0, decoder_1_out1;
  wire [3:0] binary_to_bcd_converter_1_p2, binary_to_bcd_converter_1_p3, binary_to_bcd_converter_1_p4,
       binary_to_bcd_converter_2_p2, binary_to_bcd_converter_2_p3, binary_to_bcd_converter_2_p4, R0_q,
       R0_q_2, R1_q, R1_q_2;

  Decoder decoder_1 (.out0(decoder_1_out0), .out1(decoder_1_out1), .sel(dir_W));  // open: en
  Register R1 (.D(dato_W), .en(decoder_1_out1), .clk(clock), .Q({R1_q_2, R1_q}));  // open: clr
  Register R0 (.D(dato_W), .en(decoder_1_out0), .clk(clock), .Q({R0_q_2, R0_q}));  // open: clr
  Hex_Digit_Display R1H (.value(R1_q_2));  // open: dp
  Hex_Digit_Display R0H (.value(R0_q_2));  // open: dp
  Hex_Digit_Display R1L (.value(R1_q));  // open: dp
  Hex_Digit_Display R0L (.value(R0_q));  // open: dp
  Hex_Digit_Display R1d2 (.value(binary_to_bcd_converter_1_p2));  // open: dp
  // Binary_to_BCD_converter #(.binvalue(8)) binary_to_bcd_converter_1: pin names not known; wires that end beside it: {R1_q_2, R1_q}, binary_to_bcd_converter_1_p2, binary_to_bcd_converter_1_p3, binary_to_bcd_converter_1_p4
  Hex_Digit_Display R0d2 (.value(binary_to_bcd_converter_2_p2));  // open: dp
  // Binary_to_BCD_converter #(.binvalue(8)) binary_to_bcd_converter_2: pin names not known; wires that end beside it: {R0_q_2, R0_q}, binary_to_bcd_converter_2_p2, binary_to_bcd_converter_2_p3, binary_to_bcd_converter_2_p4
  Hex_Digit_Display R1d1 (.value(binary_to_bcd_converter_1_p3));  // open: dp
  Hex_Digit_Display R0d1 (.value(binary_to_bcd_converter_2_p3));  // open: dp
  Hex_Digit_Display R1d0 (.value(binary_to_bcd_converter_1_p4));  // open: dp
  Hex_Digit_Display R0d0 (.value(binary_to_bcd_converter_2_p4));  // open: dp
  LED r17 (.in(R1_q_2[3]));
  LED r16 (.in(R1_q_2[2]));
  LED r07 (.in(R0_q_2[3]));
  LED r06 (.in(R0_q_2[2]));
  LED r15 (.in(R1_q_2[1]));
  LED r14 (.in(R1_q_2[0]));
  LED r13 (.in(R1_q[3]));
  LED r05 (.in(R0_q_2[1]));
  LED r04 (.in(R0_q_2[0]));
  LED r03 (.in(R0_q[3]));
  LED r12 (.in(R1_q[2]));
  LED r11 (.in(R1_q[1]));
  LED r10 (.in(R1_q[0]));
  LED r02 (.in(R0_q[2]));
  LED r01 (.in(R0_q[1]));
  LED r00 (.in(R0_q[0]));
endmodule

module registers_2R_2 (
  input  reset,
  input  clock,
  input  [7:0] dato_W,
  input  enable,
  input  dir_W
);

  wire decoder_1_out0, decoder_1_out1;
  wire [3:0] binary_to_bcd_converter_1_p2, binary_to_bcd_converter_1_p3, binary_to_bcd_converter_1_p4,
       binary_to_bcd_converter_2_p2, binary_to_bcd_converter_2_p3, binary_to_bcd_converter_2_p4, R0_q,
       R0_q_2, R1_q, R1_q_2;

  LED led_1 (.in(enable));
  LED led_2 (.in(enable));
  LED led_3 (.in(enable));
  LED led_4 (.in(enable));
  Decoder decoder_1 (.out0(decoder_1_out0), .out1(decoder_1_out1), .sel(dir_W), .en(enable));
  Register R1 (.D(dato_W), .en(decoder_1_out1), .clk(clock), .Q({R1_q_2, R1_q}), .clr(reset));
  Register R0 (.D(dato_W), .en(decoder_1_out0), .clk(clock), .Q({R0_q_2, R0_q}), .clr(reset));
  Hex_Digit_Display R1H (.value(R1_q_2));  // open: dp
  Hex_Digit_Display R0H (.value(R0_q_2));  // open: dp
  Hex_Digit_Display R1L (.value(R1_q));  // open: dp
  Hex_Digit_Display R0L (.value(R0_q));  // open: dp
  Hex_Digit_Display R1d2 (.value(binary_to_bcd_converter_1_p2));  // open: dp
  // Binary_to_BCD_converter #(.binvalue(8)) binary_to_bcd_converter_1: pin names not known; wires that end beside it: {R1_q_2, R1_q}, binary_to_bcd_converter_1_p2, binary_to_bcd_converter_1_p3, binary_to_bcd_converter_1_p4
  Hex_Digit_Display R0d2 (.value(binary_to_bcd_converter_2_p2));  // open: dp
  // Binary_to_BCD_converter #(.binvalue(8)) binary_to_bcd_converter_2: pin names not known; wires that end beside it: {R0_q_2, R0_q}, binary_to_bcd_converter_2_p2, binary_to_bcd_converter_2_p3, binary_to_bcd_converter_2_p4
  Hex_Digit_Display R1d1 (.value(binary_to_bcd_converter_1_p3));  // open: dp
  Hex_Digit_Display R0d1 (.value(binary_to_bcd_converter_2_p3));  // open: dp
  Hex_Digit_Display R1d0 (.value(binary_to_bcd_converter_1_p4));  // open: dp
  Hex_Digit_Display R0d0 (.value(binary_to_bcd_converter_2_p4));  // open: dp
  LED r17 (.in(R1_q_2[3]));
  LED r16 (.in(R1_q_2[2]));
  LED r07 (.in(R0_q_2[3]));
  LED r06 (.in(R0_q_2[2]));
  LED r15 (.in(R1_q_2[1]));
  LED r14 (.in(R1_q_2[0]));
  LED r13 (.in(R1_q[3]));
  LED r05 (.in(R0_q_2[1]));
  LED r04 (.in(R0_q_2[0]));
  LED r03 (.in(R0_q[3]));
  LED r12 (.in(R1_q[2]));
  LED r11 (.in(R1_q[1]));
  LED r10 (.in(R1_q[0]));
  LED r02 (.in(R0_q[2]));
  LED r01 (.in(R0_q[1]));
  LED r00 (.in(R0_q[0]));
endmodule

module registers_2R_3 (
  input  reset,
  input  clock,
  input  dir_RB,
  input  [7:0] dato_W,
  input  dir_RA,
  input  enable,
  input  dir_W,
  output [7:0] RB,
  output [7:0] RA
);

  wire decoder_1_out0, decoder_1_out1;
  wire [3:0] binary_to_bcd_converter_1_p2, binary_to_bcd_converter_1_p3, binary_to_bcd_converter_1_p4,
       binary_to_bcd_converter_2_p2, binary_to_bcd_converter_2_p3, binary_to_bcd_converter_2_p4, R0_q,
       R0_q_2, R1_q, R1_q_2;

  LED led_1 (.in(enable));
  LED led_2 (.in(enable));
  LED led_3 (.in(enable));
  LED led_4 (.in(enable));
  Decoder decoder_1 (.out0(decoder_1_out0), .out1(decoder_1_out1), .sel(dir_W), .en(enable));
  Register R1 (.D(dato_W), .en(decoder_1_out1), .clk(clock), .Q({R1_q_2, R1_q}), .clr(reset));
  Register R0 (.D(dato_W), .en(decoder_1_out0), .clk(clock), .Q({R0_q_2, R0_q}), .clr(reset));
  Hex_Digit_Display R1H (.value(R1_q_2));  // open: dp
  Hex_Digit_Display R0H (.value(R0_q_2));  // open: dp
  Hex_Digit_Display R1L (.value(R1_q));  // open: dp
  Hex_Digit_Display R0L (.value(R0_q));  // open: dp
  Hex_Digit_Display R1d2 (.value(binary_to_bcd_converter_1_p2));  // open: dp
  // Binary_to_BCD_converter #(.binvalue(8)) binary_to_bcd_converter_1: pin names not known; wires that end beside it: {R1_q_2, R1_q}, binary_to_bcd_converter_1_p2, binary_to_bcd_converter_1_p3, binary_to_bcd_converter_1_p4
  Hex_Digit_Display R0d2 (.value(binary_to_bcd_converter_2_p2));  // open: dp
  // Binary_to_BCD_converter #(.binvalue(8)) binary_to_bcd_converter_2: pin names not known; wires that end beside it: {R0_q_2, R0_q}, binary_to_bcd_converter_2_p2, binary_to_bcd_converter_2_p3, binary_to_bcd_converter_2_p4
  Hex_Digit_Display R1d1 (.value(binary_to_bcd_converter_1_p3));  // open: dp
  Hex_Digit_Display R0d1 (.value(binary_to_bcd_converter_2_p3));  // open: dp
  Hex_Digit_Display R1d0 (.value(binary_to_bcd_converter_1_p4));  // open: dp
  Hex_Digit_Display R0d0 (.value(binary_to_bcd_converter_2_p4));  // open: dp
  LED r17 (.in(R1_q_2[3]));
  LED r16 (.in(R1_q_2[2]));
  LED r07 (.in(R0_q_2[3]));
  LED r06 (.in(R0_q_2[2]));
  LED r15 (.in(R1_q_2[1]));
  LED r14 (.in(R1_q_2[0]));
  LED r13 (.in(R1_q[3]));
  LED r05 (.in(R0_q_2[1]));
  LED r04 (.in(R0_q_2[0]));
  LED r03 (.in(R0_q[3]));
  LED r12 (.in(R1_q[2]));
  LED r11 (.in(R1_q[1]));
  LED r10 (.in(R1_q[0]));
  LED r02 (.in(R0_q[2]));
  LED r01 (.in(R0_q[1]));
  LED r00 (.in(R0_q[0]));
  Multiplexer #(.width(8)) multiplexer_1 (.in0({R0_q_2, R0_q}), .in1({R1_q_2, R1_q}), .out(RA), .sel(dir_RA));
  Multiplexer #(.width(8)) multiplexer_2 (.in0({R0_q_2, R0_q}), .in1({R1_q_2, R1_q}), .out(RB), .sel(dir_RB));
endmodule

module registers_4R (
  input  reset,
  input  clock,
  input  [1:0] dir_RB,
  input  [7:0] dato_W,
  input  [1:0] dir_RA,
  input  enable,
  input  [1:0] dir_W,
  output [7:0] RB,
  output [7:0] RA
);

  wire decoder_1_out0, decoder_1_out1, decoder_1_out2, decoder_1_out3;
  wire [3:0] binary_to_bcd_converter_1_p2, binary_to_bcd_converter_1_p3, binary_to_bcd_converter_1_p4,
       binary_to_bcd_converter_2_p2, binary_to_bcd_converter_2_p3, binary_to_bcd_converter_2_p4,
       binary_to_bcd_converter_3_p2, binary_to_bcd_converter_3_p3, binary_to_bcd_converter_3_p4,
       binary_to_bcd_converter_4_p2, binary_to_bcd_converter_4_p3, binary_to_bcd_converter_4_p4, R0_q,
       R0_q_2, R1_q, R1_q_2, R2_q, R2_q_2, R3_q, R3_q_2;

  LED led_1 (.in(enable));
  LED led_2 (.in(enable));
  LED led_3 (.in(enable));
  LED led_4 (.in(enable));
  Decoder #(.select(2)) decoder_1 (
    .out0(decoder_1_out0), .out1(decoder_1_out1), .out2(decoder_1_out2), .out3(decoder_1_out3), .sel(dir_W),
    .en(enable));
  Register R3 (.D(dato_W), .en(decoder_1_out3), .clk(clock), .Q({R3_q_2, R3_q}), .clr(reset));
  Register R2 (.D(dato_W), .en(decoder_1_out2), .clk(clock), .Q({R2_q_2, R2_q}), .clr(reset));
  Register R1 (.D(dato_W), .en(decoder_1_out1), .clk(clock), .Q({R1_q_2, R1_q}), .clr(reset));
  Register R0 (.D(dato_W), .en(decoder_1_out0), .clk(clock), .Q({R0_q_2, R0_q}), .clr(reset));
  Hex_Digit_Display R3H (.value(R3_q_2));  // open: dp
  Hex_Digit_Display R2H (.value(R2_q_2));  // open: dp
  Hex_Digit_Display R1H (.value(R1_q_2));  // open: dp
  Hex_Digit_Display R0H (.value(R0_q_2));  // open: dp
  Hex_Digit_Display R3L (.value(R3_q));  // open: dp
  Hex_Digit_Display #(.decimalPoint("false")) R2L (.value(R2_q));
  Hex_Digit_Display R1L (.value(R1_q));  // open: dp
  Hex_Digit_Display R0L (.value(R0_q));  // open: dp
  Hex_Digit_Display R3d2 (.value(binary_to_bcd_converter_1_p2));  // open: dp
  // Binary_to_BCD_converter #(.binvalue(8)) binary_to_bcd_converter_1: pin names not known; wires that end beside it: {R3_q_2, R3_q}, binary_to_bcd_converter_1_p2, binary_to_bcd_converter_1_p3, binary_to_bcd_converter_1_p4
  Hex_Digit_Display R2d2 (.value(binary_to_bcd_converter_2_p2));  // open: dp
  // Binary_to_BCD_converter #(.binvalue(8)) binary_to_bcd_converter_2: pin names not known; wires that end beside it: {R2_q_2, R2_q}, binary_to_bcd_converter_2_p2, binary_to_bcd_converter_2_p3, binary_to_bcd_converter_2_p4
  Hex_Digit_Display R1d2 (.value(binary_to_bcd_converter_3_p2));  // open: dp
  // Binary_to_BCD_converter #(.binvalue(8)) binary_to_bcd_converter_3: pin names not known; wires that end beside it: {R1_q_2, R1_q}, binary_to_bcd_converter_3_p2, binary_to_bcd_converter_3_p3, binary_to_bcd_converter_3_p4
  Hex_Digit_Display R0d2 (.value(binary_to_bcd_converter_4_p2));  // open: dp
  // Binary_to_BCD_converter #(.binvalue(8)) binary_to_bcd_converter_4: pin names not known; wires that end beside it: {R0_q_2, R0_q}, binary_to_bcd_converter_4_p2, binary_to_bcd_converter_4_p3, binary_to_bcd_converter_4_p4
  Hex_Digit_Display R3d1 (.value(binary_to_bcd_converter_1_p3));  // open: dp
  Hex_Digit_Display R2d1 (.value(binary_to_bcd_converter_2_p3));  // open: dp
  Hex_Digit_Display R1d1 (.value(binary_to_bcd_converter_3_p3));  // open: dp
  Hex_Digit_Display R0d1 (.value(binary_to_bcd_converter_4_p3));  // open: dp
  Hex_Digit_Display R3d0 (.value(binary_to_bcd_converter_1_p4));  // open: dp
  Hex_Digit_Display R2d0 (.value(binary_to_bcd_converter_2_p4));  // open: dp
  Hex_Digit_Display R1d0 (.value(binary_to_bcd_converter_3_p4));  // open: dp
  Hex_Digit_Display R0d0 (.value(binary_to_bcd_converter_4_p4));  // open: dp
  LED r37 (.in(R3_q_2[3]));
  LED r36 (.in(R3_q_2[2]));
  LED r27 (.in(R2_q_2[3]));
  LED r26 (.in(R2_q_2[2]));
  LED r17 (.in(R1_q_2[3]));
  LED r16 (.in(R1_q_2[2]));
  LED r07 (.in(R0_q_2[3]));
  LED r06 (.in(R0_q_2[2]));
  LED r35 (.in(R3_q_2[1]));
  LED r34 (.in(R3_q_2[0]));
  LED r33 (.in(R3_q[3]));
  LED r25 (.in(R2_q_2[1]));
  LED r24 (.in(R2_q_2[0]));
  LED r23 (.in(R2_q[3]));
  LED r15 (.in(R1_q_2[1]));
  LED r14 (.in(R1_q_2[0]));
  LED r13 (.in(R1_q[3]));
  LED r05 (.in(R0_q_2[1]));
  LED r04 (.in(R0_q_2[0]));
  LED r03 (.in(R0_q[3]));
  LED r32 (.in(R3_q[2]));
  LED r31 (.in(R3_q[1]));
  LED r30 (.in(R3_q[0]));
  LED r22 (.in(R2_q[2]));
  LED r21 (.in(R2_q[1]));
  LED r20 (.in(R2_q[0]));
  LED r12 (.in(R1_q[2]));
  LED r11 (.in(R1_q[1]));
  LED r10 (.in(R1_q[0]));
  LED r02 (.in(R0_q[2]));
  LED r01 (.in(R0_q[1]));
  LED r00 (.in(R0_q[0]));
  Multiplexer #(.select(2), .width(8)) multiplexer_1 (
    .in0({R0_q_2, R0_q}), .in1({R1_q_2, R1_q}), .in2({R2_q_2, R2_q}), .in3({R3_q_2, R3_q}), .out(RA),
    .sel(dir_RA));
  Multiplexer #(.select(2), .width(8)) multiplexer_2 (
    .in0({R0_q_2, R0_q}), .in1({R1_q_2, R1_q}), .in2({R2_q_2, R2_q}), .in3({R3_q_2, R3_q}), .out(RB),
    .sel(dir_RB));
endmodule

module registers_8R (
  input  reset,
  input  [2:0] dir_RB,
  input  clock,
  input  [7:0] dato_W,
  input  enable,
  input  [2:0] dir_RA,
  input  [2:0] dir_W,
  output [7:0] RB,
  output [7:0] RA
);

  wire decoder_1_out0, decoder_1_out1, decoder_1_out2, decoder_1_out3, decoder_1_out4, decoder_1_out5,
       decoder_1_out6, decoder_1_out7;
  wire [3:0] binary_to_bcd_converter_1_p2, binary_to_bcd_converter_1_p3, binary_to_bcd_converter_1_p4,
       binary_to_bcd_converter_2_p2, binary_to_bcd_converter_2_p3, binary_to_bcd_converter_2_p4,
       binary_to_bcd_converter_3_p2, binary_to_bcd_converter_3_p3, binary_to_bcd_converter_3_p4,
       binary_to_bcd_converter_4_p2, binary_to_bcd_converter_4_p3, binary_to_bcd_converter_4_p4,
       binary_to_bcd_converter_5_p2, binary_to_bcd_converter_5_p3, binary_to_bcd_converter_5_p4,
       binary_to_bcd_converter_6_p2, binary_to_bcd_converter_6_p3, binary_to_bcd_converter_6_p4,
       binary_to_bcd_converter_7_p2, binary_to_bcd_converter_7_p3, binary_to_bcd_converter_7_p4,
       binary_to_bcd_converter_8_p2, binary_to_bcd_converter_8_p3, binary_to_bcd_converter_8_p4, R0_q,
       R0_q_2, R1_q, R1_q_2, R2_q, R2_q_2, R3_q, R3_q_2, register_1_q, register_1_q_2, register_2_q,
       register_2_q_2, register_3_q, register_3_q_2, register_4_q, register_4_q_2;

  LED W_EN_led (.in(enable));
  LED led_1 (.in(enable));
  LED led_2 (.in(enable));
  LED led_3 (.in(enable));
  Decoder #(.select(3)) decoder_1 (
    .out0(decoder_1_out0), .out1(decoder_1_out1), .out2(decoder_1_out2), .out3(decoder_1_out3),
    .out4(decoder_1_out4), .out5(decoder_1_out5), .out6(decoder_1_out6), .out7(decoder_1_out7), .sel(dir_W),
    .en(enable));
  Register register_1 (.D(dato_W), .en(decoder_1_out7), .clk(clock), .Q({register_1_q_2, register_1_q}), .clr(reset));
  Register register_2 (.D(dato_W), .en(decoder_1_out6), .clk(clock), .Q({register_2_q_2, register_2_q}), .clr(reset));
  Register register_3 (.D(dato_W), .en(decoder_1_out5), .clk(clock), .Q({register_3_q_2, register_3_q}), .clr(reset));
  Register register_4 (.D(dato_W), .en(decoder_1_out4), .clk(clock), .Q({register_4_q_2, register_4_q}), .clr(reset));
  Register R3 (.D(dato_W), .en(decoder_1_out3), .clk(clock), .Q({R3_q_2, R3_q}), .clr(reset));
  Register R2 (.D(dato_W), .en(decoder_1_out2), .clk(clock), .Q({R2_q_2, R2_q}), .clr(reset));
  Register R1 (.D(dato_W), .en(decoder_1_out1), .clk(clock), .Q({R1_q_2, R1_q}), .clr(reset));
  Register R0 (.D(dato_W), .en(decoder_1_out0), .clk(clock), .Q({R0_q_2, R0_q}), .clr(reset));
  Hex_Digit_Display R7H (.value(register_1_q_2));  // open: dp
  Hex_Digit_Display R6H (.value(register_2_q_2));  // open: dp
  Hex_Digit_Display R5H (.value(register_3_q_2));  // open: dp
  Hex_Digit_Display R4H (.value(register_4_q_2));  // open: dp
  Hex_Digit_Display R3H (.value(R3_q_2));  // open: dp
  Hex_Digit_Display R2H (.value(R2_q_2));  // open: dp
  Hex_Digit_Display R1H (.value(R1_q_2));  // open: dp
  Hex_Digit_Display R0H (.value(R0_q_2));  // open: dp
  Hex_Digit_Display R7L (.value(register_1_q));  // open: dp
  Hex_Digit_Display R6L (.value(register_2_q));  // open: dp
  Hex_Digit_Display R5L (.value(register_3_q));  // open: dp
  Hex_Digit_Display R4L (.value(register_4_q));  // open: dp
  Hex_Digit_Display R3L (.value(R3_q));  // open: dp
  Hex_Digit_Display R2L (.value(R2_q));  // open: dp
  Hex_Digit_Display R1L (.value(R1_q));  // open: dp
  Hex_Digit_Display R0L (.value(R0_q));  // open: dp
  Hex_Digit_Display R7d2 (.value(binary_to_bcd_converter_1_p2));  // open: dp
  Hex_Digit_Display R7d1 (.value(binary_to_bcd_converter_1_p3));  // open: dp
  // Binary_to_BCD_converter #(.binvalue(8)) binary_to_bcd_converter_1: pin names not known; wires that end beside it: {register_1_q_2, register_1_q}, binary_to_bcd_converter_1_p2, binary_to_bcd_converter_1_p3, binary_to_bcd_converter_1_p4
  Hex_Digit_Display R6d2 (.value(binary_to_bcd_converter_2_p2));  // open: dp
  Hex_Digit_Display R6d1 (.value(binary_to_bcd_converter_2_p3));  // open: dp
  // Binary_to_BCD_converter #(.binvalue(8)) binary_to_bcd_converter_2: pin names not known; wires that end beside it: {register_2_q_2, register_2_q}, binary_to_bcd_converter_2_p2, binary_to_bcd_converter_2_p3, binary_to_bcd_converter_2_p4
  Hex_Digit_Display R5d2 (.value(binary_to_bcd_converter_3_p2));  // open: dp
  Hex_Digit_Display R5d1 (.value(binary_to_bcd_converter_3_p3));  // open: dp
  // Binary_to_BCD_converter #(.binvalue(8)) binary_to_bcd_converter_3: pin names not known; wires that end beside it: {register_3_q_2, register_3_q}, binary_to_bcd_converter_3_p2, binary_to_bcd_converter_3_p3, binary_to_bcd_converter_3_p4
  Hex_Digit_Display R4d2 (.value(binary_to_bcd_converter_4_p2));  // open: dp
  Hex_Digit_Display R4d1 (.value(binary_to_bcd_converter_4_p3));  // open: dp
  // Binary_to_BCD_converter #(.binvalue(8)) binary_to_bcd_converter_4: pin names not known; wires that end beside it: {register_4_q_2, register_4_q}, binary_to_bcd_converter_4_p2, binary_to_bcd_converter_4_p3, binary_to_bcd_converter_4_p4
  Hex_Digit_Display R3d2 (.value(binary_to_bcd_converter_5_p2));  // open: dp
  Hex_Digit_Display R3d1 (.value(binary_to_bcd_converter_5_p3));  // open: dp
  // Binary_to_BCD_converter #(.binvalue(8)) binary_to_bcd_converter_5: pin names not known; wires that end beside it: {R3_q_2, R3_q}, binary_to_bcd_converter_5_p2, binary_to_bcd_converter_5_p3, binary_to_bcd_converter_5_p4
  Hex_Digit_Display R2d2 (.value(binary_to_bcd_converter_6_p2));  // open: dp
  Hex_Digit_Display R2d1 (.value(binary_to_bcd_converter_6_p3));  // open: dp
  // Binary_to_BCD_converter #(.binvalue(8)) binary_to_bcd_converter_6: pin names not known; wires that end beside it: {R2_q_2, R2_q}, binary_to_bcd_converter_6_p2, binary_to_bcd_converter_6_p3, binary_to_bcd_converter_6_p4
  Hex_Digit_Display R1d2 (.value(binary_to_bcd_converter_7_p2));  // open: dp
  Hex_Digit_Display R1d1 (.value(binary_to_bcd_converter_7_p3));  // open: dp
  // Binary_to_BCD_converter #(.binvalue(8)) binary_to_bcd_converter_7: pin names not known; wires that end beside it: {R1_q_2, R1_q}, binary_to_bcd_converter_7_p2, binary_to_bcd_converter_7_p3, binary_to_bcd_converter_7_p4
  Hex_Digit_Display R0d2 (.value(binary_to_bcd_converter_8_p2));  // open: dp
  Hex_Digit_Display R0d1 (.value(binary_to_bcd_converter_8_p3));  // open: dp
  // Binary_to_BCD_converter #(.binvalue(8)) binary_to_bcd_converter_8: pin names not known; wires that end beside it: {R0_q_2, R0_q}, binary_to_bcd_converter_8_p2, binary_to_bcd_converter_8_p3, binary_to_bcd_converter_8_p4
  Hex_Digit_Display R7d0 (.value(binary_to_bcd_converter_1_p4));  // open: dp
  Hex_Digit_Display R6d0 (.value(binary_to_bcd_converter_2_p4));  // open: dp
  Hex_Digit_Display R5d0 (.value(binary_to_bcd_converter_3_p4));  // open: dp
  Hex_Digit_Display R4d0 (.value(binary_to_bcd_converter_4_p4));  // open: dp
  Hex_Digit_Display R3d0 (.value(binary_to_bcd_converter_5_p4));  // open: dp
  Hex_Digit_Display R2d0 (.value(binary_to_bcd_converter_6_p4));  // open: dp
  Hex_Digit_Display R1d0 (.value(binary_to_bcd_converter_7_p4));  // open: dp
  Hex_Digit_Display R0d0 (.value(binary_to_bcd_converter_8_p4));  // open: dp
  LED led_4 (.in(register_1_q_2[3]));
  LED led_5 (.in(register_1_q_2[2]));
  LED led_6 (.in(register_1_q_2[1]));
  LED led_7 (.in(register_2_q_2[3]));
  LED led_8 (.in(register_2_q_2[2]));
  LED led_9 (.in(register_2_q_2[1]));
  LED led_10 (.in(register_3_q_2[3]));
  LED led_11 (.in(register_3_q_2[2]));
  LED led_12 (.in(register_3_q_2[1]));
  LED b47 (.in(register_4_q_2[3]));
  LED b46 (.in(register_4_q_2[2]));
  LED b45 (.in(register_4_q_2[1]));
  LED b37 (.in(R3_q_2[3]));
  LED b36 (.in(R3_q_2[2]));
  LED b35 (.in(R3_q_2[1]));
  LED led_13 (.in(R2_q_2[3]));
  LED led_14 (.in(R2_q_2[2]));
  LED led_15 (.in(R2_q_2[1]));
  LED led_16 (.in(R1_q_2[3]));
  LED led_17 (.in(R1_q_2[2]));
  LED led_18 (.in(R1_q_2[1]));
  LED led_19 (.in(R0_q_2[3]));
  LED led_20 (.in(R0_q_2[2]));
  LED led_21 (.in(R0_q_2[1]));
  LED led_22 (.in(register_1_q_2[0]));
  LED led_23 (.in(register_1_q[3]));
  LED led_24 (.in(register_1_q[2]));
  LED led_25 (.in(register_1_q[1]));
  LED led_26 (.in(register_2_q_2[0]));
  LED led_27 (.in(register_2_q[3]));
  LED led_28 (.in(register_2_q[2]));
  LED led_29 (.in(register_2_q[1]));
  LED led_30 (.in(register_3_q_2[0]));
  LED led_31 (.in(register_3_q[3]));
  LED led_32 (.in(register_3_q[2]));
  LED led_33 (.in(register_3_q[1]));
  LED b44 (.in(register_4_q_2[0]));
  LED b43 (.in(register_4_q[3]));
  LED b42 (.in(register_4_q[2]));
  LED b41 (.in(register_4_q[1]));
  LED b34 (.in(R3_q_2[0]));
  LED b33 (.in(R3_q[3]));
  LED b32 (.in(R3_q[2]));
  LED b31 (.in(R3_q[1]));
  LED led_34 (.in(R2_q_2[0]));
  LED led_35 (.in(R2_q[3]));
  LED led_36 (.in(R2_q[2]));
  LED led_37 (.in(R2_q[1]));
  LED led_38 (.in(R1_q_2[0]));
  LED led_39 (.in(R1_q[3]));
  LED led_40 (.in(R1_q[2]));
  LED led_41 (.in(R1_q[1]));
  LED led_42 (.in(R0_q_2[0]));
  LED led_43 (.in(R0_q[3]));
  LED led_44 (.in(R0_q[2]));
  LED led_45 (.in(R0_q[1]));
  Multiplexer #(.select(3), .width(8)) multiplexer_1 (
    .in0({R0_q_2, R0_q}), .in1({R1_q_2, R1_q}), .in2({R2_q_2, R2_q}), .in3({R3_q_2, R3_q}),
    .in4({register_4_q_2, register_4_q}), .in5({register_3_q_2, register_3_q}),
    .in6({register_2_q_2, register_2_q}), .in7({register_1_q_2, register_1_q}), .out(RA), .sel(dir_RA));
  LED led_46 (.in(register_1_q[0]));
  LED led_47 (.in(register_2_q[0]));
  LED led_48 (.in(register_3_q[0]));
  LED b40 (.in(register_4_q[0]));
  LED b30 (.in(R3_q[0]));
  LED led_49 (.in(R2_q[0]));
  LED led_50 (.in(R1_q[0]));
  LED led_51 (.in(R0_q[0]));
  Multiplexer #(.select(3), .width(8)) multiplexer_2 (
    .in0({R0_q_2, R0_q}), .in1({R1_q_2, R1_q}), .in2({R2_q_2, R2_q}), .in3({R3_q_2, R3_q}),
    .in4({register_4_q_2, register_4_q}), .in5({register_3_q_2, register_3_q}),
    .in6({register_2_q_2, register_2_q}), .in7({register_1_q_2, register_1_q}), .out(RB), .sel(dir_RB));
endmodule

module los_reales_tests (
  input  in_1,
  input  [7:0] in_2,
  input  in_3,
  input  [1:0] in_4,
  input  in_5,
  input  [7:0] in_6,
  input  in_7,
  input  [7:0] in_8,
  input  in_9,
  input  in_10,
  input  in_11,
  input  in_12,
  input  [7:0] in_13,
  output [7:0] out_14,
  output [7:0] out_15
);

  wire button_1_out, button_2_out, button_3_out, button_4_out, button_5_out, button_6_out, button_7_out;
  wire [1:0] DirA, DirB, DirD, OP;
  wire [7:0] adder_1_out, and_1_out, counter_1_q, multiplexer_1_out, or_1_out, registers_4r_1_ra,
       registers_4r_1_rb, xnor_1_out;

  Button button_1 (.out(button_1_out));
  Button button_2 (.out(button_2_out));
  Button button_3 (.out(button_3_out));
  registers_2R_1 registers_2r_1_1 ();  // open: clock, dir_W, dato_W
  registers_2R_2 registers_2r_2_1 (.enable(in_3), .reset(button_2_out), .clock(in_7), .dir_W(in_5), .dato_W(in_6));
  registers_2R_3 registers_2r_3_1 (
    .dir_RA(in_10), .dir_RB(in_11), .enable(in_9), .reset(button_3_out), .clock(button_1_out), .dir_W(in_12),
    .dato_W(in_13), .RA(out_14), .RB(out_15));
  Button button_4 (.out(button_4_out));
  Button button_5 (.out(button_5_out));
  Button button_6 (.out(button_6_out));
  Counter counter_1 (.clr(button_5_out), .clk(button_6_out), .Q(counter_1_q));  // open: load, up, count, D, carry
  Button button_7 (.out(button_7_out));
  registers_4R registers_4r_1 (
    .dir_RA(DirA), .dir_RB(DirB), .enable(in_1), .reset(button_7_out), .clock(button_4_out), .dir_W(DirD),
    .dato_W(multiplexer_1_out), .RA(registers_4r_1_ra), .RB(registers_4r_1_rb));
  ROM rom_1 (.addr(counter_1_q), .data({DirD, DirA, OP, DirB}));
  // Probe on registers_4r_1_ra
  // Probe on registers_4r_1_rb
  Multiplexer #(.select(2), .width(8)) multiplexer_1 (
    .in0(and_1_out), .in1(or_1_out), .in2(xnor_1_out), .in3(adder_1_out), .out(multiplexer_1_out), .sel(OP));
  assign and_1_out = registers_4r_1_ra & registers_4r_1_rb;  // AND_Gate and_1, 8 bits wide
  // Probe on and_1_out
  // Probe on in_8
  // Probe on or_1_out
  assign or_1_out = registers_4r_1_ra | registers_4r_1_rb;  // OR_Gate or_1, 8 bits wide
  // Probe on xnor_1_out
  assign xnor_1_out = ~(registers_4r_1_ra ^ registers_4r_1_rb);  // XNOR_Gate xnor_1, 8 bits wide
  // Probe on adder_1_out
  Adder adder_1 (.a(registers_4r_1_ra), .b(registers_4r_1_rb), .out(adder_1_out));  // open: cin, cout

  // Notes on the sheet:
  //   contents of rom_1 (hex, n*v repeats v):
  //   8 4c b9 ee 3f c 2c
  //   XNOR R0,R0,R0
  //   SUM R1,R0,R0
  //   XNOR R2,R3,R1
  //   SUM R3,R2,R2
  //   SUM R0,R2,R2
  //   SUM R0,R0,R0
  //   SUM R0,R2,R0
endmodule

module hola (
  input  in_1,
  input  in_2
);

  wire button_1_out, button_2_out, button_3_out, button_4_out, button_5_out, button_6_out;
  wire [1:0] OP, OP1;
  wire [2:0] DirA, DirA1, DirB, DirB1;
  wire [7:0] adder_1_out, alu_1_out_4, and_1_out, counter_1_q, counter_2_q, multiplexer_1_out, not_1_out,
       or_1_out, registers_8r_1_ra, registers_8r_1_rb, registers_8r_2_ra, registers_8r_2_rb, xnor_1_out;

  Button button_1 (.out(button_1_out));
  Button button_2 (.out(button_2_out));
  Counter counter_1 (.clr(button_2_out), .clk(button_1_out), .Q(counter_1_q));  // open: load, up, count, D, carry
  Button button_3 (.out(button_3_out));
  registers_8R registers_8r_1 (
    .dir_RA(DirA), .dir_RB(DirB), .enable(in_1), .dir_W(DirA), .reset(button_3_out), .clock(button_1_out),
    .dato_W(alu_1_out_4), .RA(registers_8r_1_ra), .RB(registers_8r_1_rb));
  ROM rom_1 (.addr(counter_1_q), .data({OP, DirA, DirB}));
  ALU alu_1 (.in_1(registers_8r_1_ra), .in_2(registers_8r_1_rb), .in_3(OP), .out_4(alu_1_out_4));
  Button button_4 (.out(button_4_out));
  Counter counter_2 (.clr(button_5_out), .clk(button_4_out), .Q(counter_2_q));  // open: load, up, count, D, carry
  Button button_5 (.out(button_5_out));
  Button button_6 (.out(button_6_out));
  ROM rom_2 (.addr(counter_2_q), .data({OP1, DirA1, DirB1}));
  // Probe on registers_8r_2_ra
  registers_8R registers_8r_2 (
    .dir_RA(DirA1), .dir_RB(DirB1), .enable(in_2), .dir_W(DirA1), .reset(button_6_out), .clock(button_4_out),
    .dato_W(multiplexer_1_out), .RA(registers_8r_2_ra), .RB(registers_8r_2_rb));
  // Probe on registers_8r_2_rb
  Multiplexer #(.select(2), .width(8)) multiplexer_1 (
    .in0(and_1_out), .in1(or_1_out), .in2(not_1_out), .in3(adder_1_out), .out(multiplexer_1_out), .sel(OP1));
  assign and_1_out = registers_8r_2_ra & registers_8r_2_rb;  // AND_Gate and_1, 8 bits wide
  // Probe on and_1_out
  assign or_1_out = registers_8r_2_ra | registers_8r_2_rb;  // OR_Gate or_1, 8 bits wide
  // Probe on or_1_out
  // Probe on not_1_out
  assign xnor_1_out = ~(registers_8r_2_ra ^ registers_8r_2_rb);  // XNOR_Gate xnor_1, 8 bits wide
  assign not_1_out = ~xnor_1_out;  // NOT_Gate not_1, 8 bits wide
  Adder adder_1 (.a(registers_8r_2_ra), .b(registers_8r_2_rb), .out(adder_1_out));  // open: cin, cout
  // Probe on adder_1_out

  // Notes on the sheet:
  //   contents of rom_1 (hex, n*v repeats v):
  //   80 89 c0 82 c0 f8 e8 e0 e0 d0 c cc
  //   contents of rom_2 (hex, n*v repeats v):
  //   80 89 c0 82 c0 f8 e8 e0 e0 d0 c cc
endmodule

module ALU (
  input  [7:0] in_1,
  input  [7:0] in_2,
  input  [1:0] in_3,
  output [7:0] out_4
);

  wire [7:0] adder_1_out, and_1_out, or_1_out, xnor_1_out;

  // Probe on in_1
  // Probe on in_2
  Multiplexer #(.select(2), .width(8)) multiplexer_1 (
    .in0(and_1_out), .in1(or_1_out), .in2(xnor_1_out), .in3(adder_1_out), .out(out_4), .sel(in_3));
  // Probe on and_1_out
  assign and_1_out = in_1 & in_2;  // AND_Gate and_1, 8 bits wide
  // Probe on or_1_out
  assign or_1_out = in_1 | in_2;  // OR_Gate or_1, 8 bits wide
  // Probe on xnor_1_out
  assign xnor_1_out = ~(in_1 ^ in_2);  // XNOR_Gate xnor_1, 8 bits wide
  // Probe on adder_1_out
  Adder adder_1 (.a(in_1), .b(in_2), .out(adder_1_out));  // open: cin, cout
endmodule
