// Logisim project ContadorYClock.circ as structural Verilog: 1 circuit, main circuit main
module main (
  output [1:0] out_1
);

  wire clock_1_out;

  Clock clock_1 (.out(clock_1_out));
  Counter #(.max('h3), .width(2)) counter_1 (.clk(clock_1_out), .Q(out_1));  // open: clr, load, up, count, D, carry
endmodule
