// Logisim project Tutorial.circ as structural Verilog: 2 circuits, main circuit main
module main (
  input  [7:0] in_1,
  input  [7:0] in_2,
  input  [7:0] in_3,
  input  [7:0] in_4,
  input  [7:0] in_5,
  input  [7:0] in_6,
  input  [7:0] in_7,
  output [7:0] out_8,
  output [7:0] out_9,
  output [7:0] out_10,
  output [7:0] out_11
);

  assign out_8 = ~in_1;  // NOT_Gate not_1, 8 bits wide
  assign out_9 = in_2 & in_3;  // AND_Gate and_1, 8 bits wide
  assign out_10 = in_4 | in_5;  // OR_Gate or_1, 8 bits wide
  assign out_11 = ~(in_6 ^ in_7);  // XNOR_Gate xnor_1, 8 bits wide
  NOTengoLab notengolab_1 (.Entrada(out_8));  // open: Salida
  NOTengoLab notengolab_2 (.Entrada(out_9));  // open: Salida
  NOTengoLab notengolab_3 (.Entrada(out_10));  // open: Salida
  NOTengoLab notengolab_4 (.Entrada(out_11));  // open: Salida
endmodule

module NOTengoLab (
  input  [7:0] Entrada,
  output [7:0] Salida
);

  LED Y7 (.in(Salida[7]));
  LED Y6 (.in(Salida[6]));
  assign Salida = ~Entrada;  // NOT_Gate not_1, 8 bits wide
  LED Y5 (.in(Salida[5]));
  LED Y4 (.in(Salida[4]));
  LED Y3 (.in(Salida[3]));
  LED Y2 (.in(Salida[2]));
  LED Y1 (.in(Salida[1]));
  LED Y0 (.in(Salida[0]));
endmodule
