// Logisim project probeTest.circ as structural Verilog: 1 circuit, main circuit main
module main (
  input  [7:0] in_1,
  output [7:0] out_2
);

  // Probe on in_1
  // Probe on in_1
  // Probe on in_1

  assign out_2 = in_1;
endmodule
