// Logisim project circEnBaseATablaVerdad.circ as structural Verilog: 2 circuits, main circuit main
module main (
  input  [2:0] in_1
);

  circuitoTabla circuitotabla_1 (.entrada(in_1));  // open: salida
endmodule

module circuitoTabla (
  input  [2:0] entrada,
  output [2:0] salida
);

  wire and_1_out, and_2_out, and_3_out, and_4_out, and_5_out, not_1_out, not_2_out, not_3_out;

  not not_1 (not_1_out, entrada[2]);
  not not_2 (not_2_out, entrada[1]);
  not not_3 (not_3_out, entrada[0]);
  and and_1 (and_1_out, not_1_out, not_2_out);
  and and_2 (and_2_out, entrada[2], entrada[1]);
  and and_3 (and_3_out, not_1_out, not_3_out);
  and and_4 (and_4_out, not_2_out, not_3_out);
  and and_5 (and_5_out, entrada[1], entrada[0]);
  or or_1 (salida[2], and_1_out, and_2_out, and_3_out);
  or or_2 (salida[0], and_4_out, and_5_out);
  LedBar #(.matrixcols(3)) ledbar_1 (.led0(salida[2]), .led1(1'b1), .led2(salida[0]));

  assign salida[1] = 1'b1;
endmodule
