// Logisim project Clase_3_plantilla.circ as structural Verilog: 5 circuits, main circuit registers_8R
module registers_8R (
  input  reset,
  input  [2:0] dir_RB,
  input  clock,
  input  [7:0] dato_W,
  input  enable,
  input  [2:0] dir_RA,
  input  [2:0] dir_W,
  output [7:0] RB,
  output [7:0] RA
);

  wire decoder_1_out0, decoder_1_out1, decoder_1_out2, decoder_1_out3, decoder_1_out4, decoder_1_out5,
       decoder_1_out6, decoder_1_out7;
  wire [3:0] binary_to_bcd_converter_1_p2, binary_to_bcd_converter_1_p3, binary_to_bcd_converter_1_p4,
       binary_to_bcd_converter_2_p2, binary_to_bcd_converter_2_p3, binary_to_bcd_converter_2_p4,
       binary_to_bcd_converter_3_p2, binary_to_bcd_converter_3_p3, binary_to_bcd_converter_3_p4,
       binary_to_bcd_converter_4_p2, binary_to_bcd_converter_4_p3, binary_to_bcd_converter_4_p4,
       binary_to_bcd_converter_5_p2, binary_to_bcd_converter_5_p3, binary_to_bcd_converter_5_p4,
       binary_to_bcd_converter_6_p2, binary_to_bcd_converter_6_p3, binary_to_bcd_converter_6_p4,
       binary_to_bcd_converter_7_p2, binary_to_bcd_converter_7_p3, binary_to_bcd_converter_7_p4,
       binary_to_bcd_converter_8_p2, binary_to_bcd_converter_8_p3, binary_to_bcd_converter_8_p4, R0_q,
       R0_q_2, R1_q, R1_q_2, R2_q, R2_q_2, R3_q, R3_q_2, register_1_q, register_1_q_2, register_2_q,
       register_2_q_2, register_3_q, register_3_q_2, register_4_q, register_4_q_2;

  LED W_EN_led (.in(enable));
  LED led_1 (.in(enable));
  LED led_2 (.in(enable));
  LED led_3 (.in(enable));
  Decoder #(.select(3)) decoder_1 (
    .out0(decoder_1_out0), .out1(decoder_1_out1), .out2(decoder_1_out2), .out3(decoder_1_out3),
    .out4(decoder_1_out4), .out5(decoder_1_out5), .out6(decoder_1_out6), .out7(decoder_1_out7), .sel(dir_W),
    .en(enable));
  Register register_1 (.D(dato_W), .en(decoder_1_out7), .clk(clock), .Q({register_1_q_2, register_1_q}), .clr(reset));
  Register register_2 (.D(dato_W), .en(decoder_1_out6), .clk(clock), .Q({register_2_q_2, register_2_q}), .clr(reset));
  Register register_3 (.D(dato_W), .en(decoder_1_out5), .clk(clock), .Q({register_3_q_2, register_3_q}), .clr(reset));
  Register register_4 (.D(dato_W), .en(decoder_1_out4), .clk(clock), .Q({register_4_q_2, register_4_q}), .clr(reset));
  Register R3 (.D(dato_W), .en(decoder_1_out3), .clk(clock), .Q({R3_q_2, R3_q}), .clr(reset));
  Register R2 (.D(dato_W), .en(decoder_1_out2), .clk(clock), .Q({R2_q_2, R2_q}), .clr(reset));
  Register R1 (.D(dato_W), .en(decoder_1_out1), .clk(clock), .Q({R1_q_2, R1_q}), .clr(reset));
  Register R0 (.D(dato_W), .en(decoder_1_out0), .clk(clock), .Q({R0_q_2, R0_q}), .clr(reset));
  Hex_Digit_Display R7H (.value(register_1_q_2));  // open: dp
  Hex_Digit_Display R6H (.value(register_2_q_2));  // open: dp
  Hex_Digit_Display R5H (.value(register_3_q_2));  // open: dp
  Hex_Digit_Display R4H (.value(register_4_q_2));  // open: dp
  Hex_Digit_Display R3H (.value(R3_q_2));  // open: dp
  Hex_Digit_Display R2H (.value(R2_q_2));  // open: dp
  Hex_Digit_Display R1H (.value(R1_q_2));  // open: dp
  Hex_Digit_Display R0H (.value(R0_q_2));  // open: dp
  Hex_Digit_Display R7L (.value(register_1_q));  // open: dp
  Hex_Digit_Display R6L (.value(register_2_q));  // open: dp
  Hex_Digit_Display R5L (.value(register_3_q));  // open: dp
  Hex_Digit_Display R4L (.value(register_4_q));  // open: dp
  Hex_Digit_Display R3L (.value(R3_q));  // open: dp
  Hex_Digit_Display R2L (.value(R2_q));  // open: dp
  Hex_Digit_Display R1L (.value(R1_q));  // open: dp
  Hex_Digit_Display R0L (.value(R0_q));  // open: dp
  Hex_Digit_Display R7d2 (.value(binary_to_bcd_converter_1_p2));  // open: dp
  Hex_Digit_Display R7d1 (.value(binary_to_bcd_converter_1_p3));  // open: dp
  // Binary_to_BCD_converter #(.binvalue(8)) binary_to_bcd_converter_1: pin names not known; wires that end beside it: {register_1_q_2, register_1_q}, binary_to_bcd_converter_1_p2, binary_to_bcd_converter_1_p3, binary_to_bcd_converter_1_p4
  Hex_Digit_Display R6d2 (.value(binary_to_bcd_converter_2_p2));  // open: dp
  Hex_Digit_Display R6d1 (.value(binary_to_bcd_converter_2_p3));  // open: dp
  // Binary_to_BCD_converter #(.binvalue(8)) binary_to_bcd_converter_2: pin names not known; wires that end beside it: {register_2_q_2, register_2_q}, binary_to_bcd_converter_2_p2, binary_to_bcd_converter_2_p3, binary_to_bcd_converter_2_p4
  Hex_Digit_Display R5d2 (.value(binary_to_bcd_converter_3_p2));  // open: dp
  Hex_Digit_Display R5d1 (.value(binary_to_bcd_converter_3_p3));  // open: dp
  // Binary_to_BCD_converter #(.binvalue(8)) binary_to_bcd_converter_3: pin names not known; wires that end beside it: {register_3_q_2, register_3_q}, binary_to_bcd_converter_3_p2, binary_to_bcd_converter_3_p3, binary_to_bcd_converter_3_p4
  Hex_Digit_Display R4d2 (.value(binary_to_bcd_converter_4_p2));  // open: dp
  Hex_Digit_Display R4d1 (.value(binary_to_bcd_converter_4_p3));  // open: dp
  // Binary_to_BCD_converter #(.binvalue(8)) binary_to_bcd_converter_4: pin names not known; wires that end beside it: {register_4_q_2, register_4_q}, binary_to_bcd_converter_4_p2, binary_to_bcd_converter_4_p3, binary_to_bcd_converter_4_p4
  Hex_Digit_Display R3d2 (.value(binary_to_bcd_converter_5_p2));  // open: dp
  Hex_Digit_Display R3d1 (.value(binary_to_bcd_converter_5_p3));  // open: dp
  // Binary_to_BCD_converter #(.binvalue(8)) binary_to_bcd_converter_5: pin names not known; wires that end beside it: {R3_q_2, R3_q}, binary_to_bcd_converter_5_p2, binary_to_bcd_converter_5_p3, binary_to_bcd_converter_5_p4
  Hex_Digit_Display R2d2 (.value(binary_to_bcd_converter_6_p2));  // open: dp
  Hex_Digit_Display R2d1 (.value(binary_to_bcd_converter_6_p3));  // open: dp
  // Binary_to_BCD_converter #(.binvalue(8)) binary_to_bcd_converter_6: pin names not known; wires that end beside it: {R2_q_2, R2_q}, binary_to_bcd_converter_6_p2, binary_to_bcd_converter_6_p3, binary_to_bcd_converter_6_p4
  Hex_Digit_Display R1d2 (.value(binary_to_bcd_converter_7_p2));  // open: dp
  Hex_Digit_Display R1d1 (.value(binary_to_bcd_converter_7_p3));  // open: dp
  // Binary_to_BCD_converter #(.binvalue(8)) binary_to_bcd_converter_7: pin names not known; wires that end beside it: {R1_q_2, R1_q}, binary_to_bcd_converter_7_p2, binary_to_bcd_converter_7_p3, binary_to_bcd_converter_7_p4
  Hex_Digit_Display R0d2 (.value(binary_to_bcd_converter_8_p2));  // open: dp
  Hex_Digit_Display R0d1 (.value(binary_to_bcd_converter_8_p3));  // open: dp
  // Binary_to_BCD_converter #(.binvalue(8)) binary_to_bcd_converter_8: pin names not known; wires that end beside it: {R0_q_2, R0_q}, binary_to_bcd_converter_8_p2, binary_to_bcd_converter_8_p3, binary_to_bcd_converter_8_p4
  Hex_Digit_Display R7d0 (.value(binary_to_bcd_converter_1_p4));  // open: dp
  Hex_Digit_Display R6d0 (.value(binary_to_bcd_converter_2_p4));  // open: dp
  Hex_Digit_Display R5d0 (.value(binary_to_bcd_converter_3_p4));  // open: dp
  Hex_Digit_Display R4d0 (.value(binary_to_bcd_converter_4_p4));  // open: dp
  Hex_Digit_Display R3d0 (.value(binary_to_bcd_converter_5_p4));  // open: dp
  Hex_Digit_Display R2d0 (.value(binary_to_bcd_converter_6_p4));  // open: dp
  Hex_Digit_Display R1d0 (.value(binary_to_bcd_converter_7_p4));  // open: dp
  Hex_Digit_Display R0d0 (.value(binary_to_bcd_converter_8_p4));  // open: dp
  LED led_4 (.in(register_1_q_2[3]));
  LED led_5 (.in(register_1_q_2[2]));
  LED led_6 (.in(register_1_q_2[1]));
  LED led_7 (.in(register_2_q_2[3]));
  LED led_8 (.in(register_2_q_2[2]));
  LED led_9 (.in(register_2_q_2[1]));
  LED led_10 (.in(register_3_q_2[3]));
  LED led_11 (.in(register_3_q_2[2]));
  LED led_12 (.in(register_3_q_2[1]));
  LED b47 (.in(register_4_q_2[3]));
  LED b46 (.in(register_4_q_2[2]));
  LED b45 (.in(register_4_q_2[1]));
  LED b37 (.in(R3_q_2[3]));
  LED b36 (.in(R3_q_2[2]));
  LED b35 (.in(R3_q_2[1]));
  LED led_13 (.in(R2_q_2[3]));
  LED led_14 (.in(R2_q_2[2]));
  LED led_15 (.in(R2_q_2[1]));
  LED led_16 (.in(R1_q_2[3]));
  LED led_17 (.in(R1_q_2[2]));
  LED led_18 (.in(R1_q_2[1]));
  LED led_19 (.in(R0_q_2[3]));
  LED led_20 (.in(R0_q_2[2]));
  LED led_21 (.in(R0_q_2[1]));
  LED led_22 (.in(register_1_q_2[0]));
  LED led_23 (.in(register_1_q[3]));
  LED led_24 (.in(register_1_q[2]));
  LED led_25 (.in(register_1_q[1]));
  LED led_26 (.in(register_2_q_2[0]));
  LED led_27 (.in(register_2_q[3]));
  LED led_28 (.in(register_2_q[2]));
  LED led_29 (.in(register_2_q[1]));
  LED led_30 (.in(register_3_q_2[0]));
  LED led_31 (.in(register_3_q[3]));
  LED led_32 (.in(register_3_q[2]));
  LED led_33 (.in(register_3_q[1]));
  LED b44 (.in(register_4_q_2[0]));
  LED b43 (.in(register_4_q[3]));
  LED b42 (.in(register_4_q[2]));
  LED b41 (.in(register_4_q[1]));
  LED b34 (.in(R3_q_2[0]));
  LED b33 (.in(R3_q[3]));
  LED b32 (.in(R3_q[2]));
  LED b31 (.in(R3_q[1]));
  LED led_34 (.in(R2_q_2[0]));
  LED led_35 (.in(R2_q[3]));
  LED led_36 (.in(R2_q[2]));
  LED led_37 (.in(R2_q[1]));
  LED led_38 (.in(R1_q_2[0]));
  LED led_39 (.in(R1_q[3]));
  LED led_40 (.in(R1_q[2]));
  LED led_41 (.in(R1_q[1]));
  LED led_42 (.in(R0_q_2[0]));
  LED led_43 (.in(R0_q[3]));
  LED led_44 (.in(R0_q[2]));
  LED led_45 (.in(R0_q[1]));
  Multiplexer #(.select(3), .width(8)) multiplexer_1 (
    .in0({R0_q_2, R0_q}), .in1({R1_q_2, R1_q}), .in2({R2_q_2, R2_q}), .in3({R3_q_2, R3_q}),
    .in4({register_4_q_2, register_4_q}), .in5({register_3_q_2, register_3_q}),
    .in6({register_2_q_2, register_2_q}), .in7({register_1_q_2, register_1_q}), .out(RA), .sel(dir_RA));
  LED led_46 (.in(register_1_q[0]));
  LED led_47 (.in(register_2_q[0]));
  LED led_48 (.in(register_3_q[0]));
  LED b40 (.in(register_4_q[0]));
  LED b30 (.in(R3_q[0]));
  LED led_49 (.in(R2_q[0]));
  LED led_50 (.in(R1_q[0]));
  LED led_51 (.in(R0_q[0]));
  Multiplexer #(.select(3), .width(8)) multiplexer_2 (
    .in0({R0_q_2, R0_q}), .in1({R1_q_2, R1_q}), .in2({R2_q_2, R2_q}), .in3({R3_q_2, R3_q}),
    .in4({register_4_q_2, register_4_q}), .in5({register_3_q_2, register_3_q}),
    .in6({register_2_q_2, register_2_q}), .in7({register_1_q_2, register_1_q}), .out(RB), .sel(dir_RB));
endmodule

module Compu_1_1 (
  input  [7:0] in_1
);

  wire resetear, tictac;
  wire [1:0] ope;
  wire [2:0] dirA, dirB;
  wire [7:0] adder_1_out, counter_1_q, multiplexer_1_out, multiplexer_2_out, not_1_out, registers_8r_1_ra,
       registers_8r_1_rb;

  Counter counter_1 (.clr(resetear), .clk(tictac), .Q(counter_1_q));  // open: load, up, count, D, carry
  ROM rom_1 (.addr(counter_1_q), .data({ope[1], dirB[1:0], dirA[1:0], dirB[2], dirA[2], ope[0]}));
  Button button_1 (.out(resetear));
  // Probe on ope
  // Probe on in_1
  // Probe on dirA
  // Probe on dirB
  Button button_2 (.out(tictac));
  // Probe on 8'h1d
  // Probe on dirB
  registers_8R registers_8r_1 (
    .dir_RA(dirA), .dir_RB(dirB), .enable(1'b1), .dir_W(dirA), .reset(resetear), .clock(tictac),
    .dato_W(multiplexer_1_out), .RA(registers_8r_1_ra), .RB(registers_8r_1_rb));
  // Probe on multiplexer_1_out
  // Probe on multiplexer_1_out
  // Probe on multiplexer_1_out
  Multiplexer #(.select(2), .width(8)) multiplexer_1 (
    .in0(registers_8r_1_rb), .in1(adder_1_out), .in2({{5{1'b0}}, dirB}), .in3(multiplexer_2_out),
    .out(multiplexer_1_out), .sel(ope));
  Adder adder_1 (.a(registers_8r_1_ra), .b(registers_8r_1_rb), .out(adder_1_out));  // open: cin, cout
  assign not_1_out = ~registers_8r_1_ra;  // NOT_Gate not_1, 8 bits wide
  Multiplexer #(.select(3), .width(8)) multiplexer_2 (
    .in0(not_1_out), .out(multiplexer_2_out), .sel(dirB));  // open: in1, in2, in3, in4, in5, in6, in7

  // Other names for the same wires on the sheet: inm[2:0] = dirB

  // Notes on the sheet:
  //   contents of rom_1 (hex, n*v repeats v):
  //   ea ac d0 a2 1d 15 1e 46 8b ab cb ef
  //   No muevan nada de lo que ya está puesto !!
  //   COPY
  //   SUM
  //   LOAD
  //   NOT
  //   Probar LOAD, SUM, COPY, NOT
endmodule

module Compu_1_2 (
  input  [7:0] in_1
);

  wire resetear, tictac;
  wire [1:0] ope;
  wire [2:0] dirA, dirB;
  wire [7:0] adder_1_out, counter_1_q, multiplexer_1_out, multiplexer_2_out, not_1_out, registers_8r_1_ra,
       registers_8r_1_rb;

  Counter counter_1 (.clr(resetear), .clk(tictac), .Q(counter_1_q));  // open: load, up, count, D, carry
  ROM rom_1 (.addr(counter_1_q), .data({ope[1], dirB[1:0], dirA[1:0], dirB[2], dirA[2], ope[0]}));
  Button button_1 (.out(resetear));
  // Probe on ope
  // Probe on in_1
  // Probe on dirA
  // Probe on dirB
  Button button_2 (.out(tictac));
  // Probe on dirB
  registers_8R registers_8r_1 (
    .dir_RA(dirA), .dir_RB(dirB), .enable(1'b1), .dir_W(dirA), .reset(resetear), .clock(tictac),
    .dato_W(multiplexer_1_out), .RA(registers_8r_1_ra), .RB(registers_8r_1_rb));
  // Probe on multiplexer_1_out
  // Probe on multiplexer_1_out
  // Probe on multiplexer_1_out
  Multiplexer #(.select(2), .width(8)) multiplexer_1 (
    .in0(registers_8r_1_rb), .in1(adder_1_out), .in2({{5{1'b0}}, dirB}), .in3(multiplexer_2_out),
    .out(multiplexer_1_out), .sel(ope));
  Adder adder_1 (.a(registers_8r_1_ra), .b(registers_8r_1_rb), .out(adder_1_out));  // open: cin, cout
  Multiplexer #(.select(3), .width(8)) multiplexer_2 (
    .in0(not_1_out), .in1({registers_8r_1_ra[3:0], registers_8r_1_ra[7:4]}),
    .in2({registers_8r_1_ra[0], registers_8r_1_ra[1], registers_8r_1_ra[2], registers_8r_1_ra[3], registers_8r_1_ra[4], registers_8r_1_ra[5], registers_8r_1_ra[6], registers_8r_1_ra[7]}),
    .in4({registers_8r_1_ra[6:0], 1'b0}), .in5({1'b0, registers_8r_1_ra[7:1]}),
    .in6({registers_8r_1_ra[6:0], registers_8r_1_ra[7]}),
    .in7({registers_8r_1_ra[0], registers_8r_1_ra[7:1]}), .out(multiplexer_2_out), .sel(dirB));  // open: in3
  assign not_1_out = ~registers_8r_1_ra;  // NOT_Gate not_1, 8 bits wide

  // Other names for the same wires on the sheet: inm[2:0] = dirB

  // Notes on the sheet:
  //   contents of rom_1 (hex, n*v repeats v):
  //   ea ac d0 a2 1d 15 1e 46 8b 4*ab
  //   COPY
  //   SUM
  //   LOAD
  //   NOT
  //   XNOR?
  //   SWAPN
  //   FLIP
  //   (reserved)
  //   LSL
  //   LSR
  //   ROL
  //   ROR
endmodule

module Compu_1_3 (
  input  [7:0] in_1
);

  wire and_1_out, and_2_out, and_3_out, resetear, tictac;
  wire [1:0] ope, xnor_2_out;
  wire [2:0] dirA, dirB, xnor_1_out;
  wire [7:0] adder_1_out, adder_2_out, counter_1_q, multiplexer_1_out, multiplexer_2_out, multiplexer_3_out,
       not_1_out, RA, registers_8r_1_rb;

  Counter counter_1 (
    .clr(resetear), .load(1'b1), .clk(tictac), .D(adder_1_out), .Q(counter_1_q));  // open: up, count, carry
  assign xnor_1_out = ~(dirB ^ 3'b011);  // XNOR_Gate xnor_1, 3 bits wide
  assign xnor_2_out = ~(ope ^ 2'b11);  // XNOR_Gate xnor_2, 2 bits wide
  and and_1 (and_1_out, xnor_1_out[0], xnor_1_out[1], xnor_1_out[2]);
  and and_2 (and_2_out, xnor_2_out[0], xnor_2_out[1]);
  and and_3 (and_3_out, and_1_out, and_2_out);
  Adder adder_1 (.a(counter_1_q), .b(multiplexer_1_out), .out(adder_1_out));  // open: cin, cout
  Multiplexer #(.width(8)) multiplexer_1 (
    .in0(8'h1), .in1({{5{1'b0}}, dirA}), .out(multiplexer_1_out), .sel(and_3_out));
  ROM rom_1 (.addr(counter_1_q), .data({ope[1], dirB[1:0], dirA[1:0], dirB[2], dirA[2], ope[0]}));
  Button button_1 (.out(resetear));
  // Probe on ope
  // Probe on in_1
  // Probe on dirA
  // Probe on dirB
  Button button_2 (.out(tictac));
  // Probe on {{5{1'b0}}, dirA}
  // Probe on dirB
  registers_8R registers_8r_1 (
    .dir_RA(dirA), .dir_RB(dirB), .enable(1'b1), .dir_W(dirA), .reset(resetear), .clock(tictac),
    .dato_W(multiplexer_2_out), .RA(RA), .RB(registers_8r_1_rb));
  // Probe on multiplexer_2_out
  // Probe on multiplexer_2_out
  // Probe on multiplexer_2_out
  Multiplexer #(.select(2), .width(8)) multiplexer_2 (
    .in0(registers_8r_1_rb), .in1(adder_2_out), .in2({{5{1'b0}}, dirB}), .in3(multiplexer_3_out),
    .out(multiplexer_2_out), .sel(ope));
  Adder adder_2 (.a(RA), .b(registers_8r_1_rb), .out(adder_2_out));  // open: cin, cout
  Multiplexer #(.select(3), .width(8)) multiplexer_3 (
    .in0(not_1_out), .in1({RA[3:0], RA[7:4]}),
    .in2({RA[0], RA[1], RA[2], RA[3], RA[4], RA[5], RA[6], RA[7]}), .in3(RA), .in4({RA[6:0], 1'b0}),
    .in5({1'b0, RA[7:1]}), .in6({RA[6:0], RA[7]}), .in7({RA[0], RA[7:1]}), .out(multiplexer_3_out), .sel(dirB));
  assign not_1_out = ~RA;  // NOT_Gate not_1, 8 bits wide

  // Other names for the same wires on the sheet: inm[2:0] = dirB; step[2:0] = dirA

  // Notes on the sheet:
  //   El contador es un registro
  //   contents of rom_1 (hex, n*v repeats v):
  //   ea ac d0 a2 1d 15 1e 46 8b e9 ab ab ab
  //   COPY
  //   SUM
  //   LOAD
  //   NOT
  //   XNOR?
  //   SWAPN
  //   FLIP
  //   JUMPR
  //   LSL
  //   LSR
  //   ROL
  //   ROR
endmodule

module contador (
);

  wire button_1_out, button_2_out;
  wire [7:0] adder_1_out, counter_1_q;

  Button button_1 (.out(button_1_out));
  // Probe on adder_1_out
  Counter counter_1 (
    .clr(button_2_out), .load(1'b1), .clk(button_1_out), .D(adder_1_out), .Q(counter_1_q));  // open: up, count, carry
  Button button_2 (.out(button_2_out));
  // Probe on counter_1_q
  Adder adder_1 (.a(counter_1_q), .b(8'h2), .out(adder_1_out));  // open: cin, cout
endmodule
