// Logisim project experimentacion.circ as structural Verilog: 1 circuit, main circuit main
module main (
  input  in_1,
  input  in_2,
  input  in_3,
  input  [6:0] in_4,
  input  [6:0] in_5,
  input  [6:0] in_6
);

  wire dipswitch_1_sw1;

  DotMatrix dotmatrix_1 (.col0(in_4), .col1(in_5), .col2(in_6));  // open: col3, col4
  // RGBLED rgbled_1: pin names not known; wires that end beside it: in_2, in_1, in_3
  LED led_1 (.in(dipswitch_1_sw1));
  DipSwitch dipswitch_1 (.sw1(dipswitch_1_sw1));  // open: sw2, sw3, sw4, sw5, sw6, sw7, sw8
endmodule
