// Logisim project 20240282_LAB_1.circ as structural Verilog: 7 circuits, main circuit main
module preg_1 (
  input  [2:0] in_1,
  input  in_2,
  output out_3,
  output out_4,
  output out_5
);

  wire and_1_out, and_2_out, and_3_out, and_4_out, and_5_out, and_6_out, and_7_out, not_1_out, not_2_out,
       not_3_out;
  wire [2:0] or_1_out;

  not not_1 (not_1_out, in_1[2]);
  not not_2 (not_2_out, in_1[1]);
  not not_3 (not_3_out, in_1[0]);
  and and_1 (and_1_out, not_1_out, not_2_out);
  and and_2 (and_2_out, not_2_out, not_3_out);
  and and_3 (and_3_out, not_2_out, in_1[0]);
  and and_4 (and_4_out, not_1_out, in_1[1], not_3_out);
  and and_5 (and_5_out, not_1_out, not_2_out, not_3_out);
  and and_6 (and_6_out, not_1_out, in_1[1], in_1[0]);
  and and_7 (and_7_out, in_1[2], not_2_out, in_1[0]);
  or or_1 (or_1_out[0], and_1_out, and_2_out);
  or or_2 (or_1_out[1], and_3_out, and_4_out);
  or or_3 (or_1_out[2], and_5_out, and_6_out, and_7_out);
  assign {out_5, out_4, out_3} = or_1_out & {3{in_2}};  // AND_Gate and_8, 3 bits wide
endmodule

module preg_2 (
  input  in_1
);

  wire [2:0] counter_1_q;
  wire [3:0] multiplexer_1_out;

  Counter #(.max('h7), .width(3)) counter_1 (.clk(in_1), .Q(counter_1_q));  // open: clr, load, up, count, D, carry
  Multiplexer #(.select(3), .width(4)) multiplexer_1 (
    .in0(4'b0010), .in1(4'b0000), .in2(4'b0010), .in3(4'b0100), .in4(4'b0000), .in5(4'b0010), .in6(4'b1000),
    .in7(4'b0010), .out(multiplexer_1_out), .sel(counter_1_q));
  Hex_Digit_Display hex_digit_display_1 (.value(multiplexer_1_out));  // open: dp
  Hex_Digit_Display hex_digit_display_2 (.value({1'b0, counter_1_q}));  // open: dp
endmodule

module preg_3 (
  input  [3:0] in_1,
  input  [3:0] in_2,
  input  in_3,
  output [7:0] out_4
);

  wire Igual, Mayor, Menor;
  wire [2:0] Resultado;
  wire [3:0] binary_to_bcd_converter_1_p2, binary_to_bcd_converter_1_p3, binary_to_bcd_converter_1_p4,
       binary_to_bcd_converter_1_p5;
  wire [7:0] adder_1_out, adder_3_out, adder_4_out, adder_5_out, adder_6_out, and_2_out, and_3_out,
       and_4_out, f2, f3;

  Comparator #(.width(4)) comparator_1 (.a(in_1), .b(in_2), .gt(Resultado[0]), .eq(Resultado[1]), .lt(Resultado[2]));
  Adder adder_1 (.a({1'b0, in_1, 3'b000}), .b({4'b0000, in_1}), .out(adder_1_out));  // open: cin, cout
  Adder adder_2 (.a(adder_1_out), .b({4'b0000, in_2}), .out(f2));  // open: cin, cout
  assign {Menor, Igual, Mayor} = Resultado & {3{in_3}};  // AND_Gate and_1, 3 bits wide
  LED led_1 (.in(Mayor));
  LED led_2 (.in(Igual));
  LED led_3 (.in(Menor));
  Adder adder_3 (.a({in_1, 4'b0000}), .b({4'b0000, in_1}), .out(adder_3_out));  // open: cin, cout
  Adder adder_4 (.a({1'b0, in_2, 3'b000}), .b({2'b00, in_2, 2'b00}), .out(adder_4_out));  // open: cin, cout
  assign and_2_out = {in_2, 4'b0000} & {8{Mayor}};  // AND_Gate and_2, 8 bits wide
  assign and_3_out = f3 & {8{Igual}};  // AND_Gate and_3, 8 bits wide
  assign and_4_out = f2 & {8{Menor}};  // AND_Gate and_4, 8 bits wide
  Adder adder_5 (.a(adder_4_out), .b({3'b000, in_2, 1'b0}), .out(adder_5_out));  // open: cin, cout
  assign out_4 = and_2_out | and_3_out | and_4_out;  // OR_Gate or_1, 8 bits wide
  Adder adder_6 (.a(adder_5_out), .b({4'b0000, in_2}), .out(adder_6_out));  // open: cin, cout
  Hex_Digit_Display hex_digit_display_1 (.value(binary_to_bcd_converter_1_p2));  // open: dp
  Adder adder_7 (.a(adder_3_out), .b(adder_6_out), .out(f3));  // open: cin, cout
  Hex_Digit_Display hex_digit_display_2 (.value(binary_to_bcd_converter_1_p3));  // open: dp
  // Binary_to_BCD_converter #(.binvalue(10)) binary_to_bcd_converter_1: pin names not known; wires that end beside it: {2'b00, out_4}, binary_to_bcd_converter_1_p2, binary_to_bcd_converter_1_p3, binary_to_bcd_converter_1_p4, binary_to_bcd_converter_1_p5
  Hex_Digit_Display hex_digit_display_3 (.value(binary_to_bcd_converter_1_p4));  // open: dp
  Hex_Digit_Display hex_digit_display_4 (.value(binary_to_bcd_converter_1_p5));  // open: dp

  // Other names for the same wires on the sheet: A[3:0] = in_1; B[3:0] = in_2; f1[7:4] = in_2;
  //   Enabler[2:0] = {3{in_3}}

  // Notes on the sheet:
  //   m = 16
  //   p = 9 = 8+1
  //   n =17 = 16+1
  //   s = 15 = 8+4+2+1
  //   N*A:
  //   S*B:
endmodule

module preg_4 (
  input  [3:0] X,
  input  Enabler,
  input  [3:0] Y
);

  wire x1, x2, x3, x4, x5, x6, x7, x8, x9, x10, x11, x12, x13, x14, x15;
  wire [14:0] and_1_out, and_2_out, and_3_out, and_4_out, and_5_out, and_6_out, and_7_out, and_8_out,
       and_9_out, and_10_out, and_11_out, and_12_out, and_13_out, and_14_out, and_15_out, decoder_2_out15;

  Decoder #(.select(4)) decoder_1 (
    .out1(x1), .out2(x2), .out3(x3), .out4(x4), .out5(x5), .out6(x6), .out7(x7), .out8(x8), .out9(x9),
    .out10(x10), .out11(x11), .out12(x12), .out13(x13), .out14(x14), .out15(x15), .sel(X), .en(Enabler));  // open: out0
  assign and_1_out = {15{x1}} & decoder_2_out15;  // AND_Gate and_1, 15 bits wide
  Decoder #(.select(4)) decoder_2 (
    .out1(decoder_2_out15[14]), .out2(decoder_2_out15[13]), .out3(decoder_2_out15[12]),
    .out4(decoder_2_out15[11]), .out5(decoder_2_out15[10]), .out6(decoder_2_out15[9]),
    .out7(decoder_2_out15[8]), .out8(decoder_2_out15[7]), .out9(decoder_2_out15[6]),
    .out10(decoder_2_out15[5]), .out11(decoder_2_out15[4]), .out12(decoder_2_out15[3]),
    .out13(decoder_2_out15[2]), .out14(decoder_2_out15[1]), .out15(decoder_2_out15[0]), .sel(Y), .en(Enabler));  // open: out0
  assign and_2_out = {15{x2}} & decoder_2_out15;  // AND_Gate and_2, 15 bits wide
  assign and_3_out = {15{x3}} & decoder_2_out15;  // AND_Gate and_3, 15 bits wide
  assign and_4_out = {15{x4}} & decoder_2_out15;  // AND_Gate and_4, 15 bits wide
  DotMatrix #(.matrixcols(15), .matrixrows(15)) dotmatrix_1 (
    .col0(and_1_out), .col1(and_2_out), .col2(and_3_out), .col3(and_4_out), .col4(and_5_out),
    .col5(and_7_out), .col6(and_6_out), .col7(and_8_out), .col8(and_9_out), .col9(and_10_out),
    .col10(and_11_out), .col11(and_12_out), .col12(and_13_out), .col13(and_14_out), .col14(and_15_out));
  assign and_5_out = {15{x5}} & decoder_2_out15;  // AND_Gate and_5, 15 bits wide
  assign and_6_out = {15{x7}} & decoder_2_out15;  // AND_Gate and_6, 15 bits wide
  assign and_7_out = {15{x6}} & decoder_2_out15;  // AND_Gate and_7, 15 bits wide
  assign and_8_out = {15{x8}} & decoder_2_out15;  // AND_Gate and_8, 15 bits wide
  assign and_9_out = {15{x9}} & decoder_2_out15;  // AND_Gate and_9, 15 bits wide
  assign and_10_out = {15{x10}} & decoder_2_out15;  // AND_Gate and_10, 15 bits wide
  assign and_11_out = {15{x11}} & decoder_2_out15;  // AND_Gate and_11, 15 bits wide
  assign and_12_out = {15{x12}} & decoder_2_out15;  // AND_Gate and_12, 15 bits wide
  assign and_13_out = {15{x13}} & decoder_2_out15;  // AND_Gate and_13, 15 bits wide
  assign and_14_out = {15{x14}} & decoder_2_out15;  // AND_Gate and_14, 15 bits wide
  assign and_15_out = {15{x15}} & decoder_2_out15;  // AND_Gate and_15, 15 bits wide
endmodule

module preg_5 (
  input  [3:0] in_1,
  input  [3:0] in_2,
  input  Enabler
);

  wire [3:0] X, Y;
  wire [14:0] preg_5_subcircuito_1_out_5, preg_5_subcircuito_2_out_5, preg_5_subcircuito_3_out_5,
       preg_5_subcircuito_4_out_5, preg_5_subcircuito_5_out_5, preg_5_subcircuito_6_out_5,
       preg_5_subcircuito_7_out_5, preg_5_subcircuito_8_out_5, preg_5_subcircuito_9_out_5,
       preg_5_subcircuito_10_out_5, preg_5_subcircuito_11_out_5, preg_5_subcircuito_12_out_5,
       preg_5_subcircuito_13_out_5, preg_5_subcircuito_14_out_5, preg_5_subcircuito_15_out_5;

  Subtractor #(.width(4)) subtractor_1 (.a(in_1), .b(4'b0001), .out(X));  // open: bin, bout
  Subtractor #(.width(4)) subtractor_2 (.a(in_2), .b(4'b0001), .out(Y));  // open: bin, bout
  preg_5_subcircuito preg_5_subcircuito_1 (
    .Xv(X), .Yv(Y), .R(4'b0111), .Enabler(Enabler), .out_5(preg_5_subcircuito_1_out_5));
  preg_5_subcircuito preg_5_subcircuito_2 (
    .Xv(X), .Yv(Y), .R(4'b0110), .Enabler(Enabler), .out_5(preg_5_subcircuito_2_out_5));
  preg_5_subcircuito preg_5_subcircuito_3 (
    .Xv(X), .Yv(Y), .R(4'b1000), .Enabler(Enabler), .out_5(preg_5_subcircuito_3_out_5));
  preg_5_subcircuito preg_5_subcircuito_4 (
    .Xv(X), .Yv(Y), .R(4'b0101), .Enabler(Enabler), .out_5(preg_5_subcircuito_4_out_5));
  preg_5_subcircuito preg_5_subcircuito_5 (
    .Xv(X), .Yv(Y), .R(4'b1001), .Enabler(Enabler), .out_5(preg_5_subcircuito_5_out_5));
  preg_5_subcircuito preg_5_subcircuito_6 (
    .Xv(X), .Yv(Y), .R(4'b0100), .Enabler(Enabler), .out_5(preg_5_subcircuito_6_out_5));
  preg_5_subcircuito preg_5_subcircuito_7 (
    .Xv(X), .Yv(Y), .R(4'b1010), .Enabler(Enabler), .out_5(preg_5_subcircuito_7_out_5));
  preg_5_subcircuito preg_5_subcircuito_8 (
    .Xv(X), .Yv(Y), .R(4'b0011), .Enabler(Enabler), .out_5(preg_5_subcircuito_8_out_5));
  preg_5_subcircuito preg_5_subcircuito_9 (
    .Xv(X), .Yv(Y), .R(4'b1011), .Enabler(Enabler), .out_5(preg_5_subcircuito_9_out_5));
  preg_5_subcircuito preg_5_subcircuito_10 (
    .Xv(X), .Yv(Y), .R(4'b0010), .Enabler(Enabler), .out_5(preg_5_subcircuito_10_out_5));
  preg_5_subcircuito preg_5_subcircuito_11 (
    .Xv(X), .Yv(Y), .R(4'b1100), .Enabler(Enabler), .out_5(preg_5_subcircuito_11_out_5));
  preg_5_subcircuito preg_5_subcircuito_12 (
    .Xv(X), .Yv(Y), .R(4'b0001), .Enabler(Enabler), .out_5(preg_5_subcircuito_12_out_5));
  preg_5_subcircuito preg_5_subcircuito_13 (
    .Xv(X), .Yv(Y), .R(4'b1101), .Enabler(Enabler), .out_5(preg_5_subcircuito_13_out_5));
  preg_5_subcircuito preg_5_subcircuito_14 (
    .Xv(X), .Yv(Y), .R(4'b0000), .Enabler(Enabler), .out_5(preg_5_subcircuito_14_out_5));
  preg_5_subcircuito preg_5_subcircuito_15 (
    .Xv(X), .Yv(Y), .R(4'b1110), .Enabler(Enabler), .out_5(preg_5_subcircuito_15_out_5));
  DotMatrix #(.inputtype("row"), .matrixcols(15), .matrixrows(15)) dotmatrix_1 (
    .row0(preg_5_subcircuito_14_out_5), .row1(preg_5_subcircuito_12_out_5),
    .row2(preg_5_subcircuito_10_out_5), .row3(preg_5_subcircuito_8_out_5), .row4(preg_5_subcircuito_6_out_5),
    .row5(preg_5_subcircuito_4_out_5), .row6(preg_5_subcircuito_2_out_5), .row7(preg_5_subcircuito_1_out_5),
    .row8(preg_5_subcircuito_3_out_5), .row9(preg_5_subcircuito_5_out_5), .row10(preg_5_subcircuito_7_out_5),
    .row11(preg_5_subcircuito_9_out_5), .row12(preg_5_subcircuito_11_out_5),
    .row13(preg_5_subcircuito_13_out_5), .row14(preg_5_subcircuito_15_out_5));
endmodule

module preg_5_subcircuito (
  input  [3:0] Xv,
  input  [3:0] Yv,
  input  Enabler,
  input  [3:0] R,
  output [14:0] out_5
);

  wire comparator_1_lt, comparator_2_eq, or_1_out;
  wire [3:0] d, subtractor_1_out, subtractor_2_out;
  wire [4:0] bit_extender_1_out, bit_extender_2_out, T;
  wire [14:0] multiplexer_2_out, shifter_1_out;

  Comparator #(.mode("unsigned"), .width(4)) comparator_1 (.a(R), .b(Yv), .lt(comparator_1_lt));  // open: gt, eq
  Subtractor #(.width(4)) subtractor_1 (.a(R), .b(Yv), .out(subtractor_1_out));  // open: bin, bout
  Subtractor #(.width(4)) subtractor_2 (.a(Yv), .b(R), .out(subtractor_2_out));  // open: bin, bout
  Multiplexer #(.width(4)) multiplexer_1 (
    .in0(subtractor_1_out), .in1(subtractor_2_out), .out(d), .sel(comparator_1_lt));
  Shifter #(.shift("lr"), .width(15)) shifter_1 (.in({15{1'b1}}), .\dist (T[3:0]), .out(shifter_1_out));
  Comparator #(.mode("unsigned"), .width(4)) comparator_2 (
    .a(T[3:0]), .b(4'b1111), .eq(comparator_2_eq));  // open: gt, lt
  or or_1 (or_1_out, comparator_2_eq, T[4]);
  Multiplexer #(.width(15)) multiplexer_2 (
    .in0(shifter_1_out), .in1({15{1'b0}}), .out(multiplexer_2_out), .sel(or_1_out));
  assign bit_extender_1_out = {{1{1'b0}}, d};  // Bit_Extender bit_extender_1
  assign bit_extender_2_out = {{1{1'b0}}, Xv};  // Bit_Extender bit_extender_2
  Adder #(.width(5)) adder_1 (.a(bit_extender_1_out), .b(bit_extender_2_out), .out(T));  // open: cin, cout
  assign out_5 = multiplexer_2_out & {15{Enabler}};  // AND_Gate and_1, 15 bits wide

  // Other names for the same wires on the sheet: Enabler_t[14:0] = {15{Enabler}}

  // Notes on the sheet:
  //   R-Yv
  //   Yv-R
  //   Apagar
endmodule

module main (
  input  in_1,
  input  in_2,
  input  [3:0] in_3,
  input  [2:0] in_4,
  input  [3:0] in_5,
  input  Pregunta_4,
  input  Pregunta_5
);

  wire clock_1_out, preg_1_1_out_3, preg_1_1_out_4, preg_1_1_out_5;
  wire [3:0] joystick_1_x, joystick_1_y, joystick_2_x, joystick_2_y;

  preg_1 preg_1_1 (.in_1(in_4), .in_2(in_2), .out_3(preg_1_1_out_3), .out_4(preg_1_1_out_4), .out_5(preg_1_1_out_5));
  preg_2 preg_2_1 (.in_1(clock_1_out));
  Clock clock_1 (.out(clock_1_out));
  // RGBLED rgbled_1: pin names not known; wires that end beside it: preg_1_1_out_3, preg_1_1_out_4, preg_1_1_out_5
  preg_4 preg_4_1 (.X(joystick_1_x), .Enabler(Pregunta_4), .Y(joystick_1_y));
  Joystick joystick_1 (.x(joystick_1_x), .y(joystick_1_y));
  preg_3 preg_3_1 (.in_3(in_1), .in_1(in_3), .in_2(in_5));  // open: out_4
  preg_5 preg_5_1 (.in_1(joystick_2_x), .in_2(joystick_2_y), .Enabler(Pregunta_5));
  Joystick joystick_2 (.x(joystick_2_x), .y(joystick_2_y));

  // Notes on the sheet:
  //   Pregunta 1: violeta, amarillo, verde, azul, rojo, celeste
  //   Pregunta 2: 20240282
  //   Pregunta 3
endmodule
