// Logisim project 20240282_LAB2_2026_1.circ as structural Verilog: 3 circuits, main circuit LED_matrix
module test (
);

  registers_8R_nuevo registers_8r_nuevo_1 ();  // open: dir_RA, dir_RB, enable, dir_W, reset, clock, dato_W, R1_in, R0_in, RA, RB, R7_val, R6_val
  LED_matrix led_matrix_1 ();  // open: x_coord, y_coord, X_control, Y_control
endmodule

module LED_matrix (
  input  [7:0] x_coord,
  input  [7:0] y_coord,
  output [31:0] X_control,
  output [31:0] Y_control
);

  Decoder #(.select(5)) decoder_1 (
    .out0(X_control[0]), .out1(X_control[1]), .out2(X_control[2]), .out3(X_control[3]), .out4(X_control[4]),
    .out5(X_control[5]), .out6(X_control[6]), .out7(X_control[7]), .out8(X_control[8]), .out9(X_control[9]),
    .out10(X_control[10]), .out11(X_control[11]), .out12(X_control[12]), .out13(X_control[13]),
    .out14(X_control[14]), .out15(X_control[15]), .out16(X_control[16]), .out17(X_control[17]),
    .out18(X_control[18]), .out19(X_control[19]), .out20(X_control[20]), .out21(X_control[21]),
    .out22(X_control[22]), .out23(X_control[23]), .out24(X_control[24]), .out25(X_control[25]),
    .out26(X_control[26]), .out27(X_control[27]), .out28(X_control[28]), .out29(X_control[29]),
    .out30(X_control[30]), .out31(X_control[31]), .sel(x_coord[4:0]));  // open: en
  Decoder #(.select(5)) decoder_2 (
    .out0(Y_control[0]), .out1(Y_control[1]), .out2(Y_control[2]), .out3(Y_control[3]), .out4(Y_control[4]),
    .out5(Y_control[5]), .out6(Y_control[6]), .out7(Y_control[7]), .out8(Y_control[8]), .out9(Y_control[9]),
    .out10(Y_control[10]), .out11(Y_control[11]), .out12(Y_control[12]), .out13(Y_control[13]),
    .out14(Y_control[14]), .out15(Y_control[15]), .out16(Y_control[16]), .out17(Y_control[17]),
    .out18(Y_control[18]), .out19(Y_control[19]), .out20(Y_control[20]), .out21(Y_control[21]),
    .out22(Y_control[22]), .out23(Y_control[23]), .out24(Y_control[24]), .out25(Y_control[25]),
    .out26(Y_control[26]), .out27(Y_control[27]), .out28(Y_control[28]), .out29(Y_control[29]),
    .out30(Y_control[30]), .out31(Y_control[31]), .sel(y_coord[4:0]));  // open: en
endmodule

module registers_8R_nuevo (
  input  reset,
  input  [2:0] dir_RB,
  input  clock,
  input  [7:0] dato_W,
  input  enable,
  input  [2:0] dir_RA,
  input  [2:0] dir_W,
  input  [7:0] R1_in,
  input  [7:0] R0_in,
  output [7:0] RB,
  output [7:0] RA,
  output [7:0] R7_val,
  output [7:0] R6_val
);

  wire decoder_1_out2, decoder_1_out3, decoder_1_out4, decoder_1_out5, decoder_1_out6, decoder_1_out7;
  wire [3:0] binary_to_bcd_converter_1_p2, binary_to_bcd_converter_1_p3, binary_to_bcd_converter_1_p4,
       binary_to_bcd_converter_2_p2, binary_to_bcd_converter_2_p3, binary_to_bcd_converter_2_p4,
       binary_to_bcd_converter_3_p2, binary_to_bcd_converter_3_p3, binary_to_bcd_converter_3_p4,
       binary_to_bcd_converter_4_p2, binary_to_bcd_converter_4_p3, binary_to_bcd_converter_4_p4,
       binary_to_bcd_converter_5_p2, binary_to_bcd_converter_5_p3, binary_to_bcd_converter_5_p4,
       binary_to_bcd_converter_6_p2, binary_to_bcd_converter_6_p3, binary_to_bcd_converter_6_p4,
       binary_to_bcd_converter_7_p2, binary_to_bcd_converter_7_p3, binary_to_bcd_converter_7_p4,
       binary_to_bcd_converter_8_p2, binary_to_bcd_converter_8_p3, binary_to_bcd_converter_8_p4, R0_q,
       R0_q_2, R1_q, R1_q_2, R2_q, R2_q_2, R3_q, R3_q_2, register_3_q, register_3_q_2, register_4_q,
       register_4_q_2;

  LED W_EN_led (.in(enable));
  LED led_1 (.in(enable));
  LED led_2 (.in(enable));
  LED led_3 (.in(enable));
  Decoder #(.select(3)) decoder_1 (
    .out2(decoder_1_out2), .out3(decoder_1_out3), .out4(decoder_1_out4), .out5(decoder_1_out5),
    .out6(decoder_1_out6), .out7(decoder_1_out7), .sel(dir_W), .en(enable));  // open: out0, out1
  Register register_1 (.D(dato_W), .en(decoder_1_out7), .clk(clock), .Q(R7_val), .clr(reset));
  Register register_2 (.D(dato_W), .en(decoder_1_out6), .clk(clock), .Q(R6_val), .clr(reset));
  Register register_3 (.D(dato_W), .en(decoder_1_out5), .clk(clock), .Q({register_3_q_2, register_3_q}), .clr(reset));
  Register register_4 (.D(dato_W), .en(decoder_1_out4), .clk(clock), .Q({register_4_q_2, register_4_q}), .clr(reset));
  Register R3 (.D(dato_W), .en(decoder_1_out3), .clk(clock), .Q({R3_q_2, R3_q}), .clr(reset));
  Register R2 (.D(dato_W), .en(decoder_1_out2), .clk(clock), .Q({R2_q_2, R2_q}), .clr(reset));
  Register R1 (.D(R1_in), .en(1'b1), .clk(clock), .Q({R1_q_2, R1_q}), .clr(reset));
  Register R0 (.D(R0_in), .en(1'b1), .clk(clock), .Q({R0_q_2, R0_q}), .clr(reset));
  Hex_Digit_Display R7H (.value(R7_val[7:4]));  // open: dp
  Hex_Digit_Display R6H (.value(R6_val[7:4]));  // open: dp
  Hex_Digit_Display R5H (.value(register_3_q_2));  // open: dp
  Hex_Digit_Display R4H (.value(register_4_q_2));  // open: dp
  Hex_Digit_Display R3H (.value(R3_q_2));  // open: dp
  Hex_Digit_Display R2H (.value(R2_q_2));  // open: dp
  Hex_Digit_Display R1H (.value(R1_q_2));  // open: dp
  Hex_Digit_Display R0H (.value(R0_q_2));  // open: dp
  Hex_Digit_Display R7L (.value(R7_val[3:0]));  // open: dp
  Hex_Digit_Display R6L (.value(R6_val[3:0]));  // open: dp
  Hex_Digit_Display R5L (.value(register_3_q));  // open: dp
  Hex_Digit_Display R4L (.value(register_4_q));  // open: dp
  Hex_Digit_Display R3L (.value(R3_q));  // open: dp
  Hex_Digit_Display R2L (.value(R2_q));  // open: dp
  Hex_Digit_Display R1L (.value(R1_q));  // open: dp
  Hex_Digit_Display R0L (.value(R0_q));  // open: dp
  Hex_Digit_Display R7d2 (.value(binary_to_bcd_converter_1_p2));  // open: dp
  Hex_Digit_Display R7d1 (.value(binary_to_bcd_converter_1_p3));  // open: dp
  // Binary_to_BCD_converter #(.binvalue(8)) binary_to_bcd_converter_1: pin names not known; wires that end beside it: R7_val, binary_to_bcd_converter_1_p2, binary_to_bcd_converter_1_p3, binary_to_bcd_converter_1_p4
  Hex_Digit_Display R6d2 (.value(binary_to_bcd_converter_2_p2));  // open: dp
  Hex_Digit_Display R6d1 (.value(binary_to_bcd_converter_2_p3));  // open: dp
  // Binary_to_BCD_converter #(.binvalue(8)) binary_to_bcd_converter_2: pin names not known; wires that end beside it: R6_val, binary_to_bcd_converter_2_p2, binary_to_bcd_converter_2_p3, binary_to_bcd_converter_2_p4
  Hex_Digit_Display R5d2 (.value(binary_to_bcd_converter_3_p2));  // open: dp
  Hex_Digit_Display R5d1 (.value(binary_to_bcd_converter_3_p3));  // open: dp
  // Binary_to_BCD_converter #(.binvalue(8)) binary_to_bcd_converter_3: pin names not known; wires that end beside it: {register_3_q_2, register_3_q}, binary_to_bcd_converter_3_p2, binary_to_bcd_converter_3_p3, binary_to_bcd_converter_3_p4
  Hex_Digit_Display R4d2 (.value(binary_to_bcd_converter_4_p2));  // open: dp
  Hex_Digit_Display R4d1 (.value(binary_to_bcd_converter_4_p3));  // open: dp
  // Binary_to_BCD_converter #(.binvalue(8)) binary_to_bcd_converter_4: pin names not known; wires that end beside it: {register_4_q_2, register_4_q}, binary_to_bcd_converter_4_p2, binary_to_bcd_converter_4_p3, binary_to_bcd_converter_4_p4
  Hex_Digit_Display R3d2 (.value(binary_to_bcd_converter_5_p2));  // open: dp
  Hex_Digit_Display R3d1 (.value(binary_to_bcd_converter_5_p3));  // open: dp
  // Binary_to_BCD_converter #(.binvalue(8)) binary_to_bcd_converter_5: pin names not known; wires that end beside it: {R3_q_2, R3_q}, binary_to_bcd_converter_5_p2, binary_to_bcd_converter_5_p3, binary_to_bcd_converter_5_p4
  Hex_Digit_Display R2d2 (.value(binary_to_bcd_converter_6_p2));  // open: dp
  Hex_Digit_Display R2d1 (.value(binary_to_bcd_converter_6_p3));  // open: dp
  // Binary_to_BCD_converter #(.binvalue(8)) binary_to_bcd_converter_6: pin names not known; wires that end beside it: {R2_q_2, R2_q}, binary_to_bcd_converter_6_p2, binary_to_bcd_converter_6_p3, binary_to_bcd_converter_6_p4
  Hex_Digit_Display R1d2 (.value(binary_to_bcd_converter_7_p2));  // open: dp
  Hex_Digit_Display R1d1 (.value(binary_to_bcd_converter_7_p3));  // open: dp
  // Binary_to_BCD_converter #(.binvalue(8)) binary_to_bcd_converter_7: pin names not known; wires that end beside it: {R1_q_2, R1_q}, binary_to_bcd_converter_7_p2, binary_to_bcd_converter_7_p3, binary_to_bcd_converter_7_p4
  Hex_Digit_Display R0d2 (.value(binary_to_bcd_converter_8_p2));  // open: dp
  Hex_Digit_Display R0d1 (.value(binary_to_bcd_converter_8_p3));  // open: dp
  // Binary_to_BCD_converter #(.binvalue(8)) binary_to_bcd_converter_8: pin names not known; wires that end beside it: {R0_q_2, R0_q}, binary_to_bcd_converter_8_p2, binary_to_bcd_converter_8_p3, binary_to_bcd_converter_8_p4
  Hex_Digit_Display R7d0 (.value(binary_to_bcd_converter_1_p4));  // open: dp
  Hex_Digit_Display R6d0 (.value(binary_to_bcd_converter_2_p4));  // open: dp
  Hex_Digit_Display R5d0 (.value(binary_to_bcd_converter_3_p4));  // open: dp
  Hex_Digit_Display R4d0 (.value(binary_to_bcd_converter_4_p4));  // open: dp
  Hex_Digit_Display R3d0 (.value(binary_to_bcd_converter_5_p4));  // open: dp
  Hex_Digit_Display R2d0 (.value(binary_to_bcd_converter_6_p4));  // open: dp
  Hex_Digit_Display R1d0 (.value(binary_to_bcd_converter_7_p4));  // open: dp
  Hex_Digit_Display R0d0 (.value(binary_to_bcd_converter_8_p4));  // open: dp
  LED led_4 (.in(R7_val[7]));
  LED led_5 (.in(R7_val[6]));
  LED led_6 (.in(R7_val[5]));
  LED led_7 (.in(R6_val[7]));
  LED led_8 (.in(R6_val[6]));
  LED led_9 (.in(R6_val[5]));
  LED led_10 (.in(register_3_q_2[3]));
  LED led_11 (.in(register_3_q_2[2]));
  LED led_12 (.in(register_3_q_2[1]));
  LED b47 (.in(register_4_q_2[3]));
  LED b46 (.in(register_4_q_2[2]));
  LED b45 (.in(register_4_q_2[1]));
  LED b37 (.in(R3_q_2[3]));
  LED b36 (.in(R3_q_2[2]));
  LED b35 (.in(R3_q_2[1]));
  LED led_13 (.in(R2_q_2[3]));
  LED led_14 (.in(R2_q_2[2]));
  LED led_15 (.in(R2_q_2[1]));
  LED led_16 (.in(R1_q_2[3]));
  LED led_17 (.in(R1_q_2[2]));
  LED led_18 (.in(R1_q_2[1]));
  LED led_19 (.in(R0_q_2[3]));
  LED led_20 (.in(R0_q_2[2]));
  LED led_21 (.in(R0_q_2[1]));
  LED led_22 (.in(R7_val[4]));
  LED led_23 (.in(R7_val[3]));
  LED led_24 (.in(R7_val[2]));
  LED led_25 (.in(R7_val[1]));
  LED led_26 (.in(R6_val[4]));
  LED led_27 (.in(R6_val[3]));
  LED led_28 (.in(R6_val[2]));
  LED led_29 (.in(R6_val[1]));
  LED led_30 (.in(register_3_q_2[0]));
  LED led_31 (.in(register_3_q[3]));
  LED led_32 (.in(register_3_q[2]));
  LED led_33 (.in(register_3_q[1]));
  LED b44 (.in(register_4_q_2[0]));
  LED b43 (.in(register_4_q[3]));
  LED b42 (.in(register_4_q[2]));
  LED b41 (.in(register_4_q[1]));
  LED b34 (.in(R3_q_2[0]));
  LED b33 (.in(R3_q[3]));
  LED b32 (.in(R3_q[2]));
  LED b31 (.in(R3_q[1]));
  LED led_34 (.in(R2_q_2[0]));
  LED led_35 (.in(R2_q[3]));
  LED led_36 (.in(R2_q[2]));
  LED led_37 (.in(R2_q[1]));
  LED led_38 (.in(R1_q_2[0]));
  LED led_39 (.in(R1_q[3]));
  LED led_40 (.in(R1_q[2]));
  LED led_41 (.in(R1_q[1]));
  LED led_42 (.in(R0_q_2[0]));
  LED led_43 (.in(R0_q[3]));
  LED led_44 (.in(R0_q[2]));
  LED led_45 (.in(R0_q[1]));
  Multiplexer #(.select(3), .width(8)) multiplexer_1 (
    .in0({R0_q_2, R0_q}), .in1({R1_q_2, R1_q}), .in2({R2_q_2, R2_q}), .in3({R3_q_2, R3_q}),
    .in4({register_4_q_2, register_4_q}), .in5({register_3_q_2, register_3_q}), .in6(R6_val), .in7(R7_val),
    .out(RA), .sel(dir_RA));
  LED led_46 (.in(R7_val[0]));
  LED led_47 (.in(R6_val[0]));
  LED led_48 (.in(register_3_q[0]));
  LED b40 (.in(register_4_q[0]));
  LED b30 (.in(R3_q[0]));
  LED led_49 (.in(R2_q[0]));
  LED led_50 (.in(R1_q[0]));
  LED led_51 (.in(R0_q[0]));
  Multiplexer #(.select(3), .width(8)) multiplexer_2 (
    .in0({R0_q_2, R0_q}), .in1({R1_q_2, R1_q}), .in2({R2_q_2, R2_q}), .in3({R3_q_2, R3_q}),
    .in4({register_4_q_2, register_4_q}), .in5({register_3_q_2, register_3_q}), .in6(R6_val), .in7(R7_val),
    .out(RB), .sel(dir_RB));
endmodule
