// Logisim project 20240282_LAB_2_2025_2.circ as structural Verilog: 3 circuits, main circuit registers_2_3
module registers_2_3 (
  input  reset,
  input  clock,
  input  [7:0] dato_W,
  input  enable,
  input  [1:0] dir_W,
  input  [1:0] dir_RA,
  input  [1:0] dir_RB,
  output [7:0] RA,
  output [7:0] RB
);

  wire decoder_1_out0, decoder_1_out1, decoder_1_out2, decoder_1_out3;
  wire [7:0] R0_q, R1_q, R2_q, R3_q;

  LED led_1 (.in(enable));
  LED led_2 (.in(enable));
  LED led_3 (.in(enable));
  LED led_4 (.in(enable));
  Decoder #(.select(2)) decoder_1 (
    .out0(decoder_1_out0), .out1(decoder_1_out1), .out2(decoder_1_out2), .out3(decoder_1_out3), .sel(dir_W),
    .en(enable));
  Register R3 (.D(dato_W), .en(decoder_1_out3), .clk(clock), .Q(R3_q), .clr(reset));
  Register R2 (.D(dato_W), .en(decoder_1_out2), .clk(clock), .Q(R2_q), .clr(reset));
  Register R1 (.D(dato_W), .en(decoder_1_out1), .clk(clock), .Q(R1_q), .clr(reset));
  Register R0 (.D(dato_W), .en(decoder_1_out0), .clk(clock), .Q(R0_q), .clr(reset));
  Hex_Digit_Display R3H (.value(R3_q[7:4]));  // open: dp
  Hex_Digit_Display R2H (.value(R2_q[7:4]));  // open: dp
  Hex_Digit_Display R1H (.value(R1_q[7:4]));  // open: dp
  Hex_Digit_Display R0H (.value(R0_q[7:4]));  // open: dp
  Hex_Digit_Display R3L (.value(R3_q[3:0]));  // open: dp
  Hex_Digit_Display R2L (.value(R2_q[3:0]));  // open: dp
  Hex_Digit_Display R1L (.value(R1_q[3:0]));  // open: dp
  Hex_Digit_Display R0L (.value(R0_q[3:0]));  // open: dp
  Multiplexer #(.select(2), .width(8)) multiplexer_1 (
    .in0(R0_q), .in1(R1_q), .in2(R2_q), .in3(R3_q), .out(RA), .sel(dir_RA));
  Multiplexer #(.select(2), .width(8)) multiplexer_2 (
    .in0(R0_q), .in1(R1_q), .in2(R2_q), .in3(R3_q), .out(RB), .sel(dir_RB));
endmodule

module respuesta (
  input  in_1,
  input  [7:0] in_2
);

  wire reset, tictac;
  wire [1:0] dirA, dirB, dirD, ope;
  wire [4:0] counter_1_q;
  wire [6:0] multiplexer_2_out, registers_2_3_1_ra;
  wire [7:0] adder_1_out, multiplexer_1_out, not_1_out, registers_2_3_1_rb;
  wire [7:7] registers_2_3_1_ra_2;

  Counter #(.max('h1f), .width(5)) counter_1 (
    .clr(reset), .clk(tictac), .Q(counter_1_q));  // open: load, up, count, D, carry
  ROM #(.addrWidth(5)) rom_1 (.addr(counter_1_q), .data({ope, dirD, dirA, dirB}));
  Button button_1 (.out(tictac));
  Button button_2 (.out(reset));
  // Probe on in_2
  registers_2_3 registers_2_3_1 (
    .dir_RA(dirA), .dir_RB(dirB), .reset(reset), .clock(tictac), .dato_W(multiplexer_1_out), .enable(in_1),
    .dir_W(dirD), .RA({registers_2_3_1_ra_2[7], registers_2_3_1_ra}), .RB(registers_2_3_1_rb));
  // Probe on {registers_2_3_1_ra_2[7], registers_2_3_1_ra}
  // Probe on registers_2_3_1_rb
  Multiplexer #(.select(2), .width(8)) multiplexer_1 (
    .in0(not_1_out), .in1(adder_1_out), .in2({8{1'b0}}), .in3({8{1'b0}}), .out(multiplexer_1_out), .sel(ope));
  // Probe on ope
  // Probe on not_1_out
  assign not_1_out = ~{registers_2_3_1_ra_2[7], registers_2_3_1_ra};  // NOT_Gate not_1, 8 bits wide
  // Probe on adder_1_out
  Multiplexer #(.select(2), .width(7)) multiplexer_2 (
    .in0({7{1'b0}}), .in1({7{1'b0}}), .in2({7{1'b0}}), .in3(registers_2_3_1_ra), .out(multiplexer_2_out),
    .sel(ope));
  Adder adder_1 (
    .a({registers_2_3_1_ra_2[7], registers_2_3_1_ra}), .b(registers_2_3_1_rb), .out(adder_1_out));  // open: cin, cout
  TTY #(.rows(4)) tty_1 (.data(multiplexer_2_out), .clk(tictac), .clr(reset));  // open: we

  // Notes on the sheet:
  //   contents of rom_1 (hex, n*v repeats v):
  //   0 50 14 65 6a 6a 6a 7a 7f 7d cc 7e 7d cc 0 73 cc 55 55 7d cc 7e 7d cc
  //   41 = A
  //   52 = R
  //   51 = Q
  //   55 = U
  //   69 = i
endmodule

module test_TTY (
  input  [6:0] dato_ASCII
);

  wire borrar_todo_out, tictac_out;

  // Probe on dato_ASCII
  // Probe on dato_ASCII
  Button tictac (.out(tictac_out));
  TTY #(.rows(4)) tty_1 (.data(dato_ASCII), .clk(tictac_out), .we(1'b1), .clr(borrar_todo_out));
  Button borrar_todo (.out(borrar_todo_out));

  // Notes on the sheet:
  //   41 = A
  //   52 = R
  //   51 = Q
  //   55 = U
  //   69 = i
endmodule
