// Logisim project TunelTest.circ as structural Verilog: 1 circuit, main circuit main
module main (
  input  [2:0] in_1,
  output [2:0] out_2
);


  assign out_2 = in_1;

  // Other names for the same wires on the sheet: oli_1[2:0] = in_1
endmodule
